// Logisim project cpu_husixu_flow&interrupt.circ as structural Verilog: 14 circuits, main circuit cpu
module cpu (
);

  wire alu_1_equal, and_2_out, and_3_out, and_4_out, and_5_out, controller_1_eret, controller_1_out_7,
       controller_1_out_9, controller_1_out_10, controller_1_out_12, controller_1_out_13,
       controller_1_out_14, controller_1_out_15, data_confilct_1_stall, decoder_1_out1, decoder_1_out2,
       decoder_1_out3, ERET, ex_mem_1_en_o, ex_mem_1_eret_o, ex_mem_1_lhu_o, ex_mem_1_memw_o,
       ex_mem_1_rs_ex_mem_o, ex_mem_1_rt_ex_mem_o, GO, HALT, id_ex_1_eret_o, id_ex_1_lhu_o, id_ex_1_memw_o,
       id_ex_1_rw_o, id_ex_1_sys_o, IE, inter_signal_1_ir_o, inter_signal_2_ir_o, inter_signal_3_ir_o,
       interrupt, IR1, IR2, IR3, mem_wb_1_en_o, or_1_out, or_2_out, or_3_out, or_4_out, or_8_out, or_9_out,
       or_10_out, pc_1_b_instruc, pri_1_ir, register_2_q, rs_EX_MEM, rs_EX_WB, RST, RST1, RST2, RST3,
       rt_EX_MEM, rt_EX_WB, T, W1, W2, W3;
  wire [0:0] register_1_q;
  wire [1:0] controller_1_out_5, controller_1_out_8, controller_1_out_11, id_ex_1_alux_o, inter_sel,
       mem_wb_1_wb_o_2, pri_1_inter_sel;
  wire [2:0] controller_1_des_reg, controller_1_out_6, controller_1_src_reg, ex_mem_1_des_reg_o,
       id_ex_1_aluy_o, id_ex_1_des_reg_o;
  wire [3:0] controller_1_branch, controller_1_out_4, ex_mem_1_wb_o, id_ex_1_aluop_o, id_ex_1_branch_o,
       id_ex_1_wb, mem_wb_1_wb_o;
  wire [15:0] \load_use次数 , \总周期数 , \插入气泡数 , \无条件分支指令数 , \有条件分支成功跳转 ;
  wire [23:0] cPC, EPC, inter_addr, multiplexer_1_out, pc_1_out_18;
  wire [31:0] adder_1_out, alu_1_result, alui_1_out_7, alui_1_out_8, bit_extender_1_out, EX, ex_mem_1_data_o,
       ex_mem_1_rs_o, EX_P, ID, id_ex_1_rs_o, id_ex_1_rt_o, ID_P, IF, IF_P, MEM, MEM_P, MEM_RES,
       mem_wb_1_data_o, mem_wb_1_res_o, mips_ram_1_p6, mips_ram_1_p7, multiplexer_3_out, multiplexer_4_out,
       multiplexer_5_out, multiplexer_6_out, multiplexer_7_out, reg_file_1_rf_d1, reg_file_1_rf_d2,
       shifter_1_out, SyscallOut, WB, WB_DATA, WB_P;
  wire [31:24] multiplexer_2_out;

  Button \u_总复位  (.out(RST));
  Button _1 (.out(IR1));
  Button _2 (.out(IR2));
  Button _3 (.out(IR3));
  // Probe on cPC
  Clock clock_1 (.out(T));
  LED led_1 (.in(W1));
  LED led_2 (.in(W2));
  LED led_3 (.in(W3));
  // Probe on IF
  // Probe on IF_P
  Register #(.width(1)) register_1 (.D(ERET), .Q(register_1_q[0]), .clk(T), .clr(RST));  // open: en
  PC pc_1 (
    .in_5(multiplexer_3_out), .in_6(EX[25:0]), .in_7(EX[15:0]), .in_8(alu_1_equal), .in_9(RST), .in_10(HALT),
    .in_11(T), .out_17(IF_P), .out_18(pc_1_out_18), .out_19(\总周期数 ), .out_20(\无条件分支指令数 ),
    .out_22(\有条件分支成功跳转 ), .in_2(mem_wb_1_en_o), .stall(data_confilct_1_stall), .Branch_I(id_ex_1_branch_o),
    .B_instruc(pc_1_b_instruc), .\气泡数 (\插入气泡数 ), .sys(controller_1_out_13), .\load_use数 (\load_use次数 ),
    .interrupt(interrupt), .ERET(ERET), .EPC(EPC), .inter_addr(inter_addr));  // open: out_21
  Button u_GO (.out(GO));
  Hex_Digit_Display hex_digit_display_1 (.value(SyscallOut[31:28]));  // open: dp
  // Probe on ID
  // Probe on ID_P
  Multiplexer #(.select(2), .width(24)) multiplexer_1 (
    .in0(EPC), .in1(EPC), .in2(cPC), .in3(EPC), .out(multiplexer_1_out), .sel({interrupt, register_1_q[0]}));  // open: en
  inter_signal inter_signal_1 (.T(T), .IR(IR1), .W(RST1), .IR_LED(W1), .IR_O(inter_signal_1_ir_o));
  inter_signal inter_signal_2 (.T(T), .IR(IR2), .W(RST2), .IR_LED(W2), .IR_O(inter_signal_2_ir_o));
  inter_signal inter_signal_3 (.T(T), .IR(IR3), .W(RST3), .IR_LED(W3), .IR_O(inter_signal_3_ir_o));
  ROM #(.addrWidth(24), .dataWidth(32)) rom_1 (.addr(pc_1_out_18), .data(IF));  // open: sel
  Hex_Digit_Display hex_digit_display_2 (.value(SyscallOut[23:20]));  // open: dp
  Hex_Digit_Display hex_digit_display_3 (.value(SyscallOut[27:24]));  // open: dp
  Register #(.width(1)) register_2 (.D(interrupt), .en(or_1_out), .Q(register_2_q), .clk(T));  // open: clr
  or or_1 (or_1_out, interrupt, ERET);
  // Probe on multiplexer_1_out
  Register #(.width(24)) register_3 (.D(multiplexer_1_out), .en(interrupt), .Q(EPC), .clk(T), .clr(RST));
  PRI pri_1 (
    .IR1(inter_signal_1_ir_o), .IR2(inter_signal_2_ir_o), .IR3(inter_signal_3_ir_o), .IR(pri_1_ir),
    .inter_sel(pri_1_inter_sel));
  IF_ID if_id_1 (
    .clk(T), .Data_I(IF), .RST(RST), .Data_O(ID), .oPC_I(IF_P), .oPC_O(ID_P), .stall(data_confilct_1_stall),
    .B_instruc(pc_1_b_instruc), .HALT(HALT), .inter(or_2_out));
  or or_2 (or_2_out, interrupt, ERET);
  Hex_Digit_Display hex_digit_display_4 (.value(SyscallOut[15:12]));  // open: dp
  Hex_Digit_Display hex_digit_display_5 (.value(SyscallOut[19:16]));  // open: dp
  // Probe on EX
  // Probe on EX_P
  not not_1 (IE, register_2_q);
  // Probe on EPC
  or or_3 (or_3_out, interrupt, ERET);
  and and_1 (interrupt, pri_1_ir, IE);
  // Probe on ID
  Controller controller_1 (
    .in_1(ID[31:26]), .in_2(ID[5:0]), .out_10(controller_1_out_10), .out_8(controller_1_out_8),
    .out_4(controller_1_out_4), .out_7(controller_1_out_7), .out_5(controller_1_out_5),
    .out_6(controller_1_out_6), .out_9(controller_1_out_9), .out_11(controller_1_out_11),
    .out_12(controller_1_out_12), .out_14(controller_1_out_14), .out_15(controller_1_out_15),
    .out_13(controller_1_out_13), .src_reg(controller_1_src_reg), .des_reg(controller_1_des_reg),
    .Branch(controller_1_branch), .ERET(controller_1_eret));
  Reg_File reg_file_1 (
    .rs(ID[25:21]), .rd(ID[15:11]), .rt(ID[20:16]), .clk(T), .rWE(mem_wb_1_wb_o[3]), .rW_2(mem_wb_1_wb_o_2),
    .Syscall(controller_1_out_13), .RES(mem_wb_1_res_o), .Din(mem_wb_1_data_o), .RF_D1(reg_file_1_rf_d1),
    .RF_D2(reg_file_1_rf_d2), .rW(mem_wb_1_wb_o[0]), .Instruction_I(WB));  // open: rt_I, rd_I
  Hex_Digit_Display hex_digit_display_6 (.value(SyscallOut[11:8]));  // open: dp
  Hex_Digit_Display hex_digit_display_7 (.value(SyscallOut[7:4]));  // open: dp
  // Probe on MEM
  // Probe on MEM_P
  Register #(.width(2)) register_4 (.D(pri_1_inter_sel), .en(or_3_out), .Q(inter_sel), .clk(T), .clr(RST));
  // Probe on pri_1_inter_sel
  Multiplexer #(.select(2), .width(32)) multiplexer_2 (
    .in0({32{1'b0}}), .in1(32'h45), .in2(32'h70), .in3(32'h9b), .out({multiplexer_2_out, inter_addr}),
    .sel(pri_1_inter_sel));  // open: en
  // Probe on reg_file_1_rf_d1
  Hex_Digit_Display hex_digit_display_8 (.value(SyscallOut[3:0]));  // open: dp
  // Probe on inter_sel
  Decoder #(.select(2)) decoder_1 (
    .out1(decoder_1_out1), .out2(decoder_1_out2), .out3(decoder_1_out3), .sel(inter_sel));  // open: out0, en
  data_confilct data_confilct_1 (
    .Instruction_ID(ID), .Instruction_EX(EX), .Instruction_MEM(MEM), .src_reg_ID(controller_1_src_reg),
    .des_reg_EX(id_ex_1_des_reg_o), .des_reg_MEM(ex_mem_1_des_reg_o), .stall(data_confilct_1_stall),
    .rW(id_ex_1_rw_o), .rs_EX_MEM(rs_EX_MEM), .rt_EX_MEM(rt_EX_MEM), .rs_EX_WB(rs_EX_WB),
    .rt_EX_WB(rt_EX_WB), .in_2(RST), .in_1(T));
  // Probe on WB
  // Probe on WB_P
  and and_2 (and_2_out, decoder_1_out1, ERET);
  and and_3 (and_3_out, decoder_1_out2, ERET);
  and and_4 (and_4_out, decoder_1_out3, ERET);
  ID_EX id_ex_1 (
    .clk(T), .RST(RST), .Instruction_I(ID), .syscall_I(controller_1_out_13), .rW_I_2(controller_1_out_8),
    .AluX_I(controller_1_out_5), .rWE_I(controller_1_out_7), .AluY_I(controller_1_out_6),
    .MemW_I(controller_1_out_10), .oPC_I(ID_P), .MemW_O(id_ex_1_memw_o), .AluX_O(id_ex_1_alux_o),
    .AluY_O(id_ex_1_aluy_o), .WB(id_ex_1_wb), .oPC_O(EX_P), .Instruction_O(EX), .rW_I(controller_1_out_9),
    .AluOp_I(controller_1_out_4), .AluOp_O(id_ex_1_aluop_o), .EN_I(HALT), .rs_I(reg_file_1_rf_d1),
    .rt_I(reg_file_1_rf_d2), .rs_O(id_ex_1_rs_o), .rt_O(id_ex_1_rt_o), .des_reg_O(id_ex_1_des_reg_o),
    .des_reg_I(controller_1_des_reg), .stall(data_confilct_1_stall), .Branch_O(id_ex_1_branch_o),
    .Branch_I(controller_1_branch), .B_instruc(pc_1_b_instruc), .LHU_I(controller_1_out_14),
    .LHU_O(id_ex_1_lhu_o), .sys_O(id_ex_1_sys_o), .rW_O(id_ex_1_rw_o), .inter(or_4_out),
    .ERET_I(controller_1_eret), .ERET_O(id_ex_1_eret_o));
  or or_4 (or_4_out, interrupt, ERET);
  // Probe on \总周期数 
  // Probe on \无条件分支指令数 
  // Probe on \有条件分支成功跳转 
  // Probe on \load_use次数 
  // Probe on \插入气泡数 
  or or_5 (RST1, and_2_out, RST);
  or or_6 (RST2, and_3_out, RST);
  or or_7 (RST3, and_4_out, RST);
  Multiplexer #(.select(2), .width(32)) multiplexer_3 (
    .in0(id_ex_1_rs_o), .in1(MEM_RES), .in2(WB_DATA), .in3(MEM_RES), .out(multiplexer_3_out),
    .sel({rs_EX_WB, rs_EX_MEM}));  // open: en
  Multiplexer #(.select(2), .width(32)) multiplexer_4 (
    .in0(id_ex_1_rt_o), .in1(MEM_RES), .in2(WB_DATA), .in3(MEM_RES), .out(multiplexer_4_out),
    .sel({rt_EX_WB, rt_EX_MEM}));  // open: en
  Syscall syscall_1 (
    .in_1(multiplexer_3_out), .in_2(multiplexer_4_out), .in_3(id_ex_1_sys_o), .in_4(T), .in_5(RST),
    .out_7(HALT), .out_8(SyscallOut), .GO(GO));
  // Probe on EX
  // Probe on alui_1_out_7
  AluI alui_1 (
    .in_3(EX), .in_1(id_ex_1_alux_o), .in_2(id_ex_1_aluy_o), .in_4(multiplexer_3_out),
    .in_5(multiplexer_4_out), .in_6(EX_P), .out_7(alui_1_out_7), .out_8(alui_1_out_8));
  Alu alu_1 (
    .X(alui_1_out_7), .Y(alui_1_out_8), .AluOP(id_ex_1_aluop_o), .Equal(alu_1_equal), .Result(alu_1_result));  // open: Signed_Overflow, UnSigned_Overflow, Result_2
  // Probe on alui_1_out_8
  // Probe on MEM
  EX_MEM ex_mem_1 (
    .clk(T), .RST(RST), .Data_I(multiplexer_4_out), .Data_O(ex_mem_1_data_o), .MemW_O(ex_mem_1_memw_o),
    .WB_O(ex_mem_1_wb_o), .MemW_I(id_ex_1_memw_o), .WB_I(id_ex_1_wb), .RES_I(alu_1_result), .RES_O(MEM_RES),
    .EN_I(HALT), .EN_O(ex_mem_1_en_o), .rs_EX_MEM_O(ex_mem_1_rs_ex_mem_o),
    .rt_EX_MEM_O(ex_mem_1_rt_ex_mem_o), .Instruction_I(EX), .Instruction_O(MEM),
    .des_reg_I(id_ex_1_des_reg_o), .des_reg_O(ex_mem_1_des_reg_o), .LHU_I(id_ex_1_lhu_o),
    .LHU_O(ex_mem_1_lhu_o), .rs_O(ex_mem_1_rs_o), .rs_I(multiplexer_3_out), .HALT(HALT),
    .rs_EX_MEM_I(rs_EX_MEM), .rt_EX_MEM_I(rt_EX_MEM), .inter(or_8_out), .oPC_I(EX_P), .oPC_O(MEM_P),
    .ERET_I(id_ex_1_eret_o), .ERET_O(ex_mem_1_eret_o));
  // Probe on alu_1_result
  // Probe on MEM_RES
  or or_8 (or_8_out, interrupt, ERET);
  Multiplexer #(.width(32)) multiplexer_5 (
    .in0(ex_mem_1_data_o), .in1(WB_DATA), .out(multiplexer_5_out), .sel(and_5_out));  // open: en
  and and_5 (and_5_out, ex_mem_1_memw_o, or_9_out);
  or or_9 (or_9_out, ex_mem_1_rs_ex_mem_o, ex_mem_1_rt_ex_mem_o);
  Adder #(.width(32)) adder_1 (.a(ex_mem_1_rs_o), .b({{16{1'b0}}, MEM[15:0]}), .out(adder_1_out));  // open: cin, cout
  Shifter #(.width(32), .shift("lr")) shifter_1 (.in(adder_1_out), .\dist (5'b00010), .out(shifter_1_out));
  // MIPS_RAM mips_ram_1: pin names not known; wires that end beside it: multiplexer_5_out, ex_mem_1_memw_o, T, 1'b1, RST, mips_ram_1_p6, mips_ram_1_p7, MEM_P
  // Probe on mem_wb_1_res_o
  assign bit_extender_1_out = {{16{1'b0}}, mips_ram_1_p6[15:0]};  // Bit_Extender bit_extender_1
  assign mips_ram_1_p7 = {{16{1'b0}}, mips_ram_1_p6[31:16]};  // Bit_Extender bit_extender_2
  // Probe on mem_wb_1_data_o
  MEM_WB mem_wb_1 (
    .clk(T), .RST(RST), .WB_I(ex_mem_1_wb_o), .Data_I(multiplexer_6_out),
    .WB_O({mem_wb_1_wb_o[3], mem_wb_1_wb_o_2, mem_wb_1_wb_o[0]}), .Data_O(mem_wb_1_data_o), .RES_I(MEM_RES),
    .RES_O(mem_wb_1_res_o), .EN_O(mem_wb_1_en_o), .EN_I(ex_mem_1_en_o), .Instruction_O(WB),
    .Instruction_I(MEM), .HALT(HALT), .oPC_I(MEM_P), .oPC_O(WB_P), .ERET_I(ex_mem_1_eret_o), .ERET_O(ERET),
    .inter(or_10_out));
  Multiplexer #(.width(32)) multiplexer_6 (
    .in0(mips_ram_1_p6), .in1(multiplexer_7_out), .out(multiplexer_6_out), .sel(ex_mem_1_lhu_o));  // open: en
  Multiplexer #(.width(32)) multiplexer_7 (
    .in0(bit_extender_1_out), .in1(mips_ram_1_p7), .out(multiplexer_7_out), .sel(adder_1_out[1]));  // open: en
  // Probe on mem_wb_1_data_o
  // Probe on WB_P
  or or_10 (or_10_out, interrupt, ERET);
  Multiplexer #(.width(32)) multiplexer_8 (
    .in0(mem_wb_1_data_o), .in1(mem_wb_1_res_o), .out(WB_DATA), .sel(mem_wb_1_wb_o[0]));  // open: en
  // Probe on WB_DATA
  // Probe on cPC
  Shifter #(.width(24), .shift("lr")) shifter_2 (.in(WB_P[23:0]), .\dist (5'b00010), .out(cPC));

  // Notes on the sheet:
  //   中断源
  //   中断等待指示
  //   contents of rom_1 (hex, n*v repeats v):
  //   20110200 20020022 112020 c 2231ffff 1620fffc 20020032 c 20080001 20090003 20110876 112020 20020022 c
  //   200b0008 1118804 1318804 112020 20020022 c 216bffff 1560fff9 20080001 20090003 20110876 118d00
  //   112020 20020022 c 200b0008 1118806 1318806 112020 20020022 c 216bffff 1560fff9 20090000 200b0010
  //   34118483 20120404 118c00 129400 36318281 22520404 ad310000 2328820 21290004 216bffff 1560fffb
  //   200b0020 20090000 95310000 112020 20020022 c 21290002 216bffff 1560fff9 2011000f 112020 20020022 c
  //   2231ffff 1e20fffb 2002000a c 2002000a c 3c0100ff 343dffff 27bdfffc afb00000 27bdfffc afb30000
  //   27bdfffc afb40000 27bdfffc afb50000 27bdfffc afb60000 27bdfffc afa40000 27bdfffc afa20000 20160001
  //   20140006 20150001 168020 108100 2149825 132020 20020022 c 1600fffa 295a022 1680fff7 8fa20000
  //   27bd0004 8fa40000 27bd0004 8fb60000 27bd0004 8fb50000 27bd0004 8fb40000 27bd0004 8fb30000 27bd0004
  //   8fb00000 27bd0004 42000018 3c0100ff 343dffff 27bdfffc afb00000 27bdfffc afb30000 27bdfffc afb40000
  //   27bdfffc afb50000 27bdfffc afb60000 27bdfffc afa40000 27bdfffc afa20000 20160002 20140006 20150001
  //   168020 108100 2149825 132020 20020022 c 1600fffa 295a022 1680fff7 8fa20000 27bd0004 8fa40000
  //   27bd0004 8fb60000 27bd0004 8fb50000 27bd0004 8fb40000 27bd0004 8fb30000 27bd0004 8fb00000 27bd0004
  //   42000018 3c0100ff 343dffff 27bdfffc afb00000 27bdfffc afb30000 27bdfffc afb40000 27bdfffc afb50000
  //   27bdfffc afb60000 27bdfffc afa40000 27bdfffc afa20000 20160003 20140006 20150001 168020 108100
  //   2149825 132020 20020022 c 1600fffa 295a022 1680fff7 8fa20000 27bd0004 8fa40000 27bd0004 8fb60000
  //   27bd0004 8fb50000 27bd0004 8fb40000 27bd0004 8fb30000 27bd0004 8fb00000 27bd0004 42000018
  //   数码管输出
endmodule

module Controller (
  input  [5:0] in_1,
  input  [5:0] in_2,
  output [3:0] Branch,
  output [3:0] out_4,
  output [1:0] out_5,
  output [2:0] out_6,
  output out_7,
  output [1:0] out_8,
  output out_9,
  output out_10,
  output [1:0] out_11,
  output out_12,
  output out_13,
  output out_14,
  output out_15,
  output [2:0] src_reg,
  output [2:0] des_reg,
  output ERET
);

  wire add, addi, addiu, addu, \and , and_2_out, and_3_out, and_5_out, and_6_out, and_7_out, and_8_out,
       and_9_out, and_10_out, and_11_out, and_12_out, and_18_out, andi, beq, bgtz_t, bne, comparator_26_eq,
       comparator_27_eq, j_t, jr, lhu_t, lw, \nor , Op__0, \or , or_1_out, or_2_out, or_3_out, or_4_out,
       or_5_out, or_6_out, or_12_out, or_13_out, or_14_out, or_15_out, or_16_out, or_17_out, or_18_out,
       or_19_out, or_20_out, ori, priority_encoder_2_p2, priority_encoder_2_p4, priority_encoder_2_p5, sll,
       sllv, slt, slti, sltiu, sltu, sra, srl, srlv, sub, syscall;
  wire [3:0] priority_encoder_1_out, priority_encoder_2_p1;

  Comparator #(.width(6)) comparator_1 (.a(in_1), .b({6{1'b0}}), .eq(Op__0));  // open: gt, lt
  Comparator #(.width(6)) comparator_2 (.a(in_1), .b(6'b000100), .eq(beq));  // open: gt, lt
  Comparator #(.width(6)) comparator_3 (.a(in_1), .b(6'b000101), .eq(bne));  // open: gt, lt
  Comparator #(.width(6)) comparator_4 (.a(in_1), .b(6'b001010), .eq(slti));  // open: gt, lt
  Comparator #(.width(6)) comparator_5 (.a(in_1), .b(6'b001101), .eq(ori));  // open: gt, lt
  Comparator #(.width(6)) comparator_6 (.a(in_1), .b(6'b001100), .eq(andi));  // open: gt, lt
  Comparator #(.width(6)) comparator_7 (.a(in_1), .b(6'b001001), .eq(addiu));  // open: gt, lt
  Comparator #(.width(6)) comparator_8 (.a(in_1), .b(6'b001000), .eq(addi));  // open: gt, lt
  Comparator #(.width(6)) comparator_9 (.a(in_1), .b(6'b000010), .eq(j_t));  // open: gt, lt
  or or_1 (or_1_out, bgtz_t, slti);
  or or_2 (or_2_out, bne, beq);
  or or_3 (or_3_out, add, addu, \and , sub, \or , \nor , slt, sltu, jr, sllv, srlv);
  or or_4 (or_4_out, add, addu, \and , sll, sra, srl, sub, \or , \nor , slt, sltu);
  Comparator #(.width(6)) comparator_10 (.a(in_1), .b(6'b101011), .eq(out_10));  // open: gt, lt
  Comparator #(.width(6)) comparator_11 (.a(in_1), .b(6'b100011), .eq(lw));  // open: gt, lt
  Comparator #(.width(6)) comparator_12 (.a(in_1), .b(6'b000011), .eq(des_reg[2]));  // open: gt, lt
  Comparator #(.width(6)) comparator_13 (.a(in_2), .b(6'b101011), .eq(sltu));  // open: gt, lt
  Comparator #(.width(6)) comparator_14 (.a(in_2), .b(6'b101010), .eq(slt));  // open: gt, lt
  Comparator #(.width(6)) comparator_15 (.a(in_2), .b(6'b100111), .eq(\nor ));  // open: gt, lt
  Comparator #(.width(6)) comparator_16 (.a(in_2), .b(6'b100101), .eq(\or ));  // open: gt, lt
  Comparator #(.width(6)) comparator_17 (.a(in_2), .b(6'b100100), .eq(\and ));  // open: gt, lt
  or or_5 (or_5_out, des_reg[2], addi, lw, out_10, addiu, lhu_t);
  Priority_Encoder #(.select(4)) priority_encoder_1 (
    .in5(or_5_out), .in7(andi), .in8(ori), .in11(or_1_out), .in12(sltiu), .in14(or_2_out),
    .out(priority_encoder_1_out));  // open: in0, in1, in2, in3, in4, in6, in9, in10, in13, in15, gs, en_out, en_in
  or or_6 (or_6_out, des_reg[2], j_t);
  // AND_Gate and_1 has open pins: in0=or_6_out, in1=Op__0, out=open
  or or_7 (src_reg[0], addi, addiu, andi, ori, out_10, lw, beq, bne, slti, lhu_t, bgtz_t, and_2_out);
  and and_2 (and_2_out, or_3_out, Op__0);
  or or_8 (src_reg[1], out_10, lw, sllv, srlv, beq, bne, lhu_t, and_3_out);
  and and_3 (and_3_out, or_4_out, Op__0);
  Comparator #(.width(6)) comparator_18 (.a(in_2), .b(6'b100010), .eq(sub));  // open: gt, lt
  Comparator #(.width(6)) comparator_19 (.a(in_2), .b(6'b100001), .eq(addu));  // open: gt, lt
  Comparator #(.width(6)) comparator_20 (.a(in_2), .b(6'b100000), .eq(add));  // open: gt, lt
  Comparator #(.width(6)) comparator_21 (.a(in_2), .b(6'b001100), .eq(syscall));  // open: gt, lt
  Comparator #(.width(6)) comparator_22 (.a(in_2), .b(6'b001000), .eq(jr));  // open: gt, lt
  Comparator #(.width(6)) comparator_23 (.a(in_2), .b(6'b000011), .eq(sra));  // open: gt, lt
  Comparator #(.width(6)) comparator_24 (.a(in_2), .b(6'b000010), .eq(srl));  // open: gt, lt
  Comparator #(.width(6)) comparator_25 (.a(in_2), .b({6{1'b0}}), .eq(sll));  // open: gt, lt
  Multiplexer #(.width(4)) multiplexer_1 (
    .in0(priority_encoder_1_out), .in1(priority_encoder_2_p1), .out(out_4), .sel(Op__0));  // open: en
  // Priority_Encoder #(.select(4)) priority_encoder_2: pin names not known; wires that end beside it: priority_encoder_2_p1, priority_encoder_2_p2, sra, priority_encoder_2_p4, priority_encoder_2_p5, sub, \and , \or , \nor , slt, sltu
  or or_9 (priority_encoder_2_p2, sll, sllv);
  or or_10 (priority_encoder_2_p5, add, addu);
  Comparator #(.width(6)) comparator_26 (.a(in_1), .b(6'b010000), .eq(comparator_26_eq));  // open: gt, lt
  and and_4 (ERET, comparator_26_eq, comparator_27_eq);
  Comparator #(.width(6)) comparator_27 (.a(in_2), .b(6'b011000), .eq(comparator_27_eq));  // open: gt, lt
  Multiplexer #(.select(2), .width(2)) multiplexer_2 (
    .in0(2'b10), .in1(2'b11), .in2(2'b00), .in3(2'b00), .out(out_8), .sel({Op__0, des_reg[2]}));  // open: en
  or or_11 (priority_encoder_2_p4, srl, srlv);
  or or_12 (or_12_out, addiu, lw, addi, des_reg[2], ori, andi, lhu_t, slti);
  or or_13 (or_13_out, \nor , sub, \or , \and , slt, add, sllv, sra, addu, srl, sltu, sll, srlv);
  Multiplexer multiplexer_3 (.in0(or_12_out), .in1(or_13_out), .out(out_7), .sel(Op__0));  // open: en
  and and_5 (and_5_out, Op__0, jr);
  and and_6 (and_6_out, ~Op__0, beq);  // AND_Gate
  and and_7 (and_7_out, ~Op__0, bne);  // AND_Gate
  or or_14 (or_14_out, sra, srl, sllv, sll, srlv);
  or or_15 (or_15_out, slti, lw, out_10, addiu, lhu_t, addi);
  or or_16 (or_16_out, andi, ori);
  Comparator #(.width(6)) comparator_28 (.a(in_1), .b(6'b000111), .eq(bgtz_t));  // open: gt, lt
  Comparator #(.width(6)) comparator_29 (.a(in_2), .b(6'b000100), .eq(sllv));  // open: gt, lt
  or or_17 (or_17_out, des_reg[2], j_t);
  Priority_Encoder #(.select(2)) priority_encoder_3 (
    .in0(1'b1), .in1(and_5_out), .in2(and_6_out), .in3(and_7_out), .out(Branch[2:1]));  // open: gs, en_out, en_in
  and and_8 (and_8_out, Op__0, or_14_out);
  and and_9 (and_9_out, des_reg[2], ~Op__0);  // AND_Gate
  and and_10 (and_10_out, ~Op__0, or_15_out);  // AND_Gate
  and and_11 (and_11_out, ~Op__0, or_16_out);  // AND_Gate
  or or_18 (or_18_out, sllv, srlv);
  and and_12 (and_12_out, or_18_out, Op__0);
  or or_19 (or_19_out, add, addu, \and , sll, sra, srl, sub, \or , \nor , slt, sltu, sllv, srlv);
  and and_13 (Branch[0], or_17_out, ~Op__0);  // AND_Gate
  or or_20 (or_20_out, lhu_t, lw);
  Priority_Encoder #(.select(2)) priority_encoder_4 (
    .in0(1'b1), .in1(and_8_out), .in2(and_9_out), .out(out_5));  // open: in3, gs, en_out, en_in
  Priority_Encoder priority_encoder_5 (
    .in0(1'b1), .in1(and_8_out), .in2(and_10_out), .in3(and_11_out), .in4(and_9_out), .in5(and_12_out),
    .out(out_6));  // open: in6, in7, en_in, gs, en_out
  or or_21 (des_reg[0], addi, addiu, andi, ori, lw, slti, lhu_t);
  and and_14 (des_reg[1], or_19_out, Op__0);
  Comparator #(.width(6)) comparator_30 (.a(in_1), .b(6'b100101), .eq(lhu_t));  // open: gt, lt
  Comparator #(.width(6)) comparator_31 (.a(in_2), .b(6'b000110), .eq(srlv));  // open: gt, lt
  and and_15 (Branch[3], bgtz_t, ~Op__0);  // AND_Gate
  and and_16 (out_13, syscall, Op__0);
  and and_17 (out_14, lhu_t, ~Op__0);  // AND_Gate
  and and_18 (and_18_out, or_20_out, ~Op__0);  // AND_Gate
  not not_1 (out_9, and_18_out);
  Decoder #(.select(5)) decoder_1 ();  // open: out0, out1, out2, out3, out4, out5, out6, out7, out8, out9, out10, out11, out12, out13, out14, out15, out16, out17, out18, out19, out20, out21, out22, out23, out24, out25, out26, out27, out28, out29, out30, out31, sel, en
  Decoder #(.select(5)) decoder_2 ();  // open: out0, out1, out2, out3, out4, out5, out6, out7, out8, out9, out10, out11, out12, out13, out14, out15, out16, out17, out18, out19, out20, out21, out22, out23, out24, out25, out26, out27, out28, out29, out30, out31, sel, en
  Decoder #(.select(5)) decoder_3 ();  // open: out0, out1, out2, out3, out4, out5, out6, out7, out8, out9, out10, out11, out12, out13, out14, out15, out16, out17, out18, out19, out20, out21, out22, out23, out24, out25, out26, out27, out28, out29, out30, out31, sel, en
  Decoder #(.select(5)) decoder_4 ();  // open: out0, out1, out2, out3, out4, out5, out6, out7, out8, out9, out10, out11, out12, out13, out14, out15, out16, out17, out18, out19, out20, out21, out22, out23, out24, out25, out26, out27, out28, out29, out30, out31, sel, en

  assign out_11 = Branch[2:1];
  assign out_12 = Branch[0];
  assign out_15 = Branch[3];
  assign src_reg[2] = out_13;

  // Other names for the same wires on the sheet: AluOp[3:0] = out_4; AluX[1:0] = out_5; AluY[2:0] = out_6;
  //   J = Branch[0]; PCW[1:0] = Branch[2:1]; BGTZ = Branch[3]; jal = des_reg[2]; LHU = out_14; Op[5:0] = in_1;
  //   rW = out_9; rW_t[1:0] = out_8; rWE = out_7; Sp[5:0] = in_2; Sys = out_13; MemW = out_10; sw = out_10

  // Notes on the sheet:
  //   source_rs
  //   source_rt
  //   sys->2&4
  //   Instructions
  //   Reg Write Dst
  //   O->rD
  //   2->rT
  //   3->$31
  //   Alu Operator
  //   reg Write Enable
  //   des_rd
  //   RAM Write
  //   Branching
  //   0->PC++
  //   1->$rS
  //   2->beq
  //   3->bne
  //   des_rt
  //   J/JAL
  //   3->$31
  //   CCMB
  //   lbtz(CCMB)
  //   Syscall
  //   lbu(CCMB)
  //   Reg Write Src
  //   0->MemO
  //   1->AluR
  //   Alu Input
  //   0->rS(default)
  //   1->rT
  //   2->PC
  //   0->rT(default)
  //   1->sA
  //   2->Immi_S
  //   3->Immi_U
  //   4->4
  //   5->rS(CCMB)
endmodule

module Alu (
  input  [31:0] X,
  input  [31:0] Y,
  input  [3:0] AluOP,
  output Signed_Overflow,
  output UnSigned_Overflow,
  output Equal,
  output [31:0] Result,
  output [31:0] Result_2
);

  wire OF1, OF2, UOF1, UOF2, xnor_1_out, xor_1_out, xor_2_out, xor_3_out;
  wire [0:0] R12, R13;
  wire [31:0] R1, R2, R3, R4, R5, R6, R7, R8, R9, R10, R11, R21, R22;

  // Probe on X
  // Probe on X
  // Probe on Y
  // Probe on Y
  Shifter #(.width(32)) shifter_1 (.in(X), .\dist (Y[4:0]), .out(R1));
  Shifter #(.width(32), .shift("ar")) shifter_2 (.in(X), .\dist (Y[4:0]), .out(R2));
  Shifter #(.width(32), .shift("lr")) shifter_3 (.in(X), .\dist (Y[4:0]), .out(R3));
  Multiplier #(.width(32)) multiplier_1 (.a(X), .b(Y), .out(R4), .cout(R21));  // open: cin
  Divider #(.width(32)) divider_1 (.a(X), .b(Y), .out(R5), .rem(R22));  // open: upper
  xnor xnor_1 (xnor_1_out, X[31], Y[31]);
  xor xor_1 (xor_1_out, Y[31], X[31]);
  // Probe on AluOP
  Adder #(.width(32)) adder_1 (.a(X), .b(Y), .out(R6), .cin(1'b0), .cout(UOF1));
  xor xor_2 (xor_2_out, Y[31], R6[31]);
  and and_1 (OF1, xnor_1_out, xor_2_out);
  Subtractor #(.width(32)) subtractor_1 (.a(X), .b(Y), .out(R7), .bin(1'b0), .bout(UOF2));
  xor xor_3 (xor_3_out, X[31], R7[31]);
  and and_2 (OF2, xor_1_out, xor_3_out);
  // Probe on Result
  // Probe on Result
  assign R8 = X & Y;  // AND_Gate and_3, 32 bits wide
  assign R9 = X | Y;  // OR_Gate or_1, 32 bits wide
  assign R10 = X ^ Y;  // XOR_Gate xor_4, 32 bits wide
  assign R11 = ~(X | Y);  // NOR_Gate nor_1, 32 bits wide
  Comparator #(.width(32)) comparator_1 (.a(X), .b(Y), .eq(Equal), .lt(R12[0]));  // open: gt
  Comparator #(.width(32), .mode("unsigned")) comparator_2 (.a(X), .b(Y), .lt(R13[0]));  // open: gt, eq
  // Probe on Result_2
  Multiplexer #(.select(4), .width(32)) multiplexer_1 (
    .in0(R1), .in1(R2), .in2(R3), .in3(R4), .in4(R5), .in5(R6), .in6(R7), .in7(R8), .in8(R9), .in9(R10),
    .in10(R11), .in11({{31{1'b0}}, R12[0]}), .in12({{31{1'b0}}, R13[0]}), .in13({32{1'b0}}),
    .in14({32{1'b0}}), .in15({32{1'b0}}), .out(Result), .sel(AluOP));  // open: en
  Multiplexer #(.select(4)) multiplexer_2 (
    .in0(1'b0), .in1(1'b0), .in2(1'b0), .in3(1'b0), .in4(1'b0), .in5(UOF1), .in6(UOF2), .in7(1'b0),
    .in8(1'b0), .in9(1'b0), .in10(1'b0), .in11(1'b0), .in12(1'b0), .in13(1'b0), .in14(1'b0), .in15(1'b0),
    .out(UnSigned_Overflow), .sel(AluOP));  // open: en
  Multiplexer #(.select(4), .width(32)) multiplexer_3 (
    .in0({32{1'b0}}), .in1({32{1'b0}}), .in2({32{1'b0}}), .in3(R21), .in4(R22), .in5({32{1'b0}}),
    .in6({32{1'b0}}), .in7({32{1'b0}}), .in8({32{1'b0}}), .in9({32{1'b0}}), .in10({32{1'b0}}),
    .in11({32{1'b0}}), .in12({32{1'b0}}), .in13({32{1'b0}}), .in14({32{1'b0}}), .in15({32{1'b0}}),
    .out(Result_2), .sel(AluOP));  // open: en
  Multiplexer #(.select(4)) multiplexer_4 (
    .in0(1'b0), .in1(1'b0), .in2(1'b0), .in3(1'b0), .in4(1'b0), .in5(OF1), .in6(OF2), .in7(1'b0), .in8(1'b0),
    .in9(1'b0), .in10(1'b0), .in11(1'b0), .in12(1'b0), .in13(1'b0), .in14(1'b0), .in15(1'b0),
    .out(Signed_Overflow), .sel(AluOP));  // open: en

  // Other names for the same wires on the sheet: OF = Signed_Overflow; Result2[31:0] = Result_2; S[3:0] = AluOP;
  //   UOF = UnSigned_Overflow

  // Notes on the sheet:
  //   不要改变此引脚区域内容，也不要改变ALU封装形式
  //   输入引脚
  //   请在下方利用上方输入输出引脚的隧道信号构建ALU电路，ctrl+d复制选择部件
  //   华中科技大学计算机学院 计算机组成原理，鸣谢加州大学伯克利CS61C课程
  //   输出引脚
  //   探测区域
endmodule

module PC (
  input  [3:0] Branch_I,
  input  in_2,
  input  stall,
  input  sys,
  input  [31:0] in_5,
  input  [25:0] in_6,
  input  [15:0] in_7,
  input  in_8,
  input  in_9,
  input  in_10,
  input  in_11,
  input  interrupt,
  input  ERET,
  input  [23:0] EPC,
  input  [23:0] inter_addr,
  output B_instruc,
  output [31:0] out_17,
  output [23:0] out_18,
  output [15:0] out_19,
  output [15:0] out_20,
  output [15:0] out_21,
  output [15:0] out_22,
  output [15:0] \气泡数 ,
  output [15:0] \load_use数 
);

  wire and_1_out, and_2_out, and_3_out, and_5_out, and_6_out, and_7_out, and_8_out, and_9_out, and_10_out,
       and_11_out, and_12_out, and_13_out, beq, bne, CNT, comparator_1_gt, comparator_2_gt, comparator_3_gt,
       incrementer_1_p1, JE, JN, JR, not_1_out, not_2_out, or_2_out, or_3_out, or_4_out;
  wire [1:1] and_4_out;
  wire [31:0] adder_1_out, bit_extender_1_out, bit_extender_2_out, multiplexer_1_out, multiplexer_2_out,
       multiplexer_3_out, multiplexer_4_out, NPC, PC_1, shifter_1_out, shifter_2_out, shifter_3_out,
       subtractor_2_out, undriven;
  wire [31:24] incrementer_2_p3;

  Shifter #(.width(32), .shift("ar")) shifter_1 (.in({in_7, {16{1'b0}}}), .\dist (5'b01110), .out(shifter_1_out));
  Decoder #(.select(2)) decoder_1 (.out2(beq), .out3(bne), .sel(Branch_I[2:1]));  // open: out0, out1, en
  Adder #(.width(32)) adder_1 (.a(out_17), .b(shifter_1_out), .out(adder_1_out));  // open: cin, cout
  Shifter #(.width(32), .shift("lr")) shifter_2 (.in(adder_1_out), .\dist (5'b00010), .out(shifter_2_out));
  Subtractor #(.width(32)) subtractor_1 (.a(shifter_2_out), .b(32'h2));  // open: out, bin, bout
  // Incrementer incrementer_1: pin names not known; wires that end beside it: incrementer_1_p1, Branch_I[2:1]
  Multiplexer #(.width(32)) multiplexer_1 (
    .in0(undriven), .in1(PC_1), .out(multiplexer_1_out), .sel(in_8));  // open: en
  and and_1 (and_1_out, beq, in_8);
  and and_2 (and_2_out, bne, not_1_out);
  not not_1 (not_1_out, in_8);
  and and_3 (and_3_out, Branch_I[3], comparator_1_gt);
  Comparator #(.width(32)) comparator_1 (.a(in_5), .b({32{1'b0}}), .gt(comparator_1_gt));  // open: eq, lt
  Shifter #(.width(32), .shift("lr")) shifter_3 (.in(in_5), .\dist (5'b00010), .out(shifter_3_out));
  Multiplexer #(.width(32)) multiplexer_2 (
    .in0(PC_1), .in1(undriven), .out(multiplexer_2_out), .sel(in_8));  // open: en
  or or_1 (B_instruc, Branch_I[0], and_1_out, and_2_out, and_3_out);
  Multiplexer #(.select(2), .width(32)) multiplexer_3 (
    .in0(PC_1), .in1(shifter_3_out), .in2(multiplexer_2_out), .in3(multiplexer_1_out),
    .out(multiplexer_3_out), .sel(Branch_I[2:1]));  // open: en
  Multiplexer #(.select(2), .width(32)) multiplexer_4 (
    .in0(multiplexer_3_out), .in1(subtractor_2_out), .in2(undriven), .out(multiplexer_4_out),
    .sel({and_4_out[1], Branch_I[0]}));  // open: in3, en
  and and_4 (and_4_out[1], comparator_2_gt, Branch_I[3]);
  Subtractor #(.width(32)) subtractor_2 (
    .a({{6{1'b0}}, in_6}), .b(32'hc00), .out(subtractor_2_out));  // open: bin, bout
  Comparator #(.width(32)) comparator_2 (.a(in_5), .b({32{1'b0}}), .gt(comparator_2_gt));  // open: eq, lt
  assign bit_extender_1_out = {{8{1'b0}}, inter_addr};  // Bit_Extender bit_extender_1
  assign bit_extender_2_out = {{8{1'b0}}, EPC};  // Bit_Extender bit_extender_2
  // Probe on NPC
  Multiplexer #(.select(2), .width(32)) multiplexer_5 (
    .in0(multiplexer_4_out), .in1(bit_extender_1_out), .in2(bit_extender_2_out), .out(NPC),
    .sel({ERET, interrupt}));  // open: in3, en
  and and_5 (and_5_out, in_10, not_2_out);
  not not_2 (not_2_out, stall);
  // Incrementer incrementer_2: pin names not known; wires that end beside it: Branch_I[0], Branch_I[3], {incrementer_2_p3, out_18}, PC_1
  Register #(.width(32)) PC (.D(NPC), .en(and_5_out), .Q({incrementer_2_p3, out_18}), .clk(in_11), .clr(in_9));
  // Probe on out_18
  Decoder #(.select(2)) decoder_2 (.out1(JR), .out2(JE), .out3(JN), .sel(Branch_I[2:1]));  // open: out0, en
  Shifter #(.width(32)) shifter_4 (.in({incrementer_2_p3, out_18}), .\dist (5'b00010), .out(out_17));
  Counter #(.width(16), .max('hffff)) counter_1 (
    .count(CNT), .Q(out_19), .clk(in_11), .clr(in_9));  // open: load, D, carry
  or or_2 (or_2_out, JN, Branch_I[3], JE);
  Counter #(.width(16), .max('hffff)) counter_2 (
    .count(and_6_out), .Q(out_21), .clk(in_11), .clr(in_9));  // open: load, D, carry
  and and_6 (and_6_out, or_2_out, CNT);
  and and_7 (and_7_out, comparator_3_gt, Branch_I[3]);
  Comparator #(.width(32)) comparator_3 (.a(in_5), .b({32{1'b0}}), .gt(comparator_3_gt));  // open: eq, lt
  and and_8 (and_8_out, JN, ~in_8);  // AND_Gate
  and and_9 (and_9_out, in_8, JE);
  Counter #(.width(16), .max('hffff)) counter_3 (
    .count(and_10_out), .Q(\load_use数 ), .clk(in_11));  // open: load, D, carry, clr
  and and_10 (and_10_out, stall, CNT);
  or or_3 (or_3_out, JR, Branch_I[0]);
  and and_11 (and_11_out, or_3_out, CNT);
  or or_4 (or_4_out, and_7_out, and_8_out, and_9_out);
  and and_12 (and_12_out, or_4_out, CNT);
  Counter #(.width(16), .max('hffff)) counter_4 (
    .count(and_11_out), .Q(out_20), .clk(in_11), .clr(in_9));  // open: load, D, carry
  or or_5 (CNT, in_10, in_2);
  Counter #(.width(16), .max('hffff)) counter_5 (
    .count(and_12_out), .Q(out_22), .clk(in_11), .clr(in_9));  // open: load, D, carry
  Counter #(.width(16), .max('hffff)) counter_6 (
    .count(and_13_out), .Q(\气泡数 ), .clk(in_11));  // open: load, D, carry, clr
  and and_13 (and_13_out, stall, CNT);

  // Other names for the same wires on the sheet: immi[15:0] = in_7; inst[25:0] = in_6; J = Branch_I[0];
  //   PC[23:0] = out_18; AluEq = in_8; PCW[1:0] = Branch_I[2:1]; BGTZ = Branch_I[3]; EN = in_10; END = in_2;
  //   oPC[31:0] = out_17; rS[31:0] = in_5; RST = in_9; T = in_11; 总周期数[15:0] = out_19; 无条件分支指令数[15:0] = out_20;
  //   有条件分支成功跳转[15:0] = out_22; 有条件分支指令数[15:0] = out_21
endmodule

module Syscall (
  input  [31:0] in_1,
  input  [31:0] in_2,
  input  in_3,
  input  in_4,
  input  in_5,
  input  GO,
  output out_7,
  output [31:0] out_8
);

  wire and_1_out, and_2_out, comparator_1_eq, not_1_out, or_1_out, or_2_out, register_2_q, stall;
  wire [31:0] multiplexer_1_out;

  Comparator #(.width(32)) comparator_1 (.a(in_1), .b(32'h22), .eq(comparator_1_eq));  // open: gt, lt
  and and_1 (and_1_out, in_3, not_1_out);
  not not_1 (not_1_out, comparator_1_eq);
  and and_2 (and_2_out, ~not_1_out, in_3);  // AND_Gate
  Register #(.width(32)) register_1 (.D(multiplexer_1_out), .Q(out_8), .clk(in_4), .clr(in_5));  // open: en
  Multiplexer #(.width(32)) multiplexer_1 (
    .in0(out_8), .in1(in_2), .out(multiplexer_1_out), .sel(and_2_out));  // open: en
  or or_1 (or_1_out, register_2_q, and_1_out);
  Register #(.width(1)) register_2 (.D(or_1_out), .Q(register_2_q), .clk(in_4), .clr(or_2_out));  // open: en
  or or_2 (or_2_out, GO, in_5);
  not not_2 (out_7, register_2_q);
  // NOT_Gate not_3 has open pins: in=stall, out=open

  // Other names for the same wires on the sheet: EN = out_7; rS[31:0] = in_1; RST = in_5; rT[31:0] = in_2; Sys = in_3;
  //   SyscallOut[31:0] = out_8; T = in_4
endmodule

module AluI (
  input  [1:0] in_1,
  input  [2:0] in_2,
  input  [31:0] in_3,
  input  [31:0] in_4,
  input  [31:0] in_5,
  input  [31:0] in_6,
  output [31:0] out_7,
  output [31:0] out_8
);

  wire [31:0] shifter_1_out, shifter_2_out;

  // Probe on nothing
  // Probe on nothing
  Shifter #(.width(32), .shift("ar")) shifter_1 (.in({in_3[15:0], {16{1'b0}}}), .\dist (5'b10000), .out(shifter_1_out));
  Shifter #(.width(32), .shift("lr")) shifter_2 (.in({in_3[15:0], {16{1'b0}}}), .\dist (5'b10000), .out(shifter_2_out));
  Multiplexer #(.select(2), .width(32)) multiplexer_1 (
    .in0(in_4), .in1(in_5), .in2(in_6), .out(out_7), .sel(in_1));  // open: in3, en
  // Probe on in_1
  Multiplexer #(.select(3), .width(32)) multiplexer_2 (
    .in0(in_5), .in1({{27{1'b0}}, in_3[10:6]}), .in2(shifter_1_out), .in3(shifter_2_out), .in4(32'h4),
    .in5(in_4), .out(out_8), .sel(in_2));  // open: in6, in7, en
  // Probe on in_2

  // Other names for the same wires on the sheet: Instruction[31:0] = in_3; AluX[1:0] = in_1; AluY[2:0] = in_2;
  //   oPC[31:0] = in_6; rS[31:0] = in_4; rT[31:0] = in_5; X[31:0] = out_7; Y[31:0] = out_8

  // Notes on the sheet:
  //   Immi
  //   Immi
  //   sa
endmodule

module Reg_File (
  input  rW,
  input  rWE,
  input  [1:0] rW_2,
  input  Syscall,
  input  [31:0] RES,
  input  [31:0] Din,
  input  [31:0] Instruction_I,
  input  [4:0] rs,
  input  [4:0] rt,
  input  [4:0] rt_I,
  input  [4:0] rd,
  input  [4:0] rd_I,
  input  clk,
  output [31:0] RF_D1,
  output [31:0] RF_D2
);

  wire undriven;
  wire [4:0] multiplexer_2_out, multiplexer_3_out, multiplexer_4_out;
  wire [31:0] multiplexer_1_out;

  Multiplexer #(.width(32)) multiplexer_1 (.in0(Din), .in1(RES), .out(multiplexer_1_out), .sel(rW));  // open: en
  Multiplexer #(.select(2), .width(5)) multiplexer_2 (
    .in0(Instruction_I[15:11]), .in2(Instruction_I[20:16]), .in3({5{1'b1}}), .out(multiplexer_2_out),
    .sel(rW_2));  // open: in1, en
  Multiplexer #(.width(5)) multiplexer_3 (
    .in0(rt), .in1(5'b00100), .out(multiplexer_3_out), .sel(Syscall), .en(undriven));
  Multiplexer #(.width(5)) multiplexer_4 (
    .in0(rs), .in1(5'b00010), .out(multiplexer_4_out), .sel(Syscall), .en(undriven));
  // RegisterFile registerfile_1: pin names not known; wires that end beside it: Instruction_I[25:21], multiplexer_1_out, clk, rWE, multiplexer_2_out, multiplexer_4_out, multiplexer_3_out, RF_D1, RF_D2

  // Other names for the same wires on the sheet: rW_t[1:0] = rW_2
endmodule

module ID_EX (
  input  [31:0] Instruction_I,
  input  [31:0] rs_I,
  input  [31:0] rt_I,
  input  [31:0] oPC_I,
  input  clk,
  input  RST,
  input  rW_I,
  input  [1:0] rW_I_2,
  input  rWE_I,
  input  syscall_I,
  input  MemW_I,
  input  EN_I,
  input  [2:0] des_reg_I,
  input  stall,
  input  B_instruc,
  input  LHU_I,
  input  [3:0] Branch_I,
  input  inter,
  input  ERET_I,
  input  [1:0] AluX_I,
  input  [2:0] AluY_I,
  input  [3:0] AluOp_I,
  output [1:0] AluX_O,
  output [2:0] AluY_O,
  output [3:0] AluOp_O,
  output [31:0] Instruction_O,
  output [31:0] rs_O,
  output [31:0] rt_O,
  output [31:0] oPC_O,
  output [2:0] des_reg_O,
  output MemW_O,
  output [3:0] WB,
  output rW_O,
  output [3:0] Branch_O,
  output LHU_O,
  output sys_O,
  output ERET_O
);

  wire multiplexer_9_out, multiplexer_10_out, multiplexer_11_out, multiplexer_17_out, multiplexer_18_out,
       multiplexer_19_out, or_1_out, syscall_O;
  wire [1:0] multiplexer_4_out;
  wire [2:0] multiplexer_5_out, multiplexer_15_out;
  wire [3:0] multiplexer_6_out, multiplexer_12_out, multiplexer_16_out;
  wire [4:0] multiplexer_1_out, multiplexer_2_out, multiplexer_3_out, rd_I, rd_O, rs_I_t, rs_O_t, rt_I_t,
       rt_O_t;
  wire [31:0] multiplexer_7_out, multiplexer_8_out, multiplexer_13_out, multiplexer_14_out, subtractor_1_out;

  or or_1 (or_1_out, B_instruc, inter, stall);
  Register #(.width(5)) register_1 (.D(multiplexer_1_out), .en(EN_I), .Q(rs_O_t), .clk(clk), .clr(RST));
  Multiplexer #(.width(5)) multiplexer_1 (
    .in0(rs_I_t), .in1({5{1'b0}}), .out(multiplexer_1_out), .sel(or_1_out));  // open: en
  Register #(.width(5)) register_2 (.D(multiplexer_2_out), .en(EN_I), .Q(rt_O_t), .clk(clk), .clr(RST));
  Multiplexer #(.width(5)) multiplexer_2 (
    .in0(rt_I_t), .in1({5{1'b0}}), .out(multiplexer_2_out), .sel(or_1_out));  // open: en
  Multiplexer #(.width(5)) multiplexer_3 (
    .in0(rd_I), .in1({5{1'b0}}), .out(multiplexer_3_out), .sel(or_1_out));  // open: en
  Register #(.width(5)) register_3 (.D(multiplexer_3_out), .en(EN_I), .Q(rd_O), .clk(clk), .clr(RST));
  Register #(.width(2)) register_4 (.D(multiplexer_4_out), .en(EN_I), .Q(AluX_O), .clk(clk), .clr(RST));
  Multiplexer #(.width(2)) multiplexer_4 (
    .in0(AluX_I), .in1(2'b00), .out(multiplexer_4_out), .sel(or_1_out));  // open: en
  Register #(.width(3)) register_5 (.D(multiplexer_5_out), .en(EN_I), .Q(AluY_O), .clk(clk), .clr(RST));
  Multiplexer #(.width(3)) multiplexer_5 (
    .in0(AluY_I), .in1(3'b000), .out(multiplexer_5_out), .sel(or_1_out));  // open: en
  Multiplexer #(.width(4)) multiplexer_6 (
    .in0(AluOp_I), .in1(4'b0000), .out(multiplexer_6_out), .sel(or_1_out));  // open: en
  Multiplexer #(.width(32)) multiplexer_7 (
    .in0(oPC_I), .in1(subtractor_1_out), .out(multiplexer_7_out), .sel(or_1_out));  // open: en
  Subtractor #(.width(32)) subtractor_1 (.a(oPC_I), .b(32'h4), .out(subtractor_1_out));  // open: bin, bout
  Multiplexer #(.width(32)) multiplexer_8 (
    .in0(Instruction_I), .in1({32{1'b0}}), .out(multiplexer_8_out), .sel(or_1_out));  // open: en
  Multiplexer multiplexer_9 (.in0(syscall_I), .in1(1'b0), .out(multiplexer_9_out), .sel(or_1_out));  // open: en
  Multiplexer multiplexer_10 (.in0(MemW_I), .in1(1'b0), .out(multiplexer_10_out), .sel(or_1_out));  // open: en
  Register #(.width(4)) register_6 (.D(multiplexer_6_out), .en(EN_I), .Q(AluOp_O), .clk(clk), .clr(RST));
  Register #(.width(32)) register_7 (.D(multiplexer_7_out), .en(EN_I), .Q(oPC_O), .clk(clk), .clr(RST));
  Register #(.width(32)) register_8 (.D(multiplexer_8_out), .en(EN_I), .Q(Instruction_O), .clk(clk), .clr(RST));
  Register #(.width(1)) register_9 (.D(multiplexer_9_out), .en(EN_I), .Q(syscall_O), .clk(clk), .clr(RST));
  Register #(.width(1)) register_10 (.D(multiplexer_10_out), .en(EN_I), .Q(MemW_O), .clk(clk), .clr(RST));
  Multiplexer multiplexer_11 (.in0(ERET_I), .in1(1'b0), .out(multiplexer_11_out), .sel(or_1_out));  // open: en
  Multiplexer #(.width(4)) multiplexer_12 (
    .in0({rWE_I, rW_I_2, rW_I}), .in1(4'b0000), .out(multiplexer_12_out), .sel(or_1_out));  // open: en
  Register #(.width(4)) register_11 (.D(multiplexer_12_out), .en(EN_I), .Q(WB), .clk(clk), .clr(RST));
  Multiplexer #(.width(32)) multiplexer_13 (
    .in0(rs_I), .in1({32{1'b0}}), .out(multiplexer_13_out), .sel(or_1_out));  // open: en
  Register #(.width(32)) register_12 (.D(multiplexer_13_out), .en(EN_I), .Q(rs_O), .clk(clk), .clr(RST));
  Register #(.width(32)) register_13 (.D(multiplexer_14_out), .en(EN_I), .Q(rt_O), .clk(clk), .clr(RST));
  Multiplexer #(.width(32)) multiplexer_14 (
    .in0(rt_I), .in1({32{1'b0}}), .out(multiplexer_14_out), .sel(or_1_out));  // open: en
  Multiplexer #(.width(3)) multiplexer_15 (
    .in0(des_reg_I), .in1(3'b000), .out(multiplexer_15_out), .sel(or_1_out));  // open: en
  Register #(.width(3)) register_14 (.D(multiplexer_15_out), .en(EN_I), .Q(des_reg_O), .clk(clk), .clr(RST));
  Register #(.width(1)) register_15 (.D(multiplexer_11_out), .Q(ERET_O), .clk(clk), .clr(RST));  // open: en
  Multiplexer #(.width(4)) multiplexer_16 (
    .in0(Branch_I), .in1(4'b0000), .out(multiplexer_16_out), .sel(or_1_out));  // open: en
  Multiplexer multiplexer_17 (.in0(LHU_I), .in1(1'b0), .out(multiplexer_17_out), .sel(or_1_out));  // open: en
  Multiplexer multiplexer_18 (.in0(syscall_I), .in1(1'b0), .out(multiplexer_18_out), .sel(or_1_out));  // open: en
  Multiplexer multiplexer_19 (.in0(rW_I), .in1(1'b0), .out(multiplexer_19_out), .sel(or_1_out));  // open: en
  Register #(.width(4)) register_16 (.D(multiplexer_16_out), .en(EN_I), .Q(Branch_O), .clk(clk), .clr(RST));
  Register #(.width(1)) register_17 (.D(multiplexer_17_out), .en(EN_I), .Q(LHU_O), .clk(clk), .clr(RST));
  Register #(.width(1)) register_18 (.D(multiplexer_18_out), .en(EN_I), .Q(sys_O), .clk(clk), .clr(RST));
  Register #(.width(1)) register_19 (.D(multiplexer_19_out), .en(EN_I), .Q(rW_O), .clk(clk), .clr(RST));

  // Other names for the same wires on the sheet: rW_I_t[1:0] = rW_I_2
endmodule

module IF_ID (
  input  stall,
  input  B_instruc,
  input  inter,
  input  [31:0] Data_I,
  input  [31:0] oPC_I,
  input  HALT,
  input  clk,
  input  RST,
  output [31:0] Data_O,
  output [31:0] oPC_O
);

  wire and_1_out, not_1_out, or_1_out;
  wire [31:0] multiplexer_1_out, multiplexer_2_out, subtractor_1_out;

  not not_1 (not_1_out, stall);
  or or_1 (or_1_out, B_instruc, inter);
  and and_1 (and_1_out, not_1_out, HALT);
  Multiplexer #(.width(32)) multiplexer_1 (
    .in0(Data_I), .in1({32{1'b0}}), .out(multiplexer_1_out), .sel(or_1_out));  // open: en
  Register #(.width(32)) register_1 (.D(multiplexer_1_out), .en(and_1_out), .Q(Data_O), .clk(clk), .clr(RST));
  Multiplexer #(.width(32)) multiplexer_2 (
    .in0(oPC_I), .in1(subtractor_1_out), .out(multiplexer_2_out), .sel(or_1_out));  // open: en
  Subtractor #(.width(32)) subtractor_1 (.a(oPC_I), .b(32'h8), .out(subtractor_1_out));  // open: bin, bout
  Register #(.width(32)) register_2 (.D(multiplexer_2_out), .en(and_1_out), .Q(oPC_O), .clk(clk), .clr(RST));
endmodule

module EX_MEM (
  input  MemW_I,
  input  [3:0] WB_I,
  input  [31:0] rs_I,
  input  [31:0] Instruction_I,
  input  [31:0] oPC_I,
  input  [31:0] Data_I,
  input  [31:0] RES_I,
  input  [2:0] des_reg_I,
  input  rs_EX_MEM_I,
  input  rt_EX_MEM_I,
  input  HALT,
  input  clk,
  input  RST,
  input  LHU_I,
  input  EN_I,
  input  inter,
  input  ERET_I,
  output MemW_O,
  output [3:0] WB_O,
  output [31:0] Data_O,
  output [31:0] RES_O,
  output [31:0] Instruction_O,
  output [31:0] rs_O,
  output rs_EX_MEM_O,
  output rt_EX_MEM_O,
  output [2:0] des_reg_O,
  output LHU_O,
  output EN_O,
  output [31:0] oPC_O,
  output ERET_O
);

  wire multiplexer_1_out, multiplexer_2_out, multiplexer_5_out, multiplexer_7_out, multiplexer_12_out,
       register_2_q, register_6_q;
  wire [2:0] multiplexer_3_out;
  wire [3:0] multiplexer_4_out;
  wire [23:0] Addr_I, Addr_O, multiplexer_6_out;
  wire [31:0] multiplexer_8_out, multiplexer_9_out, multiplexer_10_out, multiplexer_11_out,
       multiplexer_13_out;

  Multiplexer multiplexer_1 (.in0(MemW_I), .in1(1'b0), .out(multiplexer_1_out), .sel(inter));  // open: en
  Register #(.width(1)) register_1 (.D(multiplexer_1_out), .en(HALT), .Q(MemW_O), .clk(clk), .clr(RST));
  Register #(.width(1)) register_2 (.D(rs_EX_MEM_I), .en(HALT), .Q(register_2_q), .clk(clk), .clr(RST));
  Multiplexer multiplexer_2 (.in0(register_2_q), .in1(1'b0), .out(multiplexer_2_out), .sel(inter));  // open: en
  Multiplexer #(.width(3)) multiplexer_3 (
    .in0(des_reg_I), .in1(3'b000), .out(multiplexer_3_out), .sel(inter));  // open: en
  Register #(.width(3)) register_3 (.D(multiplexer_3_out), .en(HALT), .Q(des_reg_O), .clk(clk), .clr(RST));
  Register #(.width(1)) register_4 (.D(multiplexer_2_out), .en(HALT), .Q(rs_EX_MEM_O), .clk(clk), .clr(RST));
  Register #(.width(4)) register_5 (.D(multiplexer_4_out), .en(HALT), .Q(WB_O), .clk(clk), .clr(RST));
  Multiplexer #(.width(4)) multiplexer_4 (.in0(WB_I), .in1(4'b0000), .out(multiplexer_4_out), .sel(inter));  // open: en
  Multiplexer multiplexer_5 (.in0(LHU_I), .in1(1'b0), .out(multiplexer_5_out), .sel(inter));  // open: en
  Register #(.width(1)) register_6 (.D(rt_EX_MEM_I), .en(HALT), .Q(register_6_q), .clk(clk), .clr(RST));
  Register #(.width(1)) register_7 (.D(multiplexer_5_out), .en(HALT), .Q(LHU_O), .clk(clk), .clr(RST));
  Multiplexer #(.width(24)) multiplexer_6 (
    .in0(Addr_I), .in1({24{1'b0}}), .out(multiplexer_6_out), .sel(inter));  // open: en
  Multiplexer multiplexer_7 (.in0(register_6_q), .in1(1'b0), .out(multiplexer_7_out), .sel(inter));  // open: en
  Register #(.width(1)) register_8 (.D(multiplexer_7_out), .en(HALT), .Q(rt_EX_MEM_O), .clk(clk), .clr(RST));
  Multiplexer #(.width(32)) multiplexer_8 (
    .in0(rs_I), .in1({32{1'b0}}), .out(multiplexer_8_out), .sel(inter));  // open: en
  Register #(.width(24)) register_9 (.D(multiplexer_6_out), .en(HALT), .Q(Addr_O), .clk(clk), .clr(RST));
  Register #(.width(32)) register_10 (.D(multiplexer_8_out), .en(HALT), .Q(rs_O), .clk(clk), .clr(RST));
  Register #(.width(32)) register_11 (.D(multiplexer_9_out), .en(HALT), .Q(Data_O), .clk(clk), .clr(RST));
  Multiplexer #(.width(32)) multiplexer_9 (
    .in0(Data_I), .in1({32{1'b0}}), .out(multiplexer_9_out), .sel(inter));  // open: en
  Register #(.width(32)) register_12 (.D(multiplexer_10_out), .en(HALT), .Q(oPC_O), .clk(clk), .clr(RST));
  Multiplexer #(.width(32)) multiplexer_10 (
    .in0(oPC_I), .in1({32{1'b0}}), .out(multiplexer_10_out), .sel(inter));  // open: en
  Multiplexer #(.width(32)) multiplexer_11 (
    .in0(Instruction_I), .in1({32{1'b0}}), .out(multiplexer_11_out), .sel(inter));  // open: en
  Register #(.width(32)) register_13 (.D(multiplexer_11_out), .en(HALT), .Q(Instruction_O), .clk(clk), .clr(RST));
  Multiplexer multiplexer_12 (.in0(ERET_I), .in1(1'b0), .out(multiplexer_12_out), .sel(inter));  // open: en
  Multiplexer #(.width(32)) multiplexer_13 (
    .in0(RES_I), .in1({32{1'b0}}), .out(multiplexer_13_out), .sel(inter));  // open: en
  Register #(.width(32)) register_14 (.D(multiplexer_13_out), .en(HALT), .Q(RES_O), .clk(clk), .clr(RST));
  Register #(.width(1)) register_15 (.D(multiplexer_12_out), .en(HALT), .Q(ERET_O), .clk(clk), .clr(RST));
  Register #(.width(1)) register_16 (.D(EN_I), .Q(EN_O), .clk(clk), .clr(RST));  // open: en
endmodule

module MEM_WB (
  input  [3:0] WB_I,
  input  [31:0] Data_I,
  input  [31:0] RES_I,
  input  [31:0] Instruction_I,
  input  [31:0] oPC_I,
  input  HALT,
  input  EN_I,
  input  inter,
  input  clk,
  input  RST,
  input  ERET_I,
  output [3:0] WB_O,
  output [31:0] Instruction_O,
  output [31:0] oPC_O,
  output [31:0] Data_O,
  output [31:0] RES_O,
  output EN_O,
  output ERET_O
);

  wire multiplexer_7_out;
  wire [3:0] multiplexer_1_out;
  wire [4:0] multiplexer_2_out, multiplexer_3_out, rd_I, rd_O, rt_I, rt_O;
  wire [31:0] multiplexer_4_out, multiplexer_5_out, multiplexer_6_out, multiplexer_8_out;

  Multiplexer #(.width(4)) multiplexer_1 (.in0(WB_I), .in1(4'b0000), .out(multiplexer_1_out), .sel(inter));  // open: en
  Register #(.width(4)) register_1 (.D(multiplexer_1_out), .en(HALT), .Q(WB_O), .clk(clk), .clr(RST));
  Multiplexer #(.width(5)) multiplexer_2 (
    .in0(rt_I), .in1({5{1'b0}}), .out(multiplexer_2_out), .sel(inter));  // open: en
  Register #(.width(5)) register_2 (.D(multiplexer_2_out), .en(HALT), .Q(rt_O), .clk(clk), .clr(RST));
  Register #(.width(5)) register_3 (.D(multiplexer_3_out), .en(HALT), .Q(rd_O), .clk(clk), .clr(RST));
  Multiplexer #(.width(5)) multiplexer_3 (
    .in0(rd_I), .in1({5{1'b0}}), .out(multiplexer_3_out), .sel(inter));  // open: en
  Register #(.width(32)) register_4 (.D(multiplexer_4_out), .en(HALT), .Q(Data_O), .clk(clk), .clr(RST));
  Multiplexer #(.width(32)) multiplexer_4 (
    .in0(Data_I), .in1({32{1'b0}}), .out(multiplexer_4_out), .sel(inter));  // open: en
  Register #(.width(32)) register_5 (.D(multiplexer_5_out), .en(HALT), .Q(Instruction_O), .clk(clk), .clr(RST));
  Multiplexer #(.width(32)) multiplexer_5 (
    .in0(Instruction_I), .in1({32{1'b0}}), .out(multiplexer_5_out), .sel(inter));  // open: en
  Multiplexer #(.width(32)) multiplexer_6 (
    .in0(RES_I), .in1({32{1'b0}}), .out(multiplexer_6_out), .sel(inter));  // open: en
  Register #(.width(32)) register_6 (.D(multiplexer_6_out), .en(HALT), .Q(RES_O), .clk(clk), .clr(RST));
  Multiplexer multiplexer_7 (.in0(EN_I), .in1(1'b0), .out(multiplexer_7_out), .sel(inter));  // open: en
  Register #(.width(32)) register_7 (.D(multiplexer_8_out), .en(HALT), .Q(oPC_O), .clk(clk), .clr(RST));
  Multiplexer #(.width(32)) multiplexer_8 (
    .in0(oPC_I), .in1({32{1'b0}}), .out(multiplexer_8_out), .sel(inter));  // open: en
  Register #(.width(1)) register_8 (.D(multiplexer_7_out), .Q(EN_O), .clk(clk), .clr(RST));  // open: en
  Multiplexer multiplexer_9 ();  // open: in0, in1, out, sel, en
  Register #(.width(1)) register_9 (.D(ERET_I), .en(HALT), .Q(ERET_O), .clk(clk), .clr(RST));
endmodule

module data_confilct (
  input  in_1,
  input  in_2,
  input  [31:0] Instruction_ID,
  input  [31:0] Instruction_EX,
  input  [31:0] Instruction_MEM,
  input  [2:0] src_reg_ID,
  input  [2:0] des_reg_EX,
  input  [2:0] des_reg_MEM,
  input  rW,
  output stall,
  output rs_EX_MEM,
  output rt_EX_MEM,
  output rs_EX_WB,
  output rt_EX_WB
);

  wire and_11_out, and_12_out, and_14_out, and_25_out, comparator_1_eq, comparator_2_eq, comparator_3_eq,
       comparator_4_eq, comparator_5_eq, comparator_6_eq, comparator_7_eq, comparator_8_eq, comparator_9_eq,
       comparator_10_eq, comparator_11_eq, comparator_12_eq, comparator_13_eq, comparator_14_eq,
       comparator_15_eq, comparator_16_eq, comparator_17_eq, comparator_18_eq, comparator_19_eq,
       comparator_20_eq, comparator_21_eq, comparator_22_eq, confilct2, not_1_out, not_2_out, or_1_out,
       or_2_out, or_3_out, or_4_out, or_5_out, or_6_out, rs_EX_MEM_1, rs_EX_MEM_2, rs_EX_MEM_3, rs_EX_MEM_4,
       rs_EX_MEM_5, rs_EX_WB_1, rs_EX_WB_2, rs_EX_WB_3, rs_EX_WB_4, rs_EX_WB_5, rt_EX_MEM_1, rt_EX_MEM_2,
       rt_EX_MEM_3, rt_EX_MEM_4, rt_EX_MEM_5, rt_EX_WB_1, rt_EX_WB_2, rt_EX_WB_3, rt_EX_WB_4, rt_EX_WB_5;

  Comparator #(.width(5)) comparator_1 (
    .a(Instruction_ID[25:21]), .b(Instruction_EX[20:16]), .eq(comparator_1_eq));  // open: gt, lt
  Comparator #(.width(5)) comparator_2 (
    .a(Instruction_ID[25:21]), .b(Instruction_EX[15:11]), .eq(comparator_2_eq));  // open: gt, lt
  Comparator #(.width(5)) comparator_3 (
    .a(Instruction_ID[25:21]), .b({5{1'b1}}), .eq(comparator_3_eq));  // open: gt, lt
  Comparator #(.width(5)) comparator_4 (
    .a(Instruction_ID[20:16]), .b(Instruction_EX[20:16]), .eq(comparator_4_eq));  // open: gt, lt
  Comparator #(.width(5)) comparator_5 (
    .a(Instruction_ID[20:16]), .b(Instruction_EX[15:11]), .eq(comparator_5_eq));  // open: gt, lt
  Comparator #(.width(5)) comparator_6 (
    .a(Instruction_ID[20:16]), .b({5{1'b1}}), .eq(comparator_6_eq));  // open: gt, lt
  Comparator #(.width(5)) comparator_7 (.a(5'b00010), .b(Instruction_EX[20:16]), .eq(comparator_7_eq));  // open: gt, lt
  Comparator #(.width(5)) comparator_8 (.a(5'b00010), .b(Instruction_EX[15:11]), .eq(comparator_8_eq));  // open: gt, lt
  Comparator #(.width(5)) comparator_9 (.a(5'b00100), .b(Instruction_EX[20:16]), .eq(comparator_9_eq));  // open: gt, lt
  Comparator #(.width(5)) comparator_10 (
    .a(5'b00100), .b(Instruction_EX[15:11]), .eq(comparator_10_eq));  // open: gt, lt
  and and_1 (rs_EX_MEM_1, src_reg_ID[0], comparator_1_eq, des_reg_EX[0]);
  and and_2 (rs_EX_MEM_2, src_reg_ID[0], comparator_2_eq, des_reg_EX[1]);
  and and_3 (rs_EX_MEM_3, src_reg_ID[0], comparator_3_eq, des_reg_EX[2]);
  and and_4 (rt_EX_MEM_1, src_reg_ID[1], comparator_4_eq, des_reg_EX[0]);
  and and_5 (rt_EX_MEM_2, src_reg_ID[1], comparator_5_eq, des_reg_EX[1]);
  and and_6 (rt_EX_MEM_3, src_reg_ID[1], comparator_6_eq, des_reg_EX[2]);
  and and_7 (rs_EX_MEM_4, src_reg_ID[2], comparator_7_eq, des_reg_EX[0]);
  and and_8 (rs_EX_MEM_5, src_reg_ID[2], comparator_8_eq, des_reg_EX[1]);
  and and_9 (rt_EX_MEM_4, src_reg_ID[2], comparator_9_eq, des_reg_EX[0]);
  and and_10 (rt_EX_MEM_5, src_reg_ID[2], comparator_10_eq, des_reg_EX[1]);
  not not_1 (not_1_out, comparator_11_eq);
  Comparator #(.width(32)) comparator_11 (.a(Instruction_EX), .b({32{1'b0}}), .eq(comparator_11_eq));  // open: gt, lt
  or or_1 (or_1_out, rs_EX_MEM_1, rs_EX_MEM_2, rs_EX_MEM_3, rs_EX_MEM_4, rs_EX_MEM_5);
  or or_2 (or_2_out, rs_EX_WB_1, rs_EX_WB_2, rs_EX_WB_3, rs_EX_WB_4, rs_EX_WB_5);
  // Probe on Instruction_EX
  and and_11 (and_11_out, or_1_out, not_1_out, rW);
  Register #(.width(1)) register_1 (.D(and_11_out), .Q(rs_EX_MEM), .clk(in_1), .clr(in_2));  // open: en
  Register #(.width(1)) register_2 (.D(and_12_out), .Q(rs_EX_WB), .clk(in_1), .clr(in_2));  // open: en
  and and_12 (and_12_out, or_2_out, not_2_out);
  or or_3 (or_3_out, rs_EX_MEM_1, rs_EX_MEM_2, rs_EX_MEM_3, rt_EX_MEM_1, rt_EX_MEM_2, rt_EX_MEM_3, rs_EX_MEM_4, rs_EX_MEM_5, rt_EX_MEM_4, rt_EX_MEM_5);
  and and_13 (stall, or_3_out, ~rW, not_1_out);  // AND_Gate
  // Probe on Instruction_MEM
  Comparator #(.width(5)) comparator_12 (
    .a(Instruction_ID[25:21]), .b(Instruction_MEM[20:16]), .eq(comparator_12_eq));  // open: gt, lt
  Comparator #(.width(5)) comparator_13 (
    .a(Instruction_ID[25:21]), .b(Instruction_MEM[15:11]), .eq(comparator_13_eq));  // open: gt, lt
  Comparator #(.width(5)) comparator_14 (
    .a(Instruction_ID[25:21]), .b({5{1'b1}}), .eq(comparator_14_eq));  // open: gt, lt
  Comparator #(.width(5)) comparator_15 (
    .a(Instruction_ID[20:16]), .b(Instruction_MEM[20:16]), .eq(comparator_15_eq));  // open: gt, lt
  Comparator #(.width(5)) comparator_16 (
    .a(Instruction_ID[20:16]), .b(Instruction_MEM[15:11]), .eq(comparator_16_eq));  // open: gt, lt
  Comparator #(.width(5)) comparator_17 (
    .a(Instruction_ID[20:16]), .b({5{1'b1}}), .eq(comparator_17_eq));  // open: gt, lt
  Comparator #(.width(5)) comparator_18 (
    .a(5'b00010), .b(Instruction_MEM[20:16]), .eq(comparator_18_eq));  // open: gt, lt
  Comparator #(.width(5)) comparator_19 (
    .a(5'b00010), .b(Instruction_MEM[15:11]), .eq(comparator_19_eq));  // open: gt, lt
  Comparator #(.width(5)) comparator_20 (
    .a(5'b00100), .b(Instruction_MEM[20:16]), .eq(comparator_20_eq));  // open: gt, lt
  Comparator #(.width(5)) comparator_21 (
    .a(5'b00100), .b(Instruction_MEM[15:11]), .eq(comparator_21_eq));  // open: gt, lt
  or or_4 (or_4_out, rt_EX_MEM_1, rt_EX_MEM_2, rt_EX_MEM_3, rt_EX_MEM_4, rt_EX_MEM_5);
  and and_14 (and_14_out, or_4_out, not_1_out, rW);
  or or_5 (or_5_out, rt_EX_WB_1, rt_EX_WB_2, rt_EX_WB_3, rt_EX_WB_4, rt_EX_WB_5);
  and and_15 (rs_EX_WB_1, src_reg_ID[0], comparator_12_eq, des_reg_MEM[0]);
  and and_16 (rs_EX_WB_2, src_reg_ID[0], comparator_13_eq, des_reg_MEM[1]);
  and and_17 (rs_EX_WB_3, src_reg_ID[0], comparator_14_eq, des_reg_MEM[2]);
  and and_18 (rt_EX_WB_1, src_reg_ID[1], comparator_15_eq, des_reg_MEM[0]);
  and and_19 (rt_EX_WB_2, src_reg_ID[1], comparator_16_eq, des_reg_MEM[1]);
  and and_20 (rt_EX_WB_3, src_reg_ID[1], comparator_17_eq, des_reg_MEM[2]);
  and and_21 (rs_EX_WB_4, src_reg_ID[2], comparator_18_eq, des_reg_MEM[0]);
  and and_22 (rs_EX_WB_5, src_reg_ID[2], comparator_19_eq, des_reg_MEM[1]);
  and and_23 (rt_EX_WB_4, src_reg_ID[2], comparator_20_eq, des_reg_MEM[0]);
  and and_24 (rt_EX_WB_5, src_reg_ID[2], comparator_21_eq, des_reg_MEM[1]);
  Comparator #(.width(32)) comparator_22 (.a(Instruction_MEM), .b({32{1'b0}}), .eq(comparator_22_eq));  // open: gt, lt
  Register #(.width(1)) register_3 (.D(and_14_out), .Q(rt_EX_MEM), .clk(in_1), .clr(in_2));  // open: en
  Register #(.width(1)) register_4 (.D(and_25_out), .Q(rt_EX_WB), .clk(in_1), .clr(in_2));  // open: en
  and and_25 (and_25_out, or_5_out, not_2_out);
  not not_2 (not_2_out, comparator_22_eq);
  or or_6 (or_6_out, rs_EX_WB_1, rs_EX_WB_2, rs_EX_WB_3, rt_EX_WB_1, rt_EX_WB_2, rt_EX_WB_3, rs_EX_WB_4, rs_EX_WB_5, rt_EX_WB_4, rt_EX_WB_5);
  and and_26 (confilct2, or_6_out, ~rW, not_2_out);  // AND_Gate

  // Other names for the same wires on the sheet: confilct1 = stall; des_rt = des_reg_EX[0]; des_rd = des_reg_EX[1];
  //   jal = des_reg_EX[2]; des_rt_2 = des_reg_MEM[0]; des_rd_2 = des_reg_MEM[1]; jal_2 = des_reg_MEM[2];
  //   Sp_EX[5:0] = Instruction_EX[5:0]; rd_EX[4:0] = Instruction_EX[15:11]; rt_EX[4:0] = Instruction_EX[20:16];
  //   rs_EX[4:0] = Instruction_EX[25:21]; Op_EX[5:0] = Instruction_EX[31:26]; Sp_ID[5:0] = Instruction_ID[5:0];
  //   rd_ID[4:0] = Instruction_ID[15:11]; rt_ID[4:0] = Instruction_ID[20:16]; rs_ID[4:0] = Instruction_ID[25:21];
  //   Op_ID[5:0] = Instruction_ID[31:26]; Sp_MEM[5:0] = Instruction_MEM[5:0]; rd_MEM[4:0] = Instruction_MEM[15:11];
  //   rt_MEM[4:0] = Instruction_MEM[20:16]; rs_MEM[4:0] = Instruction_MEM[25:21];
  //   Op_MEM[5:0] = Instruction_MEM[31:26]; RST = in_2; src_rs = src_reg_ID[0]; src_rt = src_reg_ID[1];
  //   sys = src_reg_ID[2]; T = in_1

  // Notes on the sheet:
  //   0->j
  //   1->rs
  //   2->rt
  //   3->rs&rt
  //   4->sys->2&4
  //   0->non
  //   1->rt
  //   2->rd
  //   3->$31
endmodule

module inter_signal (
  input  T,
  input  IR,
  input  W,
  output IR_LED,
  output IR_O
);

  wire and_1_out, d_ff_1_q, or_2_out;

  D_Flip_Flop d_ff_1 (.clk(IR), .D(1'b1), .Q(d_ff_1_q), .reset(IR_O));  // open: Qn, preset, en
  or or_1 (IR_LED, IR_O, d_ff_1_q);
  or or_2 (or_2_out, d_ff_1_q, IR_O);
  D_Flip_Flop d_ff_2 (.clk(T), .D(and_1_out), .Q(IR_O));  // open: Qn, preset, en, reset
  and and_1 (and_1_out, or_2_out, ~W);  // AND_Gate
endmodule

module PRI (
  input  IR1,
  input  IR2,
  input  IR3,
  output IR,
  output [1:0] inter_sel
);

  Priority_Encoder #(.select(2)) priority_encoder_1 (
    .in0(1'b1), .in1(IR1), .in2(IR2), .in3(IR3), .out(inter_sel));  // open: gs, en_out, en_in
  or or_1 (IR, IR1, IR2, IR3);
endmodule
