// Logisim project cpu_husixu_flow.circ as structural Verilog: 11 circuits, main circuit cpu
module cpu (
);

  wire BGTZ, controller_1_out_6, controller_1_out_8, controller_1_out_9, controller_1_out_12, ex_mem_1_en_o,
       ex_mem_1_memw_o, id_ex_1_memw_o, IR1, IR2, IR3, J_JAL, mem_wb_1_en_o, register_1_q, RST,
       syscall_1_out_6, T, W1, W2, W3;
  wire [1:0] controller_1_out_4, controller_1_out_7, id_ex_1_alux_o;
  wire [2:0] controller_1_out_5, id_ex_1_aluy_o;
  wire [3:0] controller_1_out_3, ex_mem_1_wb_o, id_ex_1_aluop_o, id_ex_1_wb, mem_wb_1_wb_o;
  wire [4:0] ex_mem_1_rd_o, ex_mem_1_rt_o, id_ex_1_rd_o, id_ex_1_rt_o, mem_wb_1_rd_o, mem_wb_1_rt_o;
  wire [15:0] \load_use次数 , \总周期数 , \插入气泡数 , \无条件分支指令数 , \有条件分支成功跳转 ;
  wire [23:0] ex_mem_1_addr_o, pc_1_out_13;
  wire [31:0] adder_1_out, alu_1_result, alui_1_out_7, alui_1_out_8, ex_mem_1_data_o, ex_mem_1_res_o,
       id_ex_1_instruction_o, id_ex_1_opc_o, id_ex_1_rs_o, id_ex_1_rt_o_2, if_id_1_data_o, if_id_1_opc_o,
       mem_wb_1_data_o, mem_wb_1_res_o, mips_ram_1_p7, pc_1_out_12, reg_file_1_rf_d1, reg_file_1_rf_d2,
       rom_1_data, shifter_1_out, SyscallOut;

  Button \u_总复位  (.out(RST));
  Button _1 (.out(IR1));
  Button _2 (.out(IR2));
  Button _3 (.out(IR3));
  PC pc_1 (
    .in_3({26{1'b0}}), .in_4({16{1'b0}}), .in_5(2'b00), .in_7(RST), .in_8(syscall_1_out_6), .in_9(T),
    .in_10(J_JAL), .out_12(pc_1_out_12), .out_13(pc_1_out_13), .out_14(\总周期数 ), .in_11(BGTZ),
    .in_1(register_1_q));  // open: in_2, in_6, out_15, out_16, out_17
  Clock clock_1 (.out(T));
  LED led_1 (.in(W1));
  LED led_2 (.in(W2));
  LED led_3 (.in(W3));
  Hex_Digit_Display hex_digit_display_1 (.value(SyscallOut[31:28]));  // open: dp
  IF_ID if_id_1 (
    .clk(T), .Data_I(rom_1_data), .RST(RST), .Data_O(if_id_1_data_o), .oPC_I(pc_1_out_12),
    .oPC_O(if_id_1_opc_o));
  ROM #(.addrWidth(24), .dataWidth(32)) rom_1 (.addr(pc_1_out_13), .data(rom_1_data));  // open: sel
  Hex_Digit_Display hex_digit_display_2 (.value(SyscallOut[27:24]));  // open: dp
  Hex_Digit_Display hex_digit_display_3 (.value(SyscallOut[23:20]));  // open: dp
  Hex_Digit_Display hex_digit_display_4 (.value(SyscallOut[19:16]));  // open: dp
  Hex_Digit_Display hex_digit_display_5 (.value(SyscallOut[15:12]));  // open: dp
  Controller controller_1 (
    .in_1(if_id_1_data_o[31:26]), .in_2(if_id_1_data_o[5:0]), .out_9(controller_1_out_9),
    .out_7(controller_1_out_7), .out_3(controller_1_out_3), .out_6(controller_1_out_6),
    .out_4(controller_1_out_4), .out_5(controller_1_out_5), .out_8(controller_1_out_8), .out_11(J_JAL),
    .out_14(BGTZ), .out_12(controller_1_out_12));  // open: out_10, out_13
  Reg_File reg_file_1 (
    .rs(if_id_1_data_o[25:21]), .rd(if_id_1_data_o[15:11]), .rt(if_id_1_data_o[20:16]), .clk(T),
    .rWE(mem_wb_1_wb_o[0]), .rW_2(mem_wb_1_wb_o[2:1]), .Syscall(controller_1_out_12), .RES(mem_wb_1_res_o),
    .Din(mem_wb_1_data_o), .RF_D1(reg_file_1_rf_d1), .RF_D2(reg_file_1_rf_d2), .rW(mem_wb_1_wb_o[3]),
    .rt_I(mem_wb_1_rt_o), .rd_I(mem_wb_1_rd_o));
  Hex_Digit_Display hex_digit_display_6 (.value(SyscallOut[11:8]));  // open: dp
  Hex_Digit_Display hex_digit_display_7 (.value(SyscallOut[7:4]));  // open: dp
  Hex_Digit_Display hex_digit_display_8 (.value(SyscallOut[3:0]));  // open: dp
  Syscall syscall_1 (
    .in_1(reg_file_1_rf_d1), .in_2(reg_file_1_rf_d2), .in_3(controller_1_out_12), .in_4(T), .in_5(RST),
    .out_6(syscall_1_out_6), .out_7(SyscallOut));
  // Probe on \总周期数 
  // Probe on \无条件分支指令数 
  // Probe on \有条件分支成功跳转 
  // Probe on \load_use次数 
  // Probe on \插入气泡数 
  ID_EX id_ex_1 (
    .clk(T), .RST(RST), .Instruction_I(if_id_1_data_o), .syscall_I(controller_1_out_12),
    .rW_I_2(controller_1_out_7), .AluX_I(controller_1_out_4), .rWE_I(controller_1_out_6),
    .AluY_I(controller_1_out_5), .MemW_I(controller_1_out_9), .oPC_I(if_id_1_opc_o), .MemW_O(id_ex_1_memw_o),
    .AluX_O(id_ex_1_alux_o), .AluY_O(id_ex_1_aluy_o), .WB(id_ex_1_wb), .oPC_O(id_ex_1_opc_o),
    .Instruction_O(id_ex_1_instruction_o), .rW_I(controller_1_out_8), .AluOp_I(controller_1_out_3),
    .AluOp_O(id_ex_1_aluop_o), .rd_I(if_id_1_data_o[15:11]), .rt_I_2(if_id_1_data_o[20:16]),
    .rd_O(id_ex_1_rd_o), .rt_O(id_ex_1_rt_o), .rs_I(reg_file_1_rf_d1), .rt_I(reg_file_1_rf_d2),
    .rs_O(id_ex_1_rs_o), .rt_O_2(id_ex_1_rt_o_2));  // open: EN_I, EN_O
  AluI alui_1 (
    .in_3(id_ex_1_instruction_o), .in_1(id_ex_1_alux_o), .in_2(id_ex_1_aluy_o), .in_4(id_ex_1_rs_o),
    .in_5(id_ex_1_rt_o_2), .in_6(id_ex_1_opc_o), .out_7(alui_1_out_7), .out_8(alui_1_out_8));
  Alu alu_1 (
    .X(alui_1_out_7), .Y(alui_1_out_8), .AluOP(id_ex_1_aluop_o), .Result(alu_1_result));  // open: Signed_Overflow, UnSigned_Overflow, Equal, Result_2
  Adder #(.width(32)) adder_1 (
    .a(id_ex_1_rs_o), .b({{16{1'b0}}, id_ex_1_instruction_o[15:0]}), .out(adder_1_out));  // open: cin, cout
  Shifter #(.width(32), .shift("lr")) shifter_1 (.in(adder_1_out), .\dist (5'b00010), .out(shifter_1_out));
  EX_MEM ex_mem_1 (
    .clk(T), .RST(RST), .Addr_I(shifter_1_out[23:0]), .Data_I(id_ex_1_rt_o_2), .Addr_O(ex_mem_1_addr_o),
    .Data_O(ex_mem_1_data_o), .MemW_O(ex_mem_1_memw_o), .WB_O(ex_mem_1_wb_o), .MemW_I(id_ex_1_memw_o),
    .WB_I(id_ex_1_wb), .RES_I(alu_1_result), .RES_O(ex_mem_1_res_o), .EN_I(syscall_1_out_6),
    .EN_O(ex_mem_1_en_o), .rt_I(id_ex_1_rt_o), .rd_I(id_ex_1_rd_o), .rt_O(ex_mem_1_rt_o), .rd_O(ex_mem_1_rd_o));
  // MIPS_RAM mips_ram_1: pin names not known; wires that end beside it: ex_mem_1_addr_o, ex_mem_1_data_o, ex_mem_1_memw_o, T, 1'b1, RST, mips_ram_1_p7
  MEM_WB mem_wb_1 (
    .clk(T), .RST(RST), .WB_I(ex_mem_1_wb_o), .Data_I(mips_ram_1_p7), .WB_O(mem_wb_1_wb_o),
    .Data_O(mem_wb_1_data_o), .RES_I(ex_mem_1_res_o), .RES_O(mem_wb_1_res_o), .EN_O(mem_wb_1_en_o),
    .EN_I(ex_mem_1_en_o), .rt_I(ex_mem_1_rt_o), .rd_I(ex_mem_1_rd_o), .rt_O(mem_wb_1_rt_o),
    .rd_O(mem_wb_1_rd_o));
  Register #(.width(1)) register_1 (.D(mem_wb_1_en_o), .Q(register_1_q), .clk(T), .clr(RST));  // open: en

  // Notes on the sheet:
  //   中断源
  //   中断等待指示
  //   数码管输出应该用寄存器锁存，否则显示数据只能一闪而过
  //   contents of rom_1 (hex, n*v repeats v):
  //   20100000 20110000 20120000 20130000 36100000 36310001 36520002 36730003 ae100000 ae110004 ae120008
  //   ae13000c 2002000a 20110000 20120000 20130000 c
  //   可以通过项目增加Logisim库的方式将前几次实验完成的电路作为子电路引入到本电路中使用
  //   数码管输出
  //   总复位信号应将除ROM以外所有存储组件全部清零
  //   Immi
endmodule

module Controller (
  input  [5:0] in_1,
  input  [5:0] in_2,
  output [3:0] out_3,
  output [1:0] out_4,
  output [2:0] out_5,
  output out_6,
  output [1:0] out_7,
  output out_8,
  output out_9,
  output [1:0] out_10,
  output out_11,
  output out_12,
  output out_13,
  output out_14
);

  wire add, addi, addiu, addu, \and , and_1_out, and_2_out, and_3_out, and_4_out, and_5_out, and_6_out,
       and_7_out, and_12_out, andi, beq, bgtz_t, bne, j_t, jal, jr, lhu_t, lw, \nor , Op__0, \or , or_1_out,
       or_2_out, or_3_out, or_7_out, or_8_out, or_9_out, or_10_out, or_11_out, or_12_out, or_13_out, ori,
       priority_encoder_2_p2, priority_encoder_2_p4, priority_encoder_2_p5, sll, sllv, slt, slti, sltiu,
       sltu, sra, srl, srlv, sub, syscall;
  wire [3:0] priority_encoder_1_out, priority_encoder_2_p1;

  Comparator #(.width(6)) comparator_1 (.a(in_1), .b({6{1'b0}}), .eq(Op__0));  // open: gt, lt
  Comparator #(.width(6)) comparator_2 (.a(in_1), .b(6'b000100), .eq(beq));  // open: gt, lt
  Comparator #(.width(6)) comparator_3 (.a(in_1), .b(6'b000101), .eq(bne));  // open: gt, lt
  Comparator #(.width(6)) comparator_4 (.a(in_1), .b(6'b001010), .eq(slti));  // open: gt, lt
  Comparator #(.width(6)) comparator_5 (.a(in_1), .b(6'b001101), .eq(ori));  // open: gt, lt
  Comparator #(.width(6)) comparator_6 (.a(in_1), .b(6'b001100), .eq(andi));  // open: gt, lt
  Comparator #(.width(6)) comparator_7 (.a(in_1), .b(6'b001001), .eq(addiu));  // open: gt, lt
  Comparator #(.width(6)) comparator_8 (.a(in_1), .b(6'b001000), .eq(addi));  // open: gt, lt
  Comparator #(.width(6)) comparator_9 (.a(in_1), .b(6'b000010), .eq(j_t));  // open: gt, lt
  or or_1 (or_1_out, bgtz_t, slti);
  or or_2 (or_2_out, bne, beq);
  Comparator #(.width(6)) comparator_10 (.a(in_1), .b(6'b101011), .eq(out_9));  // open: gt, lt
  Comparator #(.width(6)) comparator_11 (.a(in_1), .b(6'b100011), .eq(lw));  // open: gt, lt
  Comparator #(.width(6)) comparator_12 (.a(in_1), .b(6'b000011), .eq(jal));  // open: gt, lt
  Comparator #(.width(6)) comparator_13 (.a(in_2), .b(6'b101011), .eq(sltu));  // open: gt, lt
  Comparator #(.width(6)) comparator_14 (.a(in_2), .b(6'b101010), .eq(slt));  // open: gt, lt
  Comparator #(.width(6)) comparator_15 (.a(in_2), .b(6'b100111), .eq(\nor ));  // open: gt, lt
  Comparator #(.width(6)) comparator_16 (.a(in_2), .b(6'b100101), .eq(\or ));  // open: gt, lt
  Comparator #(.width(6)) comparator_17 (.a(in_2), .b(6'b100100), .eq(\and ));  // open: gt, lt
  or or_3 (or_3_out, jal, addi, lw, out_9, addiu, lhu_t);
  Priority_Encoder #(.select(4)) priority_encoder_1 (
    .in5(or_3_out), .in7(andi), .in8(ori), .in11(or_1_out), .in12(sltiu), .in14(or_2_out),
    .out(priority_encoder_1_out));  // open: in0, in1, in2, in3, in4, in6, in9, in10, in13, in15, gs, en_out, en_in
  Comparator #(.width(6)) comparator_18 (.a(in_2), .b(6'b100010), .eq(sub));  // open: gt, lt
  Comparator #(.width(6)) comparator_19 (.a(in_2), .b(6'b100001), .eq(addu));  // open: gt, lt
  Comparator #(.width(6)) comparator_20 (.a(in_2), .b(6'b100000), .eq(add));  // open: gt, lt
  Comparator #(.width(6)) comparator_21 (.a(in_2), .b(6'b001100), .eq(syscall));  // open: gt, lt
  Comparator #(.width(6)) comparator_22 (.a(in_2), .b(6'b001000), .eq(jr));  // open: gt, lt
  Comparator #(.width(6)) comparator_23 (.a(in_2), .b(6'b000011), .eq(sra));  // open: gt, lt
  Comparator #(.width(6)) comparator_24 (.a(in_2), .b(6'b000010), .eq(srl));  // open: gt, lt
  Comparator #(.width(6)) comparator_25 (.a(in_2), .b({6{1'b0}}), .eq(sll));  // open: gt, lt
  Multiplexer #(.width(4)) multiplexer_1 (
    .in0(priority_encoder_1_out), .in1(priority_encoder_2_p1), .out(out_3), .sel(Op__0));  // open: en
  // Priority_Encoder #(.select(4)) priority_encoder_2: pin names not known; wires that end beside it: priority_encoder_2_p1, priority_encoder_2_p2, sra, priority_encoder_2_p4, priority_encoder_2_p5, sub, \and , \or , \nor , slt, sltu
  or or_4 (priority_encoder_2_p2, sll, sllv);
  or or_5 (priority_encoder_2_p5, add, addu);
  Multiplexer #(.select(2), .width(2)) multiplexer_2 (
    .in0(2'b10), .in1(2'b11), .in2(2'b00), .in3(2'b00), .out(out_7), .sel({Op__0, jal}));  // open: en
  or or_6 (priority_encoder_2_p4, srl, srlv);
  or or_7 (or_7_out, addiu, lw, addi, jal, ori, andi, lhu_t, slti);
  or or_8 (or_8_out, \nor , sub, \or , \and , slt, add, sllv, sra, addu, srl, sltu, sll, srlv);
  Multiplexer multiplexer_3 (.in0(or_7_out), .in1(or_8_out), .out(out_6), .sel(Op__0));  // open: en
  and and_1 (and_1_out, Op__0, jr);
  and and_2 (and_2_out, ~Op__0, beq);  // AND_Gate
  and and_3 (and_3_out, ~Op__0, bne);  // AND_Gate
  or or_9 (or_9_out, sra, srl, sllv, sll, srlv);
  or or_10 (or_10_out, slti, andi, ori, lw, out_9, lhu_t, addiu, addi);
  Comparator #(.width(6)) comparator_26 (.a(in_1), .b(6'b000111), .eq(bgtz_t));  // open: gt, lt
  Comparator #(.width(6)) comparator_27 (.a(in_2), .b(6'b000100), .eq(sllv));  // open: gt, lt
  or or_11 (or_11_out, jal, j_t);
  Priority_Encoder #(.select(2)) priority_encoder_3 (
    .in0(1'b1), .in1(and_1_out), .in2(and_2_out), .in3(and_3_out), .out(out_10));  // open: gs, en_out, en_in
  and and_4 (and_4_out, Op__0, or_9_out);
  and and_5 (and_5_out, jal, ~Op__0);  // AND_Gate
  and and_6 (and_6_out, ~Op__0, or_10_out);  // AND_Gate
  or or_12 (or_12_out, sllv, srlv);
  and and_7 (and_7_out, or_12_out, Op__0);
  and and_8 (out_11, or_11_out, ~Op__0);  // AND_Gate
  or or_13 (or_13_out, lhu_t, lw);
  Priority_Encoder #(.select(2)) priority_encoder_4 (
    .in0(1'b1), .in1(and_4_out), .in2(and_5_out), .out(out_4));  // open: in3, gs, en_out, en_in
  Priority_Encoder priority_encoder_5 (
    .in0(1'b1), .in1(and_4_out), .in2(and_6_out), .in3(and_5_out), .in4(and_7_out), .out(out_5));  // open: in5, in6, in7, en_in, gs, en_out
  Comparator #(.width(6)) comparator_28 (.a(in_1), .b(6'b100101), .eq(lhu_t));  // open: gt, lt
  Comparator #(.width(6)) comparator_29 (.a(in_2), .b(6'b000110), .eq(srlv));  // open: gt, lt
  and and_9 (out_14, bgtz_t, ~Op__0);  // AND_Gate
  and and_10 (out_12, syscall, Op__0);
  and and_11 (out_13, lhu_t, ~Op__0);  // AND_Gate
  and and_12 (and_12_out, or_13_out, ~Op__0);  // AND_Gate
  not not_1 (out_8, and_12_out);
  Decoder #(.select(5)) decoder_1 ();  // open: out0, out1, out2, out3, out4, out5, out6, out7, out8, out9, out10, out11, out12, out13, out14, out15, out16, out17, out18, out19, out20, out21, out22, out23, out24, out25, out26, out27, out28, out29, out30, out31, sel, en
  Decoder #(.select(5)) decoder_2 ();  // open: out0, out1, out2, out3, out4, out5, out6, out7, out8, out9, out10, out11, out12, out13, out14, out15, out16, out17, out18, out19, out20, out21, out22, out23, out24, out25, out26, out27, out28, out29, out30, out31, sel, en
  Decoder #(.select(5)) decoder_3 ();  // open: out0, out1, out2, out3, out4, out5, out6, out7, out8, out9, out10, out11, out12, out13, out14, out15, out16, out17, out18, out19, out20, out21, out22, out23, out24, out25, out26, out27, out28, out29, out30, out31, sel, en
  Decoder #(.select(5)) decoder_4 ();  // open: out0, out1, out2, out3, out4, out5, out6, out7, out8, out9, out10, out11, out12, out13, out14, out15, out16, out17, out18, out19, out20, out21, out22, out23, out24, out25, out26, out27, out28, out29, out30, out31, sel, en

  // Other names for the same wires on the sheet: AluOp[3:0] = out_3; AluX[1:0] = out_4; AluY[2:0] = out_5;
  //   BGTZ = out_14; J = out_11; LHU = out_13; Op[5:0] = in_1; PCW[1:0] = out_10; rW = out_8; rW_t[1:0] = out_7;
  //   rWE = out_6; Sp[5:0] = in_2; MemW = out_9; sw = out_9; Sys = out_12

  // Notes on the sheet:
  //   Instructions
  //   Reg Write Dst
  //   O->rD
  //   2->rT
  //   3->$31
  //   Alu Operator
  //   reg Write Enable
  //   RAM Write
  //   Branching
  //   0->PC++
  //   1->$rS
  //   2->beq
  //   3->bne
  //   J/JAL
  //   CCMB
  //   lbtz(CCMB)
  //   Syscall
  //   lbu(CCMB)
  //   Reg Write Src
  //   0->MemO
  //   1->AluR
  //   Alu Input
  //   0->rS(default)
  //   1->rT
  //   2->PC
  //   0->rT(default)
  //   1->sA
  //   2->Immi
  //   3->4
  //   4->rS(CCMB)
endmodule

module Alu (
  input  [31:0] X,
  input  [31:0] Y,
  input  [3:0] AluOP,
  output Signed_Overflow,
  output UnSigned_Overflow,
  output Equal,
  output [31:0] Result,
  output [31:0] Result_2
);

  wire OF1, OF2, UOF1, UOF2, xnor_1_out, xor_1_out, xor_2_out, xor_3_out;
  wire [0:0] R12, R13;
  wire [31:0] R1, R2, R3, R4, R5, R6, R7, R8, R9, R10, R11, R21, R22;

  // Probe on X
  // Probe on X
  // Probe on Y
  // Probe on Y
  Shifter #(.width(32)) shifter_1 (.in(X), .\dist (Y[4:0]), .out(R1));
  Shifter #(.width(32), .shift("ar")) shifter_2 (.in(X), .\dist (Y[4:0]), .out(R2));
  Shifter #(.width(32), .shift("lr")) shifter_3 (.in(X), .\dist (Y[4:0]), .out(R3));
  Multiplier #(.width(32)) multiplier_1 (.a(X), .b(Y), .out(R4), .cout(R21));  // open: cin
  Divider #(.width(32)) divider_1 (.a(X), .b(Y), .out(R5), .rem(R22));  // open: upper
  xnor xnor_1 (xnor_1_out, X[31], Y[31]);
  xor xor_1 (xor_1_out, Y[31], X[31]);
  // Probe on AluOP
  Adder #(.width(32)) adder_1 (.a(X), .b(Y), .out(R6), .cin(1'b0), .cout(UOF1));
  xor xor_2 (xor_2_out, Y[31], R6[31]);
  and and_1 (OF1, xnor_1_out, xor_2_out);
  Subtractor #(.width(32)) subtractor_1 (.a(X), .b(Y), .out(R7), .bin(1'b0), .bout(UOF2));
  xor xor_3 (xor_3_out, X[31], R7[31]);
  and and_2 (OF2, xor_1_out, xor_3_out);
  // Probe on Result
  // Probe on Result
  assign R8 = X & Y;  // AND_Gate and_3, 32 bits wide
  assign R9 = X | Y;  // OR_Gate or_1, 32 bits wide
  assign R10 = X ^ Y;  // XOR_Gate xor_4, 32 bits wide
  assign R11 = ~(X | Y);  // NOR_Gate nor_1, 32 bits wide
  Comparator #(.width(32)) comparator_1 (.a(X), .b(Y), .eq(Equal), .lt(R12[0]));  // open: gt
  Comparator #(.width(32), .mode("unsigned")) comparator_2 (.a(X), .b(Y), .lt(R13[0]));  // open: gt, eq
  // Probe on Result_2
  Multiplexer #(.select(4), .width(32)) multiplexer_1 (
    .in0(R1), .in1(R2), .in2(R3), .in3(R4), .in4(R5), .in5(R6), .in6(R7), .in7(R8), .in8(R9), .in9(R10),
    .in10(R11), .in11({{31{1'b0}}, R12[0]}), .in12({{31{1'b0}}, R13[0]}), .in13({32{1'b0}}),
    .in14({32{1'b0}}), .in15({32{1'b0}}), .out(Result), .sel(AluOP));  // open: en
  Multiplexer #(.select(4)) multiplexer_2 (
    .in0(1'b0), .in1(1'b0), .in2(1'b0), .in3(1'b0), .in4(1'b0), .in5(UOF1), .in6(UOF2), .in7(1'b0),
    .in8(1'b0), .in9(1'b0), .in10(1'b0), .in11(1'b0), .in12(1'b0), .in13(1'b0), .in14(1'b0), .in15(1'b0),
    .out(UnSigned_Overflow), .sel(AluOP));  // open: en
  Multiplexer #(.select(4), .width(32)) multiplexer_3 (
    .in0({32{1'b0}}), .in1({32{1'b0}}), .in2({32{1'b0}}), .in3(R21), .in4(R22), .in5({32{1'b0}}),
    .in6({32{1'b0}}), .in7({32{1'b0}}), .in8({32{1'b0}}), .in9({32{1'b0}}), .in10({32{1'b0}}),
    .in11({32{1'b0}}), .in12({32{1'b0}}), .in13({32{1'b0}}), .in14({32{1'b0}}), .in15({32{1'b0}}),
    .out(Result_2), .sel(AluOP));  // open: en
  Multiplexer #(.select(4)) multiplexer_4 (
    .in0(1'b0), .in1(1'b0), .in2(1'b0), .in3(1'b0), .in4(1'b0), .in5(OF1), .in6(OF2), .in7(1'b0), .in8(1'b0),
    .in9(1'b0), .in10(1'b0), .in11(1'b0), .in12(1'b0), .in13(1'b0), .in14(1'b0), .in15(1'b0),
    .out(Signed_Overflow), .sel(AluOP));  // open: en

  // Other names for the same wires on the sheet: OF = Signed_Overflow; Result2[31:0] = Result_2; S[3:0] = AluOP;
  //   UOF = UnSigned_Overflow

  // Notes on the sheet:
  //   不要改变此引脚区域内容，也不要改变ALU封装形式
  //   输入引脚
  //   请在下方利用上方输入输出引脚的隧道信号构建ALU电路，ctrl+d复制选择部件
  //   华中科技大学计算机学院 计算机组成原理，鸣谢加州大学伯克利CS61C课程
  //   输出引脚
  //   探测区域
endmodule

module PC (
  input  in_1,
  input  [31:0] in_2,
  input  [25:0] in_3,
  input  [15:0] in_4,
  input  [1:0] in_5,
  input  in_6,
  input  in_7,
  input  in_8,
  input  in_9,
  input  in_10,
  input  in_11,
  output [31:0] out_12,
  output [23:0] out_13,
  output [15:0] out_14,
  output [15:0] out_15,
  output [15:0] out_16,
  output [15:0] out_17
);

  wire and_2_out, and_3_out, and_4_out, and_5_out, and_6_out, and_7_out, CNT, comparator_1_gt,
       comparator_2_gt, incrementer_1_p1, JE, JN, JR, or_2_out, or_3_out, or_4_out;
  wire [1:1] and_1_out;
  wire [31:0] adder_1_out, incrementer_1_p2, multiplexer_1_out, multiplexer_2_out, multiplexer_3_out,
       multiplexer_4_out, PC_1, shifter_1_out, shifter_3_out, subtractor_1_out;
  wire [31:24] PC_q;

  Shifter #(.width(32), .shift("ar")) shifter_1 (.in({in_4, {16{1'b0}}}), .\dist (5'b01110), .out(shifter_1_out));
  Adder #(.width(32)) adder_1 (.a(out_12), .b(shifter_1_out), .out(adder_1_out));  // open: cin, cout
  Shifter #(.width(32), .shift("lr")) shifter_2 (.in(adder_1_out), .\dist (5'b00010));  // open: out
  Shifter #(.width(32), .shift("lr")) shifter_3 (.in(in_2), .\dist (5'b00010), .out(shifter_3_out));
  Multiplexer #(.width(32)) multiplexer_1 (
    .in0(PC_1), .in1(incrementer_1_p2), .out(multiplexer_1_out), .sel(in_6));  // open: en
  // Incrementer incrementer_1: pin names not known; wires that end beside it: incrementer_1_p1, incrementer_1_p2
  Multiplexer #(.width(32)) multiplexer_2 (
    .in0(incrementer_1_p2), .in1(PC_1), .out(multiplexer_2_out), .sel(in_6));  // open: en
  Multiplexer #(.select(2), .width(32)) multiplexer_3 (
    .in0(PC_1), .in1(shifter_3_out), .in2(multiplexer_1_out), .in3(multiplexer_2_out),
    .out(multiplexer_3_out), .sel(in_5));  // open: en
  Subtractor #(.width(32)) subtractor_1 (
    .a({{6{1'b0}}, in_3}), .b(32'hc00), .out(subtractor_1_out));  // open: bin, bout
  Comparator #(.width(32)) comparator_1 (.a(in_2), .b({32{1'b0}}), .gt(comparator_1_gt));  // open: eq, lt
  Multiplexer #(.select(2), .width(32)) multiplexer_4 (
    .in0(multiplexer_3_out), .in1(subtractor_1_out), .in2(incrementer_1_p2), .out(multiplexer_4_out),
    .sel({and_1_out[1], in_10}));  // open: in3, en
  and and_1 (and_1_out[1], comparator_1_gt, in_11);
  Register #(.width(32)) PC (.D(multiplexer_4_out), .en(in_8), .Q({PC_q, out_13}), .clk(in_9), .clr(in_7));
  Shifter #(.width(32)) shifter_4 (.in({PC_q, out_13}), .\dist (5'b00010), .out(out_12));
  // Incrementer incrementer_2: pin names not known; wires that end beside it: {PC_q, out_13}, PC_1
  or or_1 (CNT, in_8, in_1);
  Decoder #(.select(2)) decoder_1 (.out1(JR), .out2(JE), .out3(JN), .sel(in_5));  // open: out0, en
  Counter #(.width(16), .max('hffff)) counter_1 (
    .count(CNT), .Q(out_14), .clk(in_9), .clr(in_7));  // open: load, D, carry
  or or_2 (or_2_out, JN, in_11, JE);
  and and_2 (and_2_out, or_2_out, CNT);
  Comparator #(.width(32)) comparator_2 (.a(in_2), .b({32{1'b0}}), .gt(comparator_2_gt));  // open: eq, lt
  Counter #(.width(16), .max('hffff)) counter_2 (
    .count(and_2_out), .Q(out_16), .clk(in_9), .clr(in_7));  // open: load, D, carry
  and and_3 (and_3_out, comparator_2_gt, in_11);
  and and_4 (and_4_out, JN, ~in_6);  // AND_Gate
  and and_5 (and_5_out, in_6, JE);
  or or_3 (or_3_out, JR, in_10);
  Counter #(.width(16), .max('hffff)) counter_3 (
    .count(and_6_out), .Q(out_15), .clk(in_9), .clr(in_7));  // open: load, D, carry
  and and_6 (and_6_out, or_3_out, CNT);
  or or_4 (or_4_out, and_3_out, and_4_out, and_5_out);
  Counter #(.width(16), .max('hffff)) counter_4 (
    .count(and_7_out), .Q(out_17), .clk(in_9), .clr(in_7));  // open: load, D, carry
  and and_7 (and_7_out, or_4_out, CNT);

  // Other names for the same wires on the sheet: immi[15:0] = in_4; inst[25:0] = in_3; J = in_10; PC[23:0] = out_13;
  //   AluEq = in_6; BGTZ = in_11; EN = in_8; END = in_1; oPC[31:0] = out_12; PCW[1:0] = in_5; rS[31:0] = in_2;
  //   RST = in_7; T = in_9; 总周期数[15:0] = out_14; 无条件分支指令数[15:0] = out_15; 有条件分支成功跳转[15:0] = out_17;
  //   有条件分支指令数[15:0] = out_16
endmodule

module Syscall (
  input  [31:0] in_1,
  input  [31:0] in_2,
  input  in_3,
  input  in_4,
  input  in_5,
  output out_6,
  output [31:0] out_7
);

  wire and_1_out, and_2_out, comparator_1_eq, or_1_out, register_2_q;
  wire [31:0] multiplexer_1_out;

  Comparator #(.width(32)) comparator_1 (.a(in_1), .b(32'ha), .eq(comparator_1_eq));  // open: gt, lt
  or or_1 (or_1_out, register_2_q, and_1_out);
  and and_1 (and_1_out, in_3, comparator_1_eq);
  and and_2 (and_2_out, ~comparator_1_eq, in_3);  // AND_Gate
  Register #(.width(32)) register_1 (.D(multiplexer_1_out), .Q(out_7), .clk(in_4), .clr(in_5));  // open: en
  Multiplexer #(.width(32)) multiplexer_1 (
    .in0(out_7), .in1(in_2), .out(multiplexer_1_out), .sel(and_2_out));  // open: en
  Register #(.width(1)) register_2 (.D(or_1_out), .Q(register_2_q), .clk(in_4), .clr(in_5));  // open: en
  not not_1 (out_6, register_2_q);

  // Other names for the same wires on the sheet: EN = out_6; rS[31:0] = in_1; RST = in_5; rT[31:0] = in_2; Sys = in_3;
  //   SyscallOut[31:0] = out_7; T = in_4
endmodule

module AluI (
  input  [1:0] in_1,
  input  [2:0] in_2,
  input  [31:0] in_3,
  input  [31:0] in_4,
  input  [31:0] in_5,
  input  [31:0] in_6,
  output [31:0] out_7,
  output [31:0] out_8
);

  wire [31:0] shifter_1_out;

  Shifter #(.width(32), .shift("ar")) shifter_1 (.in({in_3[15:0], {16{1'b0}}}), .\dist (5'b10000), .out(shifter_1_out));
  Multiplexer #(.select(2), .width(32)) multiplexer_1 (
    .in0(in_4), .in1(in_5), .in2(in_6), .out(out_7), .sel(in_1));  // open: in3, en
  Multiplexer #(.select(3), .width(32)) multiplexer_2 (
    .in0(in_5), .in1({{27{1'b0}}, in_3[10:6]}), .in2(shifter_1_out), .in3(32'h4), .in4(in_4), .out(out_8),
    .sel(in_2));  // open: in5, in6, in7, en

  // Other names for the same wires on the sheet: Instruction[31:0] = in_3; AluX[1:0] = in_1; AluY[2:0] = in_2;
  //   oPC[31:0] = in_6; rS[31:0] = in_4; rT[31:0] = in_5; X[31:0] = out_7; Y[31:0] = out_8

  // Notes on the sheet:
  //   Immi
  //   sa
endmodule

module Reg_File (
  input  rW,
  input  rWE,
  input  [1:0] rW_2,
  input  Syscall,
  input  [31:0] RES,
  input  [31:0] Din,
  input  [4:0] rs,
  input  [4:0] rt,
  input  [4:0] rt_I,
  input  [4:0] rd,
  input  [4:0] rd_I,
  input  clk,
  output [31:0] RF_D1,
  output [31:0] RF_D2
);

  wire undriven;
  wire [4:0] multiplexer_2_out, multiplexer_3_out, multiplexer_4_out;
  wire [31:0] multiplexer_1_out;

  Multiplexer #(.width(32)) multiplexer_1 (.in0(Din), .in1(RES), .out(multiplexer_1_out), .sel(rW));  // open: en
  Multiplexer #(.select(2), .width(5)) multiplexer_2 (
    .in0(rd_I), .in2(rt_I), .in3({5{1'b1}}), .out(multiplexer_2_out), .sel(rW_2));  // open: in1, en
  Multiplexer #(.width(5)) multiplexer_3 (
    .in0(rt), .in1(5'b00100), .out(multiplexer_3_out), .sel(Syscall), .en(undriven));
  Multiplexer #(.width(5)) multiplexer_4 (
    .in0(rs), .in1(5'b00010), .out(multiplexer_4_out), .sel(Syscall), .en(undriven));
  // RegisterFile registerfile_1: pin names not known; wires that end beside it: multiplexer_1_out, clk, rWE, multiplexer_2_out, multiplexer_4_out, multiplexer_3_out, RF_D1, RF_D2

  // Other names for the same wires on the sheet: rW_t[1:0] = rW_2
endmodule

module ID_EX (
  input  [31:0] Instruction_I,
  input  [31:0] rs_I,
  input  [31:0] rt_I,
  input  [31:0] oPC_I,
  input  clk,
  input  RST,
  input  rW_I,
  input  [1:0] rW_I_2,
  input  rWE_I,
  input  syscall_I,
  input  MemW_I,
  input  EN_I,
  input  [4:0] rt_I_2,
  input  [4:0] rd_I,
  input  [1:0] AluX_I,
  input  [2:0] AluY_I,
  input  [3:0] AluOp_I,
  output [4:0] rt_O,
  output [4:0] rd_O,
  output [1:0] AluX_O,
  output [2:0] AluY_O,
  output [3:0] AluOp_O,
  output [31:0] Instruction_O,
  output [31:0] rs_O,
  output [31:0] rt_O_2,
  output [31:0] oPC_O,
  output MemW_O,
  output [3:0] WB,
  output EN_O
);

  wire syscall_O;
  wire [4:0] rs_I_t, rs_O_t;

  Register #(.width(5)) register_1 (.D(rs_I_t), .Q(rs_O_t), .clk(clk), .clr(RST));  // open: en
  Register #(.width(1)) register_2 (.D(syscall_I), .Q(syscall_O), .clk(clk), .clr(RST));  // open: en
  Register #(.width(32)) register_3 (.D(rs_I), .Q(rs_O), .clk(clk));  // open: en, clr
  Register #(.width(5)) register_4 (.D(rt_I_2), .Q(rt_O), .clk(clk), .clr(RST));  // open: en
  Register #(.width(5)) register_5 (.D(rt_I_2), .Q(rt_O), .clk(clk), .clr(RST));  // open: en
  Register #(.width(32)) register_6 (.D(rt_I), .Q(rt_O_2), .clk(clk), .clr(RST));  // open: en
  Register #(.width(5)) register_7 (.D(rd_I), .Q(rd_O), .clk(clk), .clr(RST));  // open: en
  Register #(.width(2)) register_8 (.D(AluX_I), .Q(AluX_O), .clk(clk), .clr(RST));  // open: en
  Register #(.width(5)) register_9 (.D(rd_I), .Q(rd_O), .clk(clk), .clr(RST));  // open: en
  Register #(.width(3)) register_10 (.D(AluY_I), .Q(AluY_O), .clk(clk), .clr(RST));  // open: en
  Register #(.width(1)) register_11 (.D(MemW_I), .Q(MemW_O), .clk(clk), .clr(RST));  // open: en
  Register #(.width(4)) register_12 (.D(AluOp_I), .Q(AluOp_O), .clk(clk), .clr(RST));  // open: en
  Register #(.width(32)) register_13 (.D(oPC_I), .Q(oPC_O), .clk(clk), .clr(RST));  // open: en
  Register #(.width(4)) register_14 (.D({rWE_I, rW_I_2, rW_I}), .Q(WB), .clk(clk), .clr(RST));  // open: en
  Register #(.width(32)) register_15 (.D(Instruction_I), .Q(Instruction_O), .clk(clk), .clr(RST));  // open: en
  Register #(.width(1)) register_16 (.D(EN_I), .Q(EN_O), .clk(clk), .clr(RST));  // open: en

  // Other names for the same wires on the sheet: rW_I_t[1:0] = rW_I_2; rt_I_t[4:0] = rt_I_2; rt_O_t[31:0] = rt_O_2
endmodule

module IF_ID (
  input  [31:0] Data_I,
  input  [31:0] oPC_I,
  input  clk,
  input  RST,
  output [31:0] Data_O,
  output [31:0] oPC_O
);

  Register #(.width(32)) register_1 (.D(Data_I), .Q(Data_O), .clk(clk), .clr(RST));  // open: en
  Register #(.width(32)) register_2 (.D(oPC_I), .Q(oPC_O), .clk(clk), .clr(RST));  // open: en
endmodule

module EX_MEM (
  input  MemW_I,
  input  [3:0] WB_I,
  input  [23:0] Addr_I,
  input  [31:0] Data_I,
  input  [31:0] RES_I,
  input  [4:0] rt_I,
  input  [4:0] rd_I,
  input  EN_I,
  input  clk,
  input  RST,
  output MemW_O,
  output [3:0] WB_O,
  output [23:0] Addr_O,
  output [31:0] Data_O,
  output [31:0] RES_O,
  output [4:0] rt_O,
  output [4:0] rd_O,
  output EN_O
);

  Register #(.width(1)) register_1 (.D(MemW_I), .Q(MemW_O), .clk(clk), .clr(RST));  // open: en
  Register #(.width(5)) register_2 (.D(rt_I), .Q(rt_O), .clk(clk), .clr(RST));  // open: en
  Register #(.width(5)) register_3 (.D(rd_I), .Q(rd_O), .clk(clk), .clr(RST));  // open: en
  Register #(.width(4)) register_4 (.D(WB_I), .Q(WB_O), .clk(clk), .clr(RST));  // open: en
  Register #(.width(24)) register_5 (.D(Addr_I), .Q(Addr_O), .clk(clk), .clr(RST));  // open: en
  Register #(.width(32)) register_6 (.D(Data_I), .Q(Data_O), .clk(clk), .clr(RST));  // open: en
  Register #(.width(32)) register_7 (.D(RES_I), .Q(RES_O), .clk(clk), .clr(RST));  // open: en
  Register #(.width(1)) register_8 (.D(EN_I), .Q(EN_O), .clk(clk), .clr(RST));  // open: en
endmodule

module MEM_WB (
  input  [3:0] WB_I,
  input  [31:0] Data_I,
  input  [31:0] RES_I,
  input  [4:0] rt_I,
  input  [4:0] rd_I,
  input  EN_I,
  input  clk,
  input  RST,
  output [3:0] WB_O,
  output [31:0] Data_O,
  output [31:0] RES_O,
  output EN_O,
  output [4:0] rt_O,
  output [4:0] rd_O
);

  Register #(.width(4)) register_1 (.D(WB_I), .Q(WB_O), .clk(clk), .clr(RST));  // open: en
  Register #(.width(5)) register_2 (.D(rt_I), .Q(rt_O), .clk(clk), .clr(RST));  // open: en
  Register #(.width(5)) register_3 (.D(rd_I), .Q(rd_O), .clk(clk), .clr(RST));  // open: en
  Register #(.width(32)) register_4 (.D(Data_I), .Q(Data_O), .clk(clk), .clr(RST));  // open: en
  Register #(.width(32)) register_5 (.D(RES_I), .Q(RES_O), .clk(clk), .clr(RST));  // open: en
  Register #(.width(1)) register_6 (.D(EN_I), .Q(EN_O), .clk(clk), .clr(RST));  // open: en
endmodule
