// Logisim project cpu_husixu_multi_intertupt.circ as structural Verilog: 9 circuits, main circuit cpu
module cpu (
);

  wire _ERET, _RST, alu_1_equal, and_7_out, and_8_out, and_9_out, comparator_1_eq, comparator_2_eq,
       comparator_3_eq, comparator_4_eq, comparator_5_eq, comparator_6_gt, controller_1_bgtz,
       controller_1_lhu, controller_1_out_6, controller_1_out_8, controller_1_out_9, controller_1_out_11,
       controller_1_out_12, controller_1_out_13, decoder_1_out1, decoder_1_out2, decoder_1_out3, ERET, GO,
       h_inter_l, IE, inter_signal_1_ir_o, inter_signal_2_ir_o, inter_signal_3_ir_o, interrupt, IR1, IR2,
       IR3, MFC0_EPC, MFC0_IE, MTC0_EPC, MTC0_IE, or_1_out, or_2_out, or_3_out, or_5_out, or_6_out, pri_1_ir,
       register_1_q, RST, RST1, RST2, RST3, syscall_1_out_6, T, W1, W2, W3;
  wire [1:0] controller_1_out_4, controller_1_out_7, controller_1_out_10, inter_sel, multiplexer_2_out,
       multiplexer_4_out, multiplexer_5_out, pri_1_inter_sel, register_4_q, register_5_q;
  wire [2:0] controller_1_out_5;
  wire [3:0] controller_1_out_3;
  wire [4:0] rom_1_data_2, rom_1_data_5;
  wire [5:0] rom_1_data_3, rom_1_data_4;
  wire [15:0] \load_use次数 , \总周期数 , \插入气泡数 , \无条件分支指令数 , \有条件分支成功跳转 , \有条件分支指令数 ;
  wire [20:6] rom_1_data;
  wire [23:0] EPC, EPC_O, inter_addr, multiplexer_1_out, NPC, pc_1_out_16;
  wire [31:0] adder_1_out, alu_1_result, alui_1_out_7, alui_1_out_8, bit_extender_1_out, mips_ram_1_p7,
       mips_ram_1_p8, multiplexer_6_out, multiplexer_7_out, pc_1_out_15, reg_file_1_rf_d1, reg_file_1_rf_d2,
       shifter_1_out, SyscallOut;
  wire [31:24] multiplexer_3_out;

  Button \u_总复位  (.out(RST));
  Clock clock_1 (.out(T));
  Button _1 (.out(IR1));
  Button _2 (.out(IR2));
  Button _3 (.out(IR3));
  inter_signal inter_signal_1 (.IR(IR1), .W(RST1), .IR_LED(W1), .T(T), .IR_O(inter_signal_1_ir_o));
  inter_signal inter_signal_2 (.IR(IR2), .W(RST2), .IR_LED(W2), .T(T), .IR_O(inter_signal_2_ir_o));
  inter_signal inter_signal_3 (.IR(IR3), .W(RST3), .IR_LED(W3), .T(T), .IR_O(inter_signal_3_ir_o));
  PC pc_1 (
    .in_3(reg_file_1_rf_d1),
    .in_4({rom_1_data_2, rom_1_data[20:16], rom_1_data_5, rom_1_data[10:6], rom_1_data_4}),
    .in_5({rom_1_data_5, rom_1_data[10:6], rom_1_data_4}), .in_6(controller_1_out_10), .in_7(alu_1_equal),
    .in_8(RST), .in_9(syscall_1_out_6), .in_10(T), .in_11(controller_1_out_11), .out_15(pc_1_out_15),
    .out_16(pc_1_out_16), .out_17(\总周期数 ), .out_18(\无条件分支指令数 ), .out_19(\有条件分支指令数 ), .out_20(\有条件分支成功跳转 ),
    .in_12(controller_1_bgtz), .interrupt(interrupt), .NPC(NPC), .EPC_O(EPC), .inter_addr(inter_addr),
    .ERET(ERET));
  Controller controller_1 (
    .in_1(rom_1_data_3), .in_2(rom_1_data_4), .out_9(controller_1_out_9), .out_7(controller_1_out_7),
    .out_3(controller_1_out_3), .out_6(controller_1_out_6), .out_4(controller_1_out_4),
    .out_5(controller_1_out_5), .out_8(controller_1_out_8), .out_10(controller_1_out_10),
    .out_11(controller_1_out_11), .LHU(controller_1_lhu), .out_12(controller_1_out_12),
    .out_13(controller_1_out_13), .BGTZ(controller_1_bgtz), .ERET(ERET));
  Button u_GO (.out(GO));
  LED led_1 (.in(W1));
  Hex_Digit_Display hex_digit_display_1 (.value(SyscallOut[31:28]));  // open: dp
  LED led_2 (.in(W2));
  LED led_3 (.in(W3));
  or or_1 (or_1_out, MTC0_IE, interrupt);
  or or_2 (or_2_out, interrupt, MFC0_IE, MTC0_IE, ERET);
  PRI pri_1 (
    .IR1(inter_signal_1_ir_o), .IR2(inter_signal_2_ir_o), .IR3(inter_signal_3_ir_o), .IR(pri_1_ir),
    .inter_sel(pri_1_inter_sel));
  Comparator #(.width(6)) comparator_1 (.a(rom_1_data_3), .b(6'b010000), .eq(comparator_1_eq));  // open: gt, lt
  Comparator #(.width(5)) comparator_2 (.a(rom_1_data_2), .b({5{1'b0}}), .eq(comparator_2_eq));  // open: gt, lt
  Comparator #(.width(5)) comparator_3 (.a(rom_1_data_2), .b(5'b00100), .eq(comparator_3_eq));  // open: gt, lt
  Comparator #(.width(5)) comparator_4 (.a(rom_1_data_5), .b({5{1'b1}}), .eq(comparator_4_eq));  // open: gt, lt
  Comparator #(.width(5)) comparator_5 (.a(rom_1_data_5), .b(5'b10001), .eq(comparator_5_eq));  // open: gt, lt
  and and_1 (MFC0_EPC, comparator_1_eq, comparator_2_eq, comparator_5_eq);
  Hex_Digit_Display hex_digit_display_2 (.value(SyscallOut[23:20]));  // open: dp
  Hex_Digit_Display hex_digit_display_3 (.value(SyscallOut[27:24]));  // open: dp
  not not_1 (IE, register_1_q);
  Register #(.width(1)) register_1 (.D(or_1_out), .en(or_2_out), .Q(register_1_q), .clk(T), .clr(RST));
  // Probe on pri_1_inter_sel
  Comparator #(.width(2), .mode("unsigned")) comparator_6 (
    .a(pri_1_inter_sel), .b(inter_sel), .gt(comparator_6_gt));  // open: eq, lt
  // Probe on EPC_O
  ROM #(.addrWidth(24), .dataWidth(32)) rom_1 (
    .addr(pc_1_out_16),
    .data({rom_1_data_3, rom_1_data_2, rom_1_data[20:16], rom_1_data_5, rom_1_data[10:6], rom_1_data_4}));  // open: sel
  and and_2 (MTC0_EPC, comparator_1_eq, comparator_3_eq, comparator_5_eq);
  and and_3 (MFC0_IE, comparator_1_eq, comparator_2_eq, comparator_4_eq);
  Hex_Digit_Display hex_digit_display_4 (.value(SyscallOut[19:16]));  // open: dp
  Hex_Digit_Display hex_digit_display_5 (.value(SyscallOut[15:12]));  // open: dp
  Comparator #(.width(2), .mode("unsigned")) comparator_7 (.a(pri_1_inter_sel), .b(2'b00), .eq(_RST));  // open: gt, lt
  and and_4 (h_inter_l, pri_1_ir, comparator_6_gt);
  and and_5 (interrupt, h_inter_l, IE);
  Reg_File reg_file_1 (
    .rs(rom_1_data_2), .rt(rom_1_data[20:16]), .rd(rom_1_data_5), .clk(T), .rW(controller_1_out_8),
    .rWE(controller_1_out_6), .rW_2(controller_1_out_7), .Syscall(controller_1_out_12), .RES(alu_1_result),
    .Din(multiplexer_6_out), .RF_D1(reg_file_1_rf_d1), .RF_D2(reg_file_1_rf_d2), .MFC0_EPC(MFC0_EPC),
    .EPC(EPC), .EPC_O(EPC_O), .MTC0_EPC(MTC0_EPC));
  and and_6 (MTC0_IE, comparator_1_eq, comparator_3_eq, comparator_4_eq);
  Hex_Digit_Display hex_digit_display_6 (.value(SyscallOut[7:4]));  // open: dp
  Hex_Digit_Display hex_digit_display_7 (.value(SyscallOut[11:8]));  // open: dp
  Multiplexer #(.width(24)) multiplexer_1 (
    .in0(NPC), .in1(EPC_O), .out(multiplexer_1_out), .sel(MTC0_EPC));  // open: en
  or or_3 (or_3_out, interrupt, MTC0_EPC);
  Hex_Digit_Display hex_digit_display_8 (.value(SyscallOut[3:0]));  // open: dp
  // Probe on EPC
  Register #(.width(24)) register_2 (.D(multiplexer_1_out), .en(or_3_out), .Q(EPC), .clk(T), .clr(RST));
  // OR_Gate or_4 has open pins: in0=interrupt, in1=_ERET, out=open
  Multiplexer #(.width(2)) multiplexer_2 (
    .in0(pri_1_inter_sel), .in1(register_4_q), .out(multiplexer_2_out), .sel(ERET));  // open: en
  or or_5 (or_5_out, interrupt, ERET);
  Multiplexer #(.select(2), .width(32)) multiplexer_3 (
    .in0({32{1'b0}}), .in1(32'h45), .in2(32'h7d), .in3(32'hb5), .out({multiplexer_3_out, inter_addr}),
    .sel(pri_1_inter_sel));  // open: en
  Syscall syscall_1 (
    .in_1(reg_file_1_rf_d1), .in_2(reg_file_1_rf_d2), .in_3(controller_1_out_13), .in_4(T), .in_5(RST),
    .out_6(syscall_1_out_6), .out_7(SyscallOut));
  AluI alui_1 (
    .in_3({rom_1_data_3, rom_1_data_2, rom_1_data[20:16], rom_1_data_5, rom_1_data[10:6], rom_1_data_4}),
    .in_1(controller_1_out_4), .in_2(controller_1_out_5), .in_4(reg_file_1_rf_d1), .in_5(reg_file_1_rf_d2),
    .in_6(pc_1_out_15), .out_7(alui_1_out_7), .out_8(alui_1_out_8));
  // Probe on \总周期数 
  // Probe on \无条件分支指令数 
  // Probe on \有条件分支成功跳转 
  // Probe on \load_use次数 
  // Probe on \插入气泡数 
  Multiplexer #(.width(2)) multiplexer_4 (
    .in0(inter_sel), .in1(register_5_q), .out(multiplexer_4_out), .sel(ERET));  // open: en
  // Probe on inter_sel
  Register #(.width(2)) register_3 (.D(multiplexer_2_out), .en(or_5_out), .Q(inter_sel), .clk(T));  // open: clr
  Adder #(.width(32)) adder_1 (
    .a(reg_file_1_rf_d1), .b({{16{1'b0}}, rom_1_data_5, rom_1_data[10:6], rom_1_data_4}), .out(adder_1_out));  // open: cin, cout
  Alu alu_1 (
    .X(alui_1_out_7), .Y(alui_1_out_8), .AluOP(controller_1_out_3), .Equal(alu_1_equal), .Result(alu_1_result));  // open: Signed_Overflow, UnSigned_Overflow, Result_2
  // Probe on register_4_q
  Register #(.width(2)) register_4 (.D(multiplexer_4_out), .en(or_6_out), .Q(register_4_q), .clk(T));  // open: clr
  Multiplexer #(.width(2)) multiplexer_5 (
    .in0(register_4_q), .in1(2'b00), .out(multiplexer_5_out), .sel(ERET));  // open: en
  or or_6 (or_6_out, interrupt, ERET);
  Shifter #(.width(32), .shift("lr")) shifter_1 (.in(adder_1_out), .\dist (5'b00010), .out(shifter_1_out));
  // Probe on alu_1_result
  // Probe on multiplexer_6_out
  // Probe on register_5_q
  Register #(.width(2)) register_5 (.D(multiplexer_5_out), .en(or_6_out), .Q(register_5_q), .clk(T));  // open: clr
  Decoder #(.select(2)) decoder_1 (
    .out1(decoder_1_out1), .out2(decoder_1_out2), .out3(decoder_1_out3), .sel(inter_sel));  // open: out0, en
  Multiplexer #(.width(32)) multiplexer_6 (
    .in0(mips_ram_1_p7), .in1(multiplexer_7_out), .out(multiplexer_6_out), .sel(controller_1_lhu));  // open: en
  and and_7 (and_7_out, decoder_1_out1, ERET);
  and and_8 (and_8_out, decoder_1_out2, ERET);
  and and_9 (and_9_out, decoder_1_out3, ERET);
  Register #(.width(1)) register_6 (.D(ERET), .Q(_ERET), .clk(T), .clr(RST));  // open: en
  // MIPS_RAM mips_ram_1: pin names not known; wires that end beside it: shifter_1_out[23:0], reg_file_1_rf_d2, controller_1_out_9, T, 1'b1, RST, mips_ram_1_p7, mips_ram_1_p8
  or or_7 (RST1, and_7_out, RST);
  or or_8 (RST2, and_8_out, RST);
  or or_9 (RST3, and_9_out, RST);
  assign bit_extender_1_out = {{16{1'b0}}, mips_ram_1_p7[15:0]};  // Bit_Extender bit_extender_1
  assign mips_ram_1_p8 = {{16{1'b0}}, mips_ram_1_p7[31:16]};  // Bit_Extender bit_extender_2
  Multiplexer #(.width(32)) multiplexer_7 (
    .in0(bit_extender_1_out), .in1(mips_ram_1_p8), .out(multiplexer_7_out), .sel(adder_1_out[1]));  // open: en

  // Notes on the sheet:
  //   中断源
  //   中断等待指示
  //   指令存储器
  //   contents of rom_1 (hex, n*v repeats v):
  //   20110200 20020022 112020 c 2231ffff 1620fffc 20020032 c 20080001 20090003 20110876 112020 20020022 c
  //   200b0008 1118804 1318804 112020 20020022 c 216bffff 1560fff9 20080001 20090003 20110876 118d00
  //   112020 20020022 c 200b0008 1118806 1318806 112020 20020022 c 216bffff 1560fff9 20090000 200b0010
  //   34118483 20120404 118c00 129400 36318281 22520404 ad310000 2328820 21290004 216bffff 1560fffb
  //   200b0020 20090000 95310000 112020 20020022 c 21290002 216bffff 1560fff9 2011000f 112020 20020022 c
  //   2231ffff 1e20fffb 2002000a c 2002000a c 40128800 1df020 341dfffc 27bdfffc afbe0000 27bdfffc afb00000
  //   27bdfffc afb20000 27bdfffc afb30000 27bdfffc afb40000 27bdfffc afb50000 27bdfffc afb60000 27bdfffc
  //   afa40000 27bdfffc afa20000 4012f800 20160001 20140006 20150001 168020 108100 2149825 132020 20020022
  //   c 1600fffa 295a022 1680fff7 4092f800 8fa20000 27bd0004 8fa40000 27bd0004 8fb60000 27bd0004 8fb50000
  //   27bd0004 8fb40000 27bd0004 8fb30000 27bd0004 8fb20000 27bd0004 8fb00000 27bd0004 8fbe0000 27bd0004
  //   1ee820 40928800 42000018 40128800 1df020 341deffc 27bdfffc afbe0000 27bdfffc afb00000 27bdfffc
  //   afb20000 27bdfffc afb30000 27bdfffc afb40000 27bdfffc afb50000 27bdfffc afb60000 27bdfffc afa40000
  //   27bdfffc afa20000 4012f800 20160002 20140006 20150001 168020 108100 2149825 132020 20020022 c
  //   1600fffa 295a022 1680fff7 4092f800 8fa20000 27bd0004 8fa40000 27bd0004 8fb60000 27bd0004 8fb50000
  //   27bd0004 8fb40000 27bd0004 8fb30000 27bd0004 8fb20000 27bd0004 8fb00000 27bd0004 8fbe0000 27bd0004
  //   1ee820 40928800 42000018 40128800 1df020 341ddffc 27bdfffc afbe0000 27bdfffc afb00000 27bdfffc
  //   afb20000 27bdfffc afb30000 27bdfffc afb40000 27bdfffc afb50000 27bdfffc afb60000 27bdfffc afa40000
  //   27bdfffc afa20000 4012f800 20160003 20140006 20150001 168020 108100 2149825 132020 20020022 c
  //   1600fffa 295a022 1680fff7 4092f800 8fa20000 27bd0004 8fa40000 27bd0004 8fb60000 27bd0004 8fb50000
  //   27bd0004 8fb40000 27bd0004 8fb30000 27bd0004 8fb20000 27bd0004 8fb00000 27bd0004 8fbe0000 27bd0004
  //   1ee820 40928800 42000018
  //   rD
  //   rS
  //   rT
  //   数码管输出
  //   $rS
  //   $rT
  //   Immi
  //   运行内存
endmodule

module Controller (
  input  [5:0] in_1,
  input  [5:0] in_2,
  output [3:0] out_3,
  output [1:0] out_4,
  output [2:0] out_5,
  output out_6,
  output [1:0] out_7,
  output out_8,
  output out_9,
  output [1:0] out_10,
  output out_11,
  output out_12,
  output out_13,
  output LHU,
  output BGTZ,
  output ERET
);

  wire add, addi, addiu, addu, \and , and_2_out, and_3_out, and_4_out, and_5_out, and_6_out, and_7_out,
       and_8_out, and_9_out, and_14_out, andi, beq, bgtz_t, bne, comparator_10_eq, comparator_11_eq, j_t,
       jal, jr, lhu_t, lw, \nor , Op__0, \or , or_1_out, or_2_out, or_3_out, or_7_out, or_8_out, or_9_out,
       or_10_out, or_11_out, or_12_out, or_13_out, or_14_out, ori, priority_encoder_2_p2,
       priority_encoder_2_p4, priority_encoder_2_p5, sll, sllv, slt, slti, sltiu, sltu, sra, srl, srlv, sub,
       syscall;
  wire [3:0] priority_encoder_1_out, priority_encoder_2_p1;

  Comparator #(.width(6)) comparator_1 (.a(in_1), .b({6{1'b0}}), .eq(Op__0));  // open: gt, lt
  Comparator #(.width(6)) comparator_2 (.a(in_1), .b(6'b000100), .eq(beq));  // open: gt, lt
  Comparator #(.width(6)) comparator_3 (.a(in_1), .b(6'b000101), .eq(bne));  // open: gt, lt
  Comparator #(.width(6)) comparator_4 (.a(in_1), .b(6'b001010), .eq(slti));  // open: gt, lt
  Comparator #(.width(6)) comparator_5 (.a(in_1), .b(6'b001101), .eq(ori));  // open: gt, lt
  Comparator #(.width(6)) comparator_6 (.a(in_1), .b(6'b001100), .eq(andi));  // open: gt, lt
  Comparator #(.width(6)) comparator_7 (.a(in_1), .b(6'b001001), .eq(addiu));  // open: gt, lt
  Comparator #(.width(6)) comparator_8 (.a(in_1), .b(6'b001000), .eq(addi));  // open: gt, lt
  Comparator #(.width(6)) comparator_9 (.a(in_1), .b(6'b000010), .eq(j_t));  // open: gt, lt
  or or_1 (or_1_out, bgtz_t, slti);
  or or_2 (or_2_out, bne, beq);
  Comparator #(.width(6)) comparator_10 (.a(in_1), .b(6'b010000), .eq(comparator_10_eq));  // open: gt, lt
  Comparator #(.width(6)) comparator_11 (.a(in_2), .b(6'b011000), .eq(comparator_11_eq));  // open: gt, lt
  Comparator #(.width(6)) comparator_12 (.a(in_1), .b(6'b101011), .eq(out_9));  // open: gt, lt
  Comparator #(.width(6)) comparator_13 (.a(in_1), .b(6'b100011), .eq(lw));  // open: gt, lt
  Comparator #(.width(6)) comparator_14 (.a(in_1), .b(6'b000011), .eq(jal));  // open: gt, lt
  Comparator #(.width(6)) comparator_15 (.a(in_2), .b(6'b101011), .eq(sltu));  // open: gt, lt
  Comparator #(.width(6)) comparator_16 (.a(in_2), .b(6'b101010), .eq(slt));  // open: gt, lt
  Comparator #(.width(6)) comparator_17 (.a(in_2), .b(6'b100111), .eq(\nor ));  // open: gt, lt
  Comparator #(.width(6)) comparator_18 (.a(in_2), .b(6'b100101), .eq(\or ));  // open: gt, lt
  Comparator #(.width(6)) comparator_19 (.a(in_2), .b(6'b100100), .eq(\and ));  // open: gt, lt
  or or_3 (or_3_out, jal, addi, lw, out_9, addiu, lhu_t);
  Priority_Encoder #(.select(4)) priority_encoder_1 (
    .in5(or_3_out), .in7(andi), .in8(ori), .in11(or_1_out), .in12(sltiu), .in14(or_2_out),
    .out(priority_encoder_1_out));  // open: in0, in1, in2, in3, in4, in6, in9, in10, in13, in15, gs, en_out, en_in
  and and_1 (ERET, comparator_10_eq, comparator_11_eq);
  Comparator #(.width(6)) comparator_20 (.a(in_2), .b(6'b100010), .eq(sub));  // open: gt, lt
  Comparator #(.width(6)) comparator_21 (.a(in_2), .b(6'b100001), .eq(addu));  // open: gt, lt
  Comparator #(.width(6)) comparator_22 (.a(in_2), .b(6'b100000), .eq(add));  // open: gt, lt
  Comparator #(.width(6)) comparator_23 (.a(in_2), .b(6'b001100), .eq(syscall));  // open: gt, lt
  Comparator #(.width(6)) comparator_24 (.a(in_2), .b(6'b001000), .eq(jr));  // open: gt, lt
  Comparator #(.width(6)) comparator_25 (.a(in_2), .b(6'b000011), .eq(sra));  // open: gt, lt
  Comparator #(.width(6)) comparator_26 (.a(in_2), .b(6'b000010), .eq(srl));  // open: gt, lt
  Comparator #(.width(6)) comparator_27 (.a(in_2), .b({6{1'b0}}), .eq(sll));  // open: gt, lt
  Multiplexer #(.width(4)) multiplexer_1 (
    .in0(priority_encoder_1_out), .in1(priority_encoder_2_p1), .out(out_3), .sel(Op__0));  // open: en
  // Priority_Encoder #(.select(4)) priority_encoder_2: pin names not known; wires that end beside it: priority_encoder_2_p1, priority_encoder_2_p2, sra, priority_encoder_2_p4, priority_encoder_2_p5, sub, \and , \or , \nor , slt, sltu
  or or_4 (priority_encoder_2_p2, sll, sllv);
  or or_5 (priority_encoder_2_p5, add, addu);
  Multiplexer #(.select(2), .width(2)) multiplexer_2 (
    .in0(2'b10), .in1(2'b11), .in2(2'b00), .in3(2'b00), .out(out_7), .sel({Op__0, jal}));  // open: en
  or or_6 (priority_encoder_2_p4, srl, srlv);
  or or_7 (or_7_out, addiu, lw, addi, jal, ori, andi, lhu_t, slti);
  or or_8 (or_8_out, \nor , sub, \or , \and , slt, add, sllv, sra, addu, srl, sltu, sll, srlv);
  Multiplexer multiplexer_3 (.in0(or_7_out), .in1(or_8_out), .out(out_6), .sel(Op__0));  // open: en
  and and_2 (and_2_out, Op__0, jr);
  and and_3 (and_3_out, ~Op__0, beq);  // AND_Gate
  and and_4 (and_4_out, ~Op__0, bne);  // AND_Gate
  or or_9 (or_9_out, sra, srl, sllv, sll, srlv);
  or or_10 (or_10_out, slti, lw, out_9, addiu, lhu_t, addi);
  or or_11 (or_11_out, andi, ori);
  Comparator #(.width(6)) comparator_28 (.a(in_1), .b(6'b000111), .eq(bgtz_t));  // open: gt, lt
  Comparator #(.width(6)) comparator_29 (.a(in_2), .b(6'b000100), .eq(sllv));  // open: gt, lt
  or or_12 (or_12_out, jal, j_t);
  Priority_Encoder #(.select(2)) priority_encoder_3 (
    .in0(1'b1), .in1(and_2_out), .in2(and_3_out), .in3(and_4_out), .out(out_10));  // open: gs, en_out, en_in
  and and_5 (and_5_out, Op__0, or_9_out);
  and and_6 (and_6_out, jal, ~Op__0);  // AND_Gate
  and and_7 (and_7_out, ~Op__0, or_10_out);  // AND_Gate
  and and_8 (and_8_out, ~Op__0, or_11_out);  // AND_Gate
  or or_13 (or_13_out, sllv, srlv);
  and and_9 (and_9_out, or_13_out, Op__0);
  and and_10 (out_11, or_12_out, ~Op__0);  // AND_Gate
  or or_14 (or_14_out, lhu_t, lw);
  Priority_Encoder #(.select(2)) priority_encoder_4 (
    .in0(1'b1), .in1(and_5_out), .in2(and_6_out), .out(out_4));  // open: in3, gs, en_out, en_in
  Priority_Encoder priority_encoder_5 (
    .in0(1'b1), .in1(and_5_out), .in2(and_7_out), .in3(and_8_out), .in4(and_6_out), .in5(and_9_out),
    .out(out_5));  // open: in6, in7, en_in, gs, en_out
  Comparator #(.width(6)) comparator_30 (.a(in_1), .b(6'b100101), .eq(lhu_t));  // open: gt, lt
  Comparator #(.width(6)) comparator_31 (.a(in_2), .b(6'b000110), .eq(srlv));  // open: gt, lt
  and and_11 (BGTZ, bgtz_t, ~Op__0);  // AND_Gate
  and and_12 (out_12, syscall, Op__0);
  and and_13 (LHU, lhu_t, ~Op__0);  // AND_Gate
  and and_14 (and_14_out, or_14_out, ~Op__0);  // AND_Gate
  not not_1 (out_8, and_14_out);
  Decoder #(.select(5)) decoder_1 ();  // open: out0, out1, out2, out3, out4, out5, out6, out7, out8, out9, out10, out11, out12, out13, out14, out15, out16, out17, out18, out19, out20, out21, out22, out23, out24, out25, out26, out27, out28, out29, out30, out31, sel, en
  Decoder #(.select(5)) decoder_2 ();  // open: out0, out1, out2, out3, out4, out5, out6, out7, out8, out9, out10, out11, out12, out13, out14, out15, out16, out17, out18, out19, out20, out21, out22, out23, out24, out25, out26, out27, out28, out29, out30, out31, sel, en
  Decoder #(.select(5)) decoder_3 ();  // open: out0, out1, out2, out3, out4, out5, out6, out7, out8, out9, out10, out11, out12, out13, out14, out15, out16, out17, out18, out19, out20, out21, out22, out23, out24, out25, out26, out27, out28, out29, out30, out31, sel, en
  Decoder #(.select(5)) decoder_4 ();  // open: out0, out1, out2, out3, out4, out5, out6, out7, out8, out9, out10, out11, out12, out13, out14, out15, out16, out17, out18, out19, out20, out21, out22, out23, out24, out25, out26, out27, out28, out29, out30, out31, sel, en

  assign out_13 = out_12;

  // Other names for the same wires on the sheet: AluOp[3:0] = out_3; AluX[1:0] = out_4; AluY[2:0] = out_5; J = out_11;
  //   Op[5:0] = in_1; PCW[1:0] = out_10; rW = out_8; rW_t[1:0] = out_7; rWE = out_6; Sp[5:0] = in_2; MemW = out_9;
  //   sw = out_9; Sys = out_12

  // Notes on the sheet:
  //   Instructions
  //   Reg Write Dst
  //   O->rD
  //   2->rT
  //   3->$31
  //   Alu Operator
  //   reg Write Enable
  //   RAM Write
  //   Branching
  //   0->PC++
  //   1->$rS
  //   2->beq
  //   3->bne
  //   J/JAL
  //   CCMB
  //   lbtz(CCMB)
  //   Syscall
  //   lbu(CCMB)
  //   Reg Write Src
  //   0->MemO
  //   1->AluR
  //   Alu Input
  //   0->rS(default)
  //   1->rT
  //   2->PC
  //   0->rT(default)
  //   1->sA
  //   2->Immi_S
  //   3->Immi_U
  //   4->4
  //   5->rS(CCMB)
endmodule

module Alu (
  input  [31:0] X,
  input  [31:0] Y,
  input  [3:0] AluOP,
  output Signed_Overflow,
  output UnSigned_Overflow,
  output Equal,
  output [31:0] Result,
  output [31:0] Result_2
);

  wire OF1, OF2, UOF1, UOF2, xnor_1_out, xor_1_out, xor_2_out, xor_3_out;
  wire [0:0] R12, R13;
  wire [31:0] R1, R2, R3, R4, R5, R6, R7, R8, R9, R10, R11, R21, R22;

  // Probe on X
  // Probe on X
  // Probe on Y
  // Probe on Y
  Shifter #(.width(32)) shifter_1 (.in(X), .\dist (Y[4:0]), .out(R1));
  Shifter #(.width(32), .shift("ar")) shifter_2 (.in(X), .\dist (Y[4:0]), .out(R2));
  Shifter #(.width(32), .shift("lr")) shifter_3 (.in(X), .\dist (Y[4:0]), .out(R3));
  Multiplier #(.width(32)) multiplier_1 (.a(X), .b(Y), .out(R4), .cout(R21));  // open: cin
  Divider #(.width(32)) divider_1 (.a(X), .b(Y), .out(R5), .rem(R22));  // open: upper
  xnor xnor_1 (xnor_1_out, X[31], Y[31]);
  xor xor_1 (xor_1_out, Y[31], X[31]);
  // Probe on AluOP
  Adder #(.width(32)) adder_1 (.a(X), .b(Y), .out(R6), .cin(1'b0), .cout(UOF1));
  xor xor_2 (xor_2_out, Y[31], R6[31]);
  and and_1 (OF1, xnor_1_out, xor_2_out);
  Subtractor #(.width(32)) subtractor_1 (.a(X), .b(Y), .out(R7), .bin(1'b0), .bout(UOF2));
  xor xor_3 (xor_3_out, X[31], R7[31]);
  and and_2 (OF2, xor_1_out, xor_3_out);
  // Probe on Result
  // Probe on Result
  assign R8 = X & Y;  // AND_Gate and_3, 32 bits wide
  assign R9 = X | Y;  // OR_Gate or_1, 32 bits wide
  assign R10 = X ^ Y;  // XOR_Gate xor_4, 32 bits wide
  assign R11 = ~(X | Y);  // NOR_Gate nor_1, 32 bits wide
  Comparator #(.width(32)) comparator_1 (.a(X), .b(Y), .eq(Equal), .lt(R12[0]));  // open: gt
  Comparator #(.width(32), .mode("unsigned")) comparator_2 (.a(X), .b(Y), .lt(R13[0]));  // open: gt, eq
  // Probe on Result_2
  Multiplexer #(.select(4), .width(32)) multiplexer_1 (
    .in0(R1), .in1(R2), .in2(R3), .in3(R4), .in4(R5), .in5(R6), .in6(R7), .in7(R8), .in8(R9), .in9(R10),
    .in10(R11), .in11({{31{1'b0}}, R12[0]}), .in12({{31{1'b0}}, R13[0]}), .in13({32{1'b0}}),
    .in14({32{1'b0}}), .in15({32{1'b0}}), .out(Result), .sel(AluOP));  // open: en
  Multiplexer #(.select(4)) multiplexer_2 (
    .in0(1'b0), .in1(1'b0), .in2(1'b0), .in3(1'b0), .in4(1'b0), .in5(UOF1), .in6(UOF2), .in7(1'b0),
    .in8(1'b0), .in9(1'b0), .in10(1'b0), .in11(1'b0), .in12(1'b0), .in13(1'b0), .in14(1'b0), .in15(1'b0),
    .out(UnSigned_Overflow), .sel(AluOP));  // open: en
  Multiplexer #(.select(4), .width(32)) multiplexer_3 (
    .in0({32{1'b0}}), .in1({32{1'b0}}), .in2({32{1'b0}}), .in3(R21), .in4(R22), .in5({32{1'b0}}),
    .in6({32{1'b0}}), .in7({32{1'b0}}), .in8({32{1'b0}}), .in9({32{1'b0}}), .in10({32{1'b0}}),
    .in11({32{1'b0}}), .in12({32{1'b0}}), .in13({32{1'b0}}), .in14({32{1'b0}}), .in15({32{1'b0}}),
    .out(Result_2), .sel(AluOP));  // open: en
  Multiplexer #(.select(4)) multiplexer_4 (
    .in0(1'b0), .in1(1'b0), .in2(1'b0), .in3(1'b0), .in4(1'b0), .in5(OF1), .in6(OF2), .in7(1'b0), .in8(1'b0),
    .in9(1'b0), .in10(1'b0), .in11(1'b0), .in12(1'b0), .in13(1'b0), .in14(1'b0), .in15(1'b0),
    .out(Signed_Overflow), .sel(AluOP));  // open: en

  // Other names for the same wires on the sheet: OF = Signed_Overflow; Result2[31:0] = Result_2; S[3:0] = AluOP;
  //   UOF = UnSigned_Overflow

  // Notes on the sheet:
  //   不要改变此引脚区域内容，也不要改变ALU封装形式
  //   输入引脚
  //   请在下方利用上方输入输出引脚的隧道信号构建ALU电路，ctrl+d复制选择部件
  //   华中科技大学计算机学院 计算机组成原理，鸣谢加州大学伯克利CS61C课程
  //   输出引脚
  //   探测区域
endmodule

module PC (
  input  interrupt,
  input  ERET,
  input  [31:0] in_3,
  input  [25:0] in_4,
  input  [15:0] in_5,
  input  [1:0] in_6,
  input  in_7,
  input  in_8,
  input  in_9,
  input  in_10,
  input  in_11,
  input  in_12,
  input  [23:0] EPC_O,
  input  [23:0] inter_addr,
  output [31:0] out_15,
  output [23:0] out_16,
  output [15:0] out_17,
  output [15:0] out_18,
  output [15:0] out_19,
  output [15:0] out_20,
  output [23:0] NPC
);

  wire and_2_out, and_3_out, and_4_out, and_5_out, and_6_out, and_7_out, comparator_1_gt, comparator_2_gt,
       JE, JN, JR, or_1_out, or_2_out, or_3_out;
  wire [1:1] and_1_out;
  wire [31:0] adder_1_out, bit_extender_1_out, bit_extender_2_out, multiplexer_1_out, multiplexer_2_out,
       multiplexer_3_out, multiplexer_5_out, PC_1, shifter_1_out, shifter_3_out, subtractor_1_out, undriven;
  wire [31:24] multiplexer_4_out, PC_q;

  Adder #(.width(32)) adder_1 (.a(out_15), .b(shifter_1_out), .out(adder_1_out));  // open: cin, cout
  Shifter #(.width(32), .shift("ar")) shifter_1 (.in({in_5, {16{1'b0}}}), .\dist (5'b01110), .out(shifter_1_out));
  Shifter #(.width(32), .shift("lr")) shifter_2 (.in(adder_1_out), .\dist (5'b00010));  // open: out
  // Incrementer incrementer_1: pin names not known
  Multiplexer #(.width(32)) multiplexer_1 (
    .in0(undriven), .in1(PC_1), .out(multiplexer_1_out), .sel(in_7));  // open: en
  Shifter #(.width(32), .shift("lr")) shifter_3 (.in(in_3), .\dist (5'b00010), .out(shifter_3_out));
  Multiplexer #(.width(32)) multiplexer_2 (
    .in0(PC_1), .in1(undriven), .out(multiplexer_2_out), .sel(in_7));  // open: en
  Multiplexer #(.select(2), .width(32)) multiplexer_3 (
    .in0(PC_1), .in1(shifter_3_out), .in2(multiplexer_2_out), .in3(multiplexer_1_out),
    .out(multiplexer_3_out), .sel(in_6));  // open: en
  Multiplexer #(.select(2), .width(32)) multiplexer_4 (
    .in0(multiplexer_3_out), .in1(subtractor_1_out), .in2(undriven), .out({multiplexer_4_out, NPC}),
    .sel({and_1_out[1], in_11}));  // open: in3, en
  and and_1 (and_1_out[1], comparator_1_gt, in_12);
  Subtractor #(.width(32)) subtractor_1 (
    .a({{6{1'b0}}, in_4}), .b(32'hc00), .out(subtractor_1_out));  // open: bin, bout
  Comparator #(.width(32)) comparator_1 (.a(in_3), .b({32{1'b0}}), .gt(comparator_1_gt));  // open: eq, lt
  assign bit_extender_1_out = {{8{1'b0}}, inter_addr};  // Bit_Extender bit_extender_1
  assign bit_extender_2_out = {{8{1'b0}}, EPC_O};  // Bit_Extender bit_extender_2
  Multiplexer #(.select(2), .width(32)) multiplexer_5 (
    .in0({multiplexer_4_out, NPC}), .in1(bit_extender_1_out), .in2(bit_extender_2_out),
    .out(multiplexer_5_out), .sel({ERET, interrupt}));  // open: in3, en
  // Probe on multiplexer_5_out
  Register #(.width(32)) PC (.D(multiplexer_5_out), .en(in_9), .Q({PC_q, out_16}), .clk(in_10), .clr(in_8));
  // Probe on out_16
  Decoder #(.select(2)) decoder_1 (.out1(JR), .out2(JE), .out3(JN), .sel(in_6));  // open: out0, en
  Shifter #(.width(32)) shifter_4 (.in({PC_q, out_16}), .\dist (5'b00010), .out(out_15));
  // Incrementer incrementer_2: pin names not known; wires that end beside it: {PC_q, out_16}, PC_1
  Counter #(.width(16), .max('hffff)) counter_1 (
    .count(in_9), .Q(out_17), .clk(in_10), .clr(in_8));  // open: load, D, carry
  or or_1 (or_1_out, JN, in_12, JE);
  Counter #(.width(16), .max('hffff)) counter_2 (
    .count(and_2_out), .Q(out_19), .clk(in_10), .clr(in_8));  // open: load, D, carry
  and and_2 (and_2_out, or_1_out, in_9);
  and and_3 (and_3_out, comparator_2_gt, in_12);
  Comparator #(.width(32)) comparator_2 (.a(in_3), .b({32{1'b0}}), .gt(comparator_2_gt));  // open: eq, lt
  and and_4 (and_4_out, JN, ~in_7);  // AND_Gate
  and and_5 (and_5_out, in_7, JE);
  or or_2 (or_2_out, JR, in_11);
  and and_6 (and_6_out, or_2_out, in_9);
  or or_3 (or_3_out, and_3_out, and_4_out, and_5_out);
  and and_7 (and_7_out, or_3_out, in_9);
  Counter #(.width(16), .max('hffff)) counter_3 (
    .count(and_6_out), .Q(out_18), .clk(in_10), .clr(in_8));  // open: load, D, carry
  Counter #(.width(16), .max('hffff)) counter_4 (
    .count(and_7_out), .Q(out_20), .clk(in_10), .clr(in_8));  // open: load, D, carry

  // Other names for the same wires on the sheet: immi[15:0] = in_5; inst[25:0] = in_4; J = in_11; PC[23:0] = out_16;
  //   AluEq = in_7; BGTZ = in_12; EN = in_9; oPC[31:0] = out_15; PCW[1:0] = in_6; rS[31:0] = in_3; RST = in_8;
  //   T = in_10; 总周期数[15:0] = out_17; 无条件分支指令数[15:0] = out_18; 有条件分支成功跳转[15:0] = out_20; 有条件分支指令数[15:0] = out_19
endmodule

module Syscall (
  input  [31:0] in_1,
  input  [31:0] in_2,
  input  in_3,
  input  in_4,
  input  in_5,
  output out_6,
  output [31:0] out_7
);

  wire and_1_out, and_2_out, comparator_1_eq, not_1_out, or_1_out, register_1_q;
  wire [31:0] multiplexer_1_out;

  Comparator #(.width(32)) comparator_1 (.a(in_1), .b(32'h22), .eq(comparator_1_eq));  // open: gt, lt
  and and_1 (and_1_out, in_3, not_1_out);
  not not_1 (not_1_out, comparator_1_eq);
  and and_2 (and_2_out, ~not_1_out, in_3);  // AND_Gate
  Multiplexer #(.width(32)) multiplexer_1 (
    .in0(out_7), .in1(in_2), .out(multiplexer_1_out), .sel(and_2_out));  // open: en
  or or_1 (or_1_out, register_1_q, and_1_out);
  Register #(.width(1)) register_1 (.D(or_1_out), .Q(register_1_q), .clk(in_4), .clr(in_5));  // open: en
  not not_2 (out_6, register_1_q);
  Register #(.width(32)) register_2 (.D(multiplexer_1_out), .Q(out_7), .clk(in_4), .clr(in_5));  // open: en

  // Other names for the same wires on the sheet: EN = out_6; rS[31:0] = in_1; RST = in_5; rT[31:0] = in_2; Sys = in_3;
  //   SyscallOut[31:0] = out_7; T = in_4
endmodule

module AluI (
  input  [1:0] in_1,
  input  [2:0] in_2,
  input  [31:0] in_3,
  input  [31:0] in_4,
  input  [31:0] in_5,
  input  [31:0] in_6,
  output [31:0] out_7,
  output [31:0] out_8
);

  wire [31:0] shifter_1_out, shifter_2_out;

  Shifter #(.width(32), .shift("ar")) shifter_1 (.in({in_3[15:0], {16{1'b0}}}), .\dist (5'b10000), .out(shifter_1_out));
  Shifter #(.width(32), .shift("lr")) shifter_2 (.in({in_3[15:0], {16{1'b0}}}), .\dist (5'b10000), .out(shifter_2_out));
  Multiplexer #(.select(2), .width(32)) multiplexer_1 (
    .in0(in_4), .in1(in_5), .in2(in_6), .out(out_7), .sel(in_1));  // open: in3, en
  Multiplexer #(.select(3), .width(32)) multiplexer_2 (
    .in0(in_5), .in1({{27{1'b0}}, in_3[10:6]}), .in2(shifter_1_out), .in3(shifter_2_out), .in4(32'h4),
    .in5(in_4), .out(out_8), .sel(in_2));  // open: in6, in7, en

  // Other names for the same wires on the sheet: Instruction[31:0] = in_3; AluX[1:0] = in_1; AluY[2:0] = in_2;
  //   oPC[31:0] = in_6; rS[31:0] = in_4; rT[31:0] = in_5; X[31:0] = out_7; Y[31:0] = out_8

  // Notes on the sheet:
  //   Immi
  //   Immi
  //   sa
endmodule

module Reg_File (
  input  rW,
  input  rWE,
  input  [1:0] rW_2,
  input  Syscall,
  input  [23:0] EPC,
  input  [31:0] RES,
  input  [31:0] Din,
  input  [4:0] rs,
  input  MFC0_EPC,
  input  MTC0_EPC,
  input  [4:0] rt,
  input  [4:0] rd,
  input  clk,
  output [31:0] RF_D1,
  output [31:0] RF_D2,
  output [23:0] EPC_O
);

  wire or_1_out, undriven;
  wire [4:0] multiplexer_3_out, multiplexer_4_out, multiplexer_5_out, multiplexer_6_out, registerfile_1_p6;
  wire [31:0] bit_extender_1_out, multiplexer_1_out, multiplexer_2_out;

  // Probe on multiplexer_1_out
  Multiplexer #(.width(32)) multiplexer_1 (.in0(Din), .in1(RES), .out(multiplexer_1_out), .sel(rW));  // open: en
  assign bit_extender_1_out = {{8{1'b0}}, EPC};  // Bit_Extender bit_extender_1
  or or_1 (or_1_out, rWE, MFC0_EPC);
  Multiplexer #(.width(32)) multiplexer_2 (
    .in0(multiplexer_1_out), .in1(bit_extender_1_out), .out(multiplexer_2_out), .sel(MFC0_EPC));  // open: en
  Multiplexer #(.width(5)) multiplexer_3 (
    .in0(multiplexer_4_out), .in1(5'b10010), .out(multiplexer_3_out), .sel(MFC0_EPC));  // open: en
  Multiplexer #(.select(2), .width(5)) multiplexer_4 (
    .in0(rd), .in2(rt), .in3({5{1'b1}}), .out(multiplexer_4_out), .sel(rW_2));  // open: in1, en
  // Probe on multiplexer_3_out
  Multiplexer #(.width(5)) multiplexer_5 (
    .in0(rs), .in1(5'b00010), .out(multiplexer_5_out), .sel(Syscall), .en(undriven));
  Multiplexer #(.width(5)) multiplexer_6 (
    .in0(rt), .in1(5'b00100), .out(multiplexer_6_out), .sel(Syscall), .en(undriven));
  // RegisterFile registerfile_1: pin names not known; wires that end beside it: multiplexer_2_out, clk, or_1_out, multiplexer_3_out, multiplexer_5_out, registerfile_1_p6, RF_D1, {RF_D2[31:24], EPC_O}
  Multiplexer #(.width(5)) multiplexer_7 (
    .in0(multiplexer_6_out), .in1(5'b10010), .out(registerfile_1_p6), .sel(MTC0_EPC));  // open: en
  // Probe on EPC_O

  assign RF_D2[23:0] = EPC_O;

  // Other names for the same wires on the sheet: rW_t[1:0] = rW_2
endmodule

module inter_signal (
  input  T,
  input  IR,
  input  W,
  output IR_LED,
  output IR_O
);

  wire and_1_out, d_ff_1_q, or_2_out;

  D_Flip_Flop d_ff_1 (.clk(IR), .D(1'b1), .Q(d_ff_1_q), .reset(IR_O));  // open: Qn, preset, en
  or or_1 (IR_LED, IR_O, d_ff_1_q);
  or or_2 (or_2_out, d_ff_1_q, IR_O);
  D_Flip_Flop d_ff_2 (.clk(T), .D(and_1_out), .Q(IR_O));  // open: Qn, preset, en, reset
  and and_1 (and_1_out, or_2_out, ~W);  // AND_Gate
endmodule

module PRI (
  input  IR1,
  input  IR2,
  input  IR3,
  output IR,
  output [1:0] inter_sel
);

  Priority_Encoder #(.select(2)) priority_encoder_1 (
    .in0(1'b1), .in1(IR1), .in2(IR2), .in3(IR3), .out(inter_sel));  // open: gs, en_out, en_in
  or or_1 (IR, IR1, IR2, IR3);
endmodule
