// Logisim project cpu_husixu_redirect&pre.circ as structural Verilog: 14 circuits, main circuit cpu
module cpu (
);

  wire alu_1_equal, and_1_out, clear, controller_1_out_7, controller_1_out_9, controller_1_out_10,
       controller_1_out_12, controller_1_out_13, controller_1_out_14, controller_1_out_15,
       data_confilct_1_stall, ex_mem_1_en_o, ex_mem_1_lhu_o, ex_mem_1_memw_o, ex_mem_1_rs_ex_mem_o,
       ex_mem_1_rt_ex_mem_o, GO, HALT, hit_I, hit_O, hit_O_ID, id_ex_1_p22, id_ex_1_p29, id_ex_1_p31,
       id_ex_1_p37, id_ex_1_p41, if_id_1_pre_o, IR1, IR2, IR3, mem_wb_1_en_o, or_1_out, pre_EX, pre_J,
       rs_EX_MEM, rs_EX_WB, RST, rt_EX_MEM, rt_EX_WB, suc, T, W1, W2, W3, write;
  wire [1:0] controller_1_out_5, controller_1_out_8, controller_1_out_11, id_ex_1_p32, mem_wb_1_wb_o_2;
  wire [2:0] controller_1_des_reg, controller_1_out_6, controller_1_src_reg, ex_mem_1_des_reg_o, id_ex_1_p27,
       id_ex_1_p33, sel_I, sel_O, sel_O_ID;
  wire [3:0] controller_1_branch, controller_1_out_4, ex_mem_1_wb_o, id_ex_1_p26, id_ex_1_p30, id_ex_1_p36,
       mem_wb_1_wb_o;
  wire [15:0] \load_use次数 , \总周期数 , \插入气泡数 , \无条件分支指令数 , \有条件分支成功跳转 ;
  wire [23:0] cur_JPC_O, NPC, oPC_EX, PC, pre_PC;
  wire [31:0] adder_1_out, alu_1_result, alui_1_out_7, alui_1_out_8, bit_extender_1_out, EX, ex_mem_1_data_o,
       ex_mem_1_rs_o, ID, id_ex_1_p34, id_ex_1_p38, IF, if_id_1_opc_o, MEM, MEM_RES, mem_wb_1_data_o,
       mem_wb_1_res_o, mips_ram_1_p6, mips_ram_1_p7, mips_ram_1_p8, multiplexer_1_out, multiplexer_2_out,
       multiplexer_3_out, multiplexer_4_out, oPC, pc_1_out_20, reg_file_1_rf_d1, reg_file_1_rf_d2,
       shifter_2_out, SyscallOut, WB, WB_DATA;
  wire [31:24] shifter_1_out;

  Button \u_总复位  (.out(RST));
  Button _1 (.out(IR1));
  Button _2 (.out(IR2));
  Button _3 (.out(IR3));
  Clock clock_1 (.out(T));
  LED led_1 (.in(W1));
  LED led_2 (.in(W2));
  LED led_3 (.in(W3));
  // Probe on IF
  PC pc_1 (
    .in_5(multiplexer_1_out), .in_6(EX[25:0]), .in_7(EX[15:0]), .in_8(alu_1_equal), .in_9(RST), .in_10(HALT),
    .in_11(T), .out_20(pc_1_out_20), .out_21(PC), .out_22(\总周期数 ), .out_23(\无条件分支指令数 ), .out_25(\有条件分支成功跳转 ),
    .in_2(mem_wb_1_en_o), .stall(data_confilct_1_stall), .Branch_I(id_ex_1_p26), .\气泡数 (\插入气泡数 ),
    .sys(controller_1_out_13), .\load_use数 (\load_use次数 ), .NPC(NPC), .write(write), .suc(suc),
    .pre_PC(pre_PC), .hit(hit_O), .pre_J(pre_J), .clear(clear), .hit_I(hit_I), .cur_JPC(oPC_EX),
    .oPC_EX(oPC), .pre_EX(pre_EX));  // open: out_24, B_instruc
  Button u_GO (.out(GO));
  Hex_Digit_Display hex_digit_display_1 (.value(SyscallOut[31:28]));  // open: dp
  // Probe on ID
  ROM #(.addrWidth(24), .dataWidth(32)) rom_1 (.addr(PC), .data(IF));  // open: sel
  Hex_Digit_Display hex_digit_display_2 (.value(SyscallOut[23:20]));  // open: dp
  Hex_Digit_Display hex_digit_display_3 (.value(SyscallOut[27:24]));  // open: dp
  IF_ID if_id_1 (
    .clk(T), .Data_I(IF), .RST(RST), .Data_O(ID), .oPC_I(pc_1_out_20), .oPC_O(if_id_1_opc_o),
    .stall(data_confilct_1_stall), .clear(clear), .HALT(HALT), .hit_I(hit_O), .hit_O(hit_O_ID),
    .sel_O(sel_O_ID), .sel_I(sel_O), .pre_I(pre_J), .pre_O(if_id_1_pre_o));
  Hex_Digit_Display hex_digit_display_4 (.value(SyscallOut[15:12]));  // open: dp
  Hex_Digit_Display hex_digit_display_5 (.value(SyscallOut[19:16]));  // open: dp
  // Probe on EX
  // Probe on ID
  Controller controller_1 (
    .in_1(ID[31:26]), .in_2(ID[5:0]), .out_10(controller_1_out_10), .out_8(controller_1_out_8),
    .out_4(controller_1_out_4), .out_7(controller_1_out_7), .out_5(controller_1_out_5),
    .out_6(controller_1_out_6), .out_9(controller_1_out_9), .out_11(controller_1_out_11),
    .out_12(controller_1_out_12), .out_14(controller_1_out_14), .out_15(controller_1_out_15),
    .out_13(controller_1_out_13), .src_reg(controller_1_src_reg), .des_reg(controller_1_des_reg),
    .Branch(controller_1_branch));
  Reg_File reg_file_1 (
    .rs(ID[25:21]), .rd(ID[15:11]), .rt(ID[20:16]), .clk(T), .rWE(mem_wb_1_wb_o[3]), .rW_2(mem_wb_1_wb_o_2),
    .Syscall(controller_1_out_13), .RES(mem_wb_1_res_o), .Din(mem_wb_1_data_o), .RF_D1(reg_file_1_rf_d1),
    .RF_D2(reg_file_1_rf_d2), .rW(mem_wb_1_wb_o[0]), .Instruction_I(WB));  // open: rt_I, rd_I
  Hex_Digit_Display hex_digit_display_6 (.value(SyscallOut[7:4]));  // open: dp
  Hex_Digit_Display hex_digit_display_7 (.value(SyscallOut[11:8]));  // open: dp
  // Probe on MEM
  // Probe on reg_file_1_rf_d1
  Hex_Digit_Display hex_digit_display_8 (.value(SyscallOut[3:0]));  // open: dp
  data_confilct data_confilct_1 (
    .Instruction_ID(ID), .Instruction_EX(EX), .Instruction_MEM(MEM), .src_reg_ID(controller_1_src_reg),
    .des_reg_EX(id_ex_1_p27), .des_reg_MEM(ex_mem_1_des_reg_o), .stall(data_confilct_1_stall),
    .rW(id_ex_1_p31), .rs_EX_MEM(rs_EX_MEM), .rt_EX_MEM(rt_EX_MEM), .rs_EX_WB(rs_EX_WB), .rt_EX_WB(rt_EX_WB),
    .in_2(RST), .in_1(T));
  // Probe on WB
  // ID_EX id_ex_1: pin names not known; wires that end beside it: controller_1_branch, controller_1_des_reg, controller_1_out_10, controller_1_out_9, controller_1_out_8, controller_1_out_7, controller_1_out_13, controller_1_out_5, controller_1_out_6, controller_1_out_4, controller_1_out_14, ID, reg_file_1_rf_d1, reg_file_1_rf_d2, hit_O_ID, sel_O_ID, HALT, if_id_1_opc_o, if_id_1_pre_o, T, data_confilct_1_stall, id_ex_1_p22, id_ex_1_p22, RST, clear, id_ex_1_p26, id_ex_1_p27, EX, id_ex_1_p29, id_ex_1_p30, id_ex_1_p31, id_ex_1_p32, id_ex_1_p33, id_ex_1_p34, oPC, id_ex_1_p36, id_ex_1_p37, id_ex_1_p38, hit_I, sel_I, id_ex_1_p41, pre_EX
  // Probe on \总周期数 
  // Probe on \无条件分支指令数 
  // Probe on \有条件分支成功跳转 
  // Probe on \load_use次数 
  // Probe on \插入气泡数 
  Multiplexer #(.select(2), .width(32)) multiplexer_1 (
    .in0(id_ex_1_p34), .in1(MEM_RES), .in2(WB_DATA), .in3(MEM_RES), .out(multiplexer_1_out),
    .sel({rs_EX_WB, rs_EX_MEM}));  // open: en
  Multiplexer #(.select(2), .width(32)) multiplexer_2 (
    .in0(id_ex_1_p38), .in1(MEM_RES), .in2(WB_DATA), .in3(MEM_RES), .out(multiplexer_2_out),
    .sel({rt_EX_WB, rt_EX_MEM}));  // open: en
  Syscall syscall_1 (
    .in_1(multiplexer_1_out), .in_2(multiplexer_2_out), .in_3(id_ex_1_p41), .in_4(T), .in_5(RST),
    .out_7(HALT), .out_8(SyscallOut), .GO(GO));
  Shifter #(.width(32), .shift("lr")) shifter_1 (.in(oPC), .\dist (5'b00010), .out({shifter_1_out, oPC_EX}));
  // Probe on alui_1_out_7
  AluI alui_1 (
    .in_3(EX), .in_1(id_ex_1_p32), .in_2(id_ex_1_p33), .in_4(multiplexer_1_out), .in_5(multiplexer_2_out),
    .in_6(oPC), .out_7(alui_1_out_7), .out_8(alui_1_out_8));
  // Probe on alui_1_out_8
  BHT bht_1 (
    .T(T), .RST(RST), .suc(suc), .write(write), .hit_I(hit_I), .sel_I(sel_I), .PC(PC), .cur_PC(oPC_EX),
    .NPC(NPC), .pre_PC(pre_PC), .sel(sel_O), .hit(hit_O), .pre_J(pre_J), .cur_JPC_O(cur_JPC_O));
  Alu alu_1 (
    .X(alui_1_out_7), .Y(alui_1_out_8), .AluOP(id_ex_1_p36), .Equal(alu_1_equal), .Result(alu_1_result));  // open: Signed_Overflow, UnSigned_Overflow, Result_2
  EX_MEM ex_mem_1 (
    .clk(T), .RST(RST), .Data_I(multiplexer_2_out), .Data_O(ex_mem_1_data_o), .MemW_O(ex_mem_1_memw_o),
    .WB_O(ex_mem_1_wb_o), .MemW_I(id_ex_1_p29), .WB_I(id_ex_1_p30), .RES_I(alu_1_result), .RES_O(MEM_RES),
    .EN_I(HALT), .EN_O(ex_mem_1_en_o), .rs_EX_MEM_O(ex_mem_1_rs_ex_mem_o),
    .rt_EX_MEM_O(ex_mem_1_rt_ex_mem_o), .Instruction_I(EX), .Instruction_O(MEM), .des_reg_I(id_ex_1_p27),
    .des_reg_O(ex_mem_1_des_reg_o), .LHU_I(id_ex_1_p37), .LHU_O(ex_mem_1_lhu_o), .rs_O(ex_mem_1_rs_o),
    .rs_I(multiplexer_1_out), .HALT(HALT), .rs_EX_MEM_I(rs_EX_MEM), .rt_EX_MEM_I(rt_EX_MEM));  // open: Addr_I, Addr_O
  // Probe on alu_1_result
  // Probe on ex_mem_1_data_o
  // Probe on ex_mem_1_rs_o
  Multiplexer #(.width(32)) multiplexer_3 (
    .in0(ex_mem_1_data_o), .in1(WB_DATA), .out(multiplexer_3_out), .sel(and_1_out));  // open: en
  and and_1 (and_1_out, ex_mem_1_memw_o, or_1_out);
  or or_1 (or_1_out, ex_mem_1_rs_ex_mem_o, ex_mem_1_rt_ex_mem_o);
  // Probe on shifter_2_out[23:0]
  Adder #(.width(32)) adder_1 (.a(ex_mem_1_rs_o), .b({{16{1'b0}}, MEM[15:0]}), .out(adder_1_out));  // open: cin, cout
  Shifter #(.width(32), .shift("lr")) shifter_2 (.in(adder_1_out), .\dist (5'b00010), .out(shifter_2_out));
  // Probe on multiplexer_3_out
  // MIPS_RAM mips_ram_1: pin names not known; wires that end beside it: multiplexer_3_out, ex_mem_1_memw_o, T, 1'b1, RST, mips_ram_1_p6, mips_ram_1_p7, mips_ram_1_p8, HALT
  // Probe on mem_wb_1_res_o
  // Probe on mips_ram_1_p6
  assign bit_extender_1_out = {{16{1'b0}}, mips_ram_1_p6[15:0]};  // Bit_Extender bit_extender_1
  assign mips_ram_1_p7 = {{16{1'b0}}, mips_ram_1_p6[31:16]};  // Bit_Extender bit_extender_2
  // Probe on mem_wb_1_data_o
  MEM_WB mem_wb_1 (
    .clk(T), .RST(RST), .WB_I(ex_mem_1_wb_o), .Data_I(multiplexer_4_out),
    .WB_O({mem_wb_1_wb_o[3], mem_wb_1_wb_o_2, mem_wb_1_wb_o[0]}), .Data_O(mem_wb_1_data_o), .RES_I(MEM_RES),
    .RES_O(mem_wb_1_res_o), .EN_O(mem_wb_1_en_o), .EN_I(ex_mem_1_en_o), .Instruction_O(WB),
    .Instruction_I(MEM), .HALT(HALT));  // open: rt_I, rd_I, rt_O, rd_O
  Multiplexer #(.width(32)) multiplexer_4 (
    .in0(mips_ram_1_p6), .in1(mips_ram_1_p8), .out(multiplexer_4_out), .sel(ex_mem_1_lhu_o));  // open: en
  Multiplexer #(.width(32)) multiplexer_5 (
    .in0(bit_extender_1_out), .in1(mips_ram_1_p7), .out(mips_ram_1_p8), .sel(adder_1_out[1]));  // open: en
  // Probe on mem_wb_1_data_o
  Multiplexer #(.width(32)) multiplexer_6 (
    .in0(mem_wb_1_data_o), .in1(mem_wb_1_res_o), .out(WB_DATA), .sel(mem_wb_1_wb_o[0]));  // open: en
  // Probe on WB_DATA

  // Notes on the sheet:
  //   中断源
  //   中断等待指示
  //   contents of rom_1 (hex, n*v repeats v):
  //   20110001 8000c05 20110001 20120002 20130003 8000c09 20110001 20120002 20130003 8000c0d 20110001
  //   20120002 20130003 8000c11 20110001 20120002 20130003 c000cfb 20100001 20110001 118fc0 112020
  //   20020022 c 118882 12200001 8000c15 112020 20020022 c 20110001 118880 112020 20020022 c 12200001
  //   8000c1f 20110001 118fc0 112020 20020022 c 1188c3 112020 20020022 c 118903 112020 20020022 c 118903
  //   112020 20020022 c 118903 112020 20020022 c 118903 112020 20020022 c 118903 112020 20020022 c 118903
  //   112020 20020022 c 118903 112020 20020022 c 20100001 109fc0 139fc3 8021 2012000c 24160003 26100001
  //   3210000f 20080008 20090001 139900 2709825 132020 20020022 c 1094022 1500fff9 22100001 2018000f
  //   2188024 108700 20080008 20090001 139902 2709825 132021 20020022 c 1094022 1500fff9 108702 2c9b022
  //   12c00001 8000c50 4020 1084027 84400 3508ffff 82021 20020022 c 2010ffff 20110000 ae300000 22100001
  //   22310004 ae300000 22100001 22310004 ae300000 22100001 22310004 ae300000 22100001 22310004 ae300000
  //   22100001 22310004 ae300000 22100001 22310004 ae300000 22100001 22310004 ae300000 22100001 22310004
  //   ae300000 22100001 22310004 ae300000 22100001 22310004 ae300000 22100001 22310004 ae300000 22100001
  //   22310004 ae300000 22100001 22310004 ae300000 22100001 22310004 ae300000 22100001 22310004 ae300000
  //   22100001 22310004 22100001 8020 2011003c 8e130000 8e340000 274402a 11000002 ae330000 ae140000
  //   2231fffc 1611fff8 102020 20020022 c 22100004 2011003c 1611fff2 20020032 c 20080001 20090003 20110876
  //   112020 20020022 c 200b0008 1118804 1318804 112020 20020022 c 216bffff 1560fff9 2002000a c 20080001
  //   20090003 20110876 118d00 112020 20020022 c 200b0008 1118806 1318806 112020 20020022 c 216bffff
  //   1560fff9 2002000a c 20090000 200b0010 34118483 20120404 118c00 129400 36318281 22520404 ad310000
  //   2328820 21290004 216bffff 1560fffb 200b0020 20090000 95310000 112020 20020022 c 21290002 216bffff
  //   1560fff9 2002000a c 2011000f 112020 20020022 c 2231ffff 1e20fffb 2002000a c 2002000a c 20100000
  //   22100001 102020 20020022 c 22100002 102020 20020022 c 22100003 102020 20020022 c 22100004 102020
  //   20020022 c 22100005 102020 20020022 c 22100006 102020 20020022 c 22100007 102020 20020022 c 22100008
  //   102020 20020022 20020022 c 3e00008
  //   数码管输出
endmodule

module Controller (
  input  [5:0] in_1,
  input  [5:0] in_2,
  output [3:0] Branch,
  output [3:0] out_4,
  output [1:0] out_5,
  output [2:0] out_6,
  output out_7,
  output [1:0] out_8,
  output out_9,
  output out_10,
  output [1:0] out_11,
  output out_12,
  output out_13,
  output out_14,
  output out_15,
  output [2:0] src_reg,
  output [2:0] des_reg
);

  wire add, addi, addiu, addu, \and , and_2_out, and_3_out, and_4_out, and_5_out, and_6_out, and_7_out,
       and_8_out, and_9_out, and_10_out, and_11_out, and_17_out, andi, beq, bgtz_t, bne, j_t, jr, lhu_t, lw,
       \nor , Op__0, \or , or_1_out, or_2_out, or_3_out, or_4_out, or_5_out, or_6_out, or_12_out, or_13_out,
       or_14_out, or_15_out, or_16_out, or_17_out, or_18_out, or_19_out, or_20_out, ori,
       priority_encoder_2_p2, priority_encoder_2_p4, priority_encoder_2_p5, sll, sllv, slt, slti, sltiu,
       sltu, sra, srl, srlv, sub, syscall;
  wire [3:0] priority_encoder_1_out, priority_encoder_2_p1;

  Comparator #(.width(6)) comparator_1 (.a(in_1), .b({6{1'b0}}), .eq(Op__0));  // open: gt, lt
  Comparator #(.width(6)) comparator_2 (.a(in_1), .b(6'b000100), .eq(beq));  // open: gt, lt
  Comparator #(.width(6)) comparator_3 (.a(in_1), .b(6'b000101), .eq(bne));  // open: gt, lt
  Comparator #(.width(6)) comparator_4 (.a(in_1), .b(6'b001010), .eq(slti));  // open: gt, lt
  Comparator #(.width(6)) comparator_5 (.a(in_1), .b(6'b001101), .eq(ori));  // open: gt, lt
  Comparator #(.width(6)) comparator_6 (.a(in_1), .b(6'b001100), .eq(andi));  // open: gt, lt
  Comparator #(.width(6)) comparator_7 (.a(in_1), .b(6'b001001), .eq(addiu));  // open: gt, lt
  Comparator #(.width(6)) comparator_8 (.a(in_1), .b(6'b001000), .eq(addi));  // open: gt, lt
  Comparator #(.width(6)) comparator_9 (.a(in_1), .b(6'b000010), .eq(j_t));  // open: gt, lt
  or or_1 (or_1_out, bgtz_t, slti);
  or or_2 (or_2_out, bne, beq);
  or or_3 (or_3_out, add, addu, \and , sub, \or , \nor , slt, sltu, jr, sllv, srlv);
  or or_4 (or_4_out, add, addu, \and , sll, sra, srl, sub, \or , \nor , slt, sltu);
  Comparator #(.width(6)) comparator_10 (.a(in_1), .b(6'b101011), .eq(out_10));  // open: gt, lt
  Comparator #(.width(6)) comparator_11 (.a(in_1), .b(6'b100011), .eq(lw));  // open: gt, lt
  Comparator #(.width(6)) comparator_12 (.a(in_1), .b(6'b000011), .eq(des_reg[2]));  // open: gt, lt
  Comparator #(.width(6)) comparator_13 (.a(in_2), .b(6'b101011), .eq(sltu));  // open: gt, lt
  Comparator #(.width(6)) comparator_14 (.a(in_2), .b(6'b101010), .eq(slt));  // open: gt, lt
  Comparator #(.width(6)) comparator_15 (.a(in_2), .b(6'b100111), .eq(\nor ));  // open: gt, lt
  Comparator #(.width(6)) comparator_16 (.a(in_2), .b(6'b100101), .eq(\or ));  // open: gt, lt
  Comparator #(.width(6)) comparator_17 (.a(in_2), .b(6'b100100), .eq(\and ));  // open: gt, lt
  or or_5 (or_5_out, des_reg[2], addi, lw, out_10, addiu, lhu_t);
  Priority_Encoder #(.select(4)) priority_encoder_1 (
    .in5(or_5_out), .in7(andi), .in8(ori), .in11(or_1_out), .in12(sltiu), .in14(or_2_out),
    .out(priority_encoder_1_out));  // open: in0, in1, in2, in3, in4, in6, in9, in10, in13, in15, gs, en_out, en_in
  or or_6 (or_6_out, des_reg[2], j_t);
  // AND_Gate and_1 has open pins: in0=or_6_out, in1=Op__0, out=open
  or or_7 (src_reg[0], addi, addiu, andi, ori, out_10, lw, beq, bne, slti, lhu_t, bgtz_t, and_2_out);
  and and_2 (and_2_out, or_3_out, Op__0);
  or or_8 (src_reg[1], out_10, lw, sllv, srlv, beq, bne, lhu_t, and_3_out);
  and and_3 (and_3_out, or_4_out, Op__0);
  Comparator #(.width(6)) comparator_18 (.a(in_2), .b(6'b100010), .eq(sub));  // open: gt, lt
  Comparator #(.width(6)) comparator_19 (.a(in_2), .b(6'b100001), .eq(addu));  // open: gt, lt
  Comparator #(.width(6)) comparator_20 (.a(in_2), .b(6'b100000), .eq(add));  // open: gt, lt
  Comparator #(.width(6)) comparator_21 (.a(in_2), .b(6'b001100), .eq(syscall));  // open: gt, lt
  Comparator #(.width(6)) comparator_22 (.a(in_2), .b(6'b001000), .eq(jr));  // open: gt, lt
  Comparator #(.width(6)) comparator_23 (.a(in_2), .b(6'b000011), .eq(sra));  // open: gt, lt
  Comparator #(.width(6)) comparator_24 (.a(in_2), .b(6'b000010), .eq(srl));  // open: gt, lt
  Comparator #(.width(6)) comparator_25 (.a(in_2), .b({6{1'b0}}), .eq(sll));  // open: gt, lt
  Multiplexer #(.width(4)) multiplexer_1 (
    .in0(priority_encoder_1_out), .in1(priority_encoder_2_p1), .out(out_4), .sel(Op__0));  // open: en
  // Priority_Encoder #(.select(4)) priority_encoder_2: pin names not known; wires that end beside it: priority_encoder_2_p1, priority_encoder_2_p2, sra, priority_encoder_2_p4, priority_encoder_2_p5, sub, \and , \or , \nor , slt, sltu
  or or_9 (priority_encoder_2_p2, sll, sllv);
  or or_10 (priority_encoder_2_p5, add, addu);
  Multiplexer #(.select(2), .width(2)) multiplexer_2 (
    .in0(2'b10), .in1(2'b11), .in2(2'b00), .in3(2'b00), .out(out_8), .sel({Op__0, des_reg[2]}));  // open: en
  or or_11 (priority_encoder_2_p4, srl, srlv);
  or or_12 (or_12_out, addiu, lw, addi, des_reg[2], ori, andi, lhu_t, slti);
  or or_13 (or_13_out, \nor , sub, \or , \and , slt, add, sllv, sra, addu, srl, sltu, sll, srlv);
  Multiplexer multiplexer_3 (.in0(or_12_out), .in1(or_13_out), .out(out_7), .sel(Op__0));  // open: en
  and and_4 (and_4_out, Op__0, jr);
  and and_5 (and_5_out, ~Op__0, beq);  // AND_Gate
  and and_6 (and_6_out, ~Op__0, bne);  // AND_Gate
  or or_14 (or_14_out, sra, srl, sllv, sll, srlv);
  or or_15 (or_15_out, slti, lw, out_10, addiu, lhu_t, addi);
  or or_16 (or_16_out, andi, ori);
  Comparator #(.width(6)) comparator_26 (.a(in_1), .b(6'b000111), .eq(bgtz_t));  // open: gt, lt
  Comparator #(.width(6)) comparator_27 (.a(in_2), .b(6'b000100), .eq(sllv));  // open: gt, lt
  or or_17 (or_17_out, des_reg[2], j_t);
  Priority_Encoder #(.select(2)) priority_encoder_3 (
    .in0(1'b1), .in1(and_4_out), .in2(and_5_out), .in3(and_6_out), .out(Branch[2:1]));  // open: gs, en_out, en_in
  and and_7 (and_7_out, Op__0, or_14_out);
  and and_8 (and_8_out, des_reg[2], ~Op__0);  // AND_Gate
  and and_9 (and_9_out, ~Op__0, or_15_out);  // AND_Gate
  and and_10 (and_10_out, ~Op__0, or_16_out);  // AND_Gate
  or or_18 (or_18_out, sllv, srlv);
  and and_11 (and_11_out, or_18_out, Op__0);
  or or_19 (or_19_out, add, addu, \and , sll, sra, srl, sub, \or , \nor , slt, sltu, sllv, srlv);
  and and_12 (Branch[0], or_17_out, ~Op__0);  // AND_Gate
  or or_20 (or_20_out, lhu_t, lw);
  Priority_Encoder #(.select(2)) priority_encoder_4 (
    .in0(1'b1), .in1(and_7_out), .in2(and_8_out), .out(out_5));  // open: in3, gs, en_out, en_in
  Priority_Encoder priority_encoder_5 (
    .in0(1'b1), .in1(and_7_out), .in2(and_9_out), .in3(and_10_out), .in4(and_8_out), .in5(and_11_out),
    .out(out_6));  // open: in6, in7, en_in, gs, en_out
  or or_21 (des_reg[0], addi, addiu, andi, ori, lw, slti, lhu_t);
  and and_13 (des_reg[1], or_19_out, Op__0);
  Comparator #(.width(6)) comparator_28 (.a(in_1), .b(6'b100101), .eq(lhu_t));  // open: gt, lt
  Comparator #(.width(6)) comparator_29 (.a(in_2), .b(6'b000110), .eq(srlv));  // open: gt, lt
  and and_14 (Branch[3], bgtz_t, ~Op__0);  // AND_Gate
  and and_15 (out_13, syscall, Op__0);
  and and_16 (out_14, lhu_t, ~Op__0);  // AND_Gate
  and and_17 (and_17_out, or_20_out, ~Op__0);  // AND_Gate
  not not_1 (out_9, and_17_out);
  Decoder #(.select(5)) decoder_1 ();  // open: out0, out1, out2, out3, out4, out5, out6, out7, out8, out9, out10, out11, out12, out13, out14, out15, out16, out17, out18, out19, out20, out21, out22, out23, out24, out25, out26, out27, out28, out29, out30, out31, sel, en
  Decoder #(.select(5)) decoder_2 ();  // open: out0, out1, out2, out3, out4, out5, out6, out7, out8, out9, out10, out11, out12, out13, out14, out15, out16, out17, out18, out19, out20, out21, out22, out23, out24, out25, out26, out27, out28, out29, out30, out31, sel, en
  Decoder #(.select(5)) decoder_3 ();  // open: out0, out1, out2, out3, out4, out5, out6, out7, out8, out9, out10, out11, out12, out13, out14, out15, out16, out17, out18, out19, out20, out21, out22, out23, out24, out25, out26, out27, out28, out29, out30, out31, sel, en
  Decoder #(.select(5)) decoder_4 ();  // open: out0, out1, out2, out3, out4, out5, out6, out7, out8, out9, out10, out11, out12, out13, out14, out15, out16, out17, out18, out19, out20, out21, out22, out23, out24, out25, out26, out27, out28, out29, out30, out31, sel, en

  assign out_11 = Branch[2:1];
  assign out_12 = Branch[0];
  assign out_15 = Branch[3];
  assign src_reg[2] = out_13;

  // Other names for the same wires on the sheet: AluOp[3:0] = out_4; AluX[1:0] = out_5; AluY[2:0] = out_6;
  //   J = Branch[0]; PCW[1:0] = Branch[2:1]; BGTZ = Branch[3]; jal = des_reg[2]; LHU = out_14; Op[5:0] = in_1;
  //   rW = out_9; rW_t[1:0] = out_8; rWE = out_7; Sp[5:0] = in_2; Sys = out_13; MemW = out_10; sw = out_10

  // Notes on the sheet:
  //   source_rs
  //   source_rt
  //   sys->2&4
  //   Instructions
  //   Reg Write Dst
  //   O->rD
  //   2->rT
  //   3->$31
  //   Alu Operator
  //   reg Write Enable
  //   des_rd
  //   RAM Write
  //   Branching
  //   0->PC++
  //   1->$rS
  //   2->beq
  //   3->bne
  //   des_rt
  //   J/JAL
  //   3->$31
  //   CCMB
  //   lbtz(CCMB)
  //   Syscall
  //   lbu(CCMB)
  //   Reg Write Src
  //   0->MemO
  //   1->AluR
  //   Alu Input
  //   0->rS(default)
  //   1->rT
  //   2->PC
  //   0->rT(default)
  //   1->sA
  //   2->Immi_S
  //   3->Immi_U
  //   4->4
  //   5->rS(CCMB)
endmodule

module Alu (
  input  [31:0] X,
  input  [31:0] Y,
  input  [3:0] AluOP,
  output Signed_Overflow,
  output UnSigned_Overflow,
  output Equal,
  output [31:0] Result,
  output [31:0] Result_2
);

  wire OF1, OF2, UOF1, UOF2, xnor_1_out, xor_1_out, xor_2_out, xor_3_out;
  wire [0:0] R12, R13;
  wire [31:0] R1, R2, R3, R4, R5, R6, R7, R8, R9, R10, R11, R21, R22;

  // Probe on X
  // Probe on X
  // Probe on Y
  // Probe on Y
  Shifter #(.width(32)) shifter_1 (.in(X), .\dist (Y[4:0]), .out(R1));
  Shifter #(.width(32), .shift("ar")) shifter_2 (.in(X), .\dist (Y[4:0]), .out(R2));
  Shifter #(.width(32), .shift("lr")) shifter_3 (.in(X), .\dist (Y[4:0]), .out(R3));
  Multiplier #(.width(32)) multiplier_1 (.a(X), .b(Y), .out(R4), .cout(R21));  // open: cin
  Divider #(.width(32)) divider_1 (.a(X), .b(Y), .out(R5), .rem(R22));  // open: upper
  xnor xnor_1 (xnor_1_out, X[31], Y[31]);
  xor xor_1 (xor_1_out, Y[31], X[31]);
  // Probe on AluOP
  Adder #(.width(32)) adder_1 (.a(X), .b(Y), .out(R6), .cin(1'b0), .cout(UOF1));
  xor xor_2 (xor_2_out, Y[31], R6[31]);
  and and_1 (OF1, xnor_1_out, xor_2_out);
  Subtractor #(.width(32)) subtractor_1 (.a(X), .b(Y), .out(R7), .bin(1'b0), .bout(UOF2));
  xor xor_3 (xor_3_out, X[31], R7[31]);
  and and_2 (OF2, xor_1_out, xor_3_out);
  // Probe on Result
  // Probe on Result
  assign R8 = X & Y;  // AND_Gate and_3, 32 bits wide
  assign R9 = X | Y;  // OR_Gate or_1, 32 bits wide
  assign R10 = X ^ Y;  // XOR_Gate xor_4, 32 bits wide
  assign R11 = ~(X | Y);  // NOR_Gate nor_1, 32 bits wide
  Comparator #(.width(32)) comparator_1 (.a(X), .b(Y), .eq(Equal), .lt(R12[0]));  // open: gt
  Comparator #(.width(32), .mode("unsigned")) comparator_2 (.a(X), .b(Y), .lt(R13[0]));  // open: gt, eq
  // Probe on Result_2
  Multiplexer #(.select(4), .width(32)) multiplexer_1 (
    .in0(R1), .in1(R2), .in2(R3), .in3(R4), .in4(R5), .in5(R6), .in6(R7), .in7(R8), .in8(R9), .in9(R10),
    .in10(R11), .in11({{31{1'b0}}, R12[0]}), .in12({{31{1'b0}}, R13[0]}), .in13({32{1'b0}}),
    .in14({32{1'b0}}), .in15({32{1'b0}}), .out(Result), .sel(AluOP));  // open: en
  Multiplexer #(.select(4)) multiplexer_2 (
    .in0(1'b0), .in1(1'b0), .in2(1'b0), .in3(1'b0), .in4(1'b0), .in5(UOF1), .in6(UOF2), .in7(1'b0),
    .in8(1'b0), .in9(1'b0), .in10(1'b0), .in11(1'b0), .in12(1'b0), .in13(1'b0), .in14(1'b0), .in15(1'b0),
    .out(UnSigned_Overflow), .sel(AluOP));  // open: en
  Multiplexer #(.select(4), .width(32)) multiplexer_3 (
    .in0({32{1'b0}}), .in1({32{1'b0}}), .in2({32{1'b0}}), .in3(R21), .in4(R22), .in5({32{1'b0}}),
    .in6({32{1'b0}}), .in7({32{1'b0}}), .in8({32{1'b0}}), .in9({32{1'b0}}), .in10({32{1'b0}}),
    .in11({32{1'b0}}), .in12({32{1'b0}}), .in13({32{1'b0}}), .in14({32{1'b0}}), .in15({32{1'b0}}),
    .out(Result_2), .sel(AluOP));  // open: en
  Multiplexer #(.select(4)) multiplexer_4 (
    .in0(1'b0), .in1(1'b0), .in2(1'b0), .in3(1'b0), .in4(1'b0), .in5(OF1), .in6(OF2), .in7(1'b0), .in8(1'b0),
    .in9(1'b0), .in10(1'b0), .in11(1'b0), .in12(1'b0), .in13(1'b0), .in14(1'b0), .in15(1'b0),
    .out(Signed_Overflow), .sel(AluOP));  // open: en

  // Other names for the same wires on the sheet: OF = Signed_Overflow; Result2[31:0] = Result_2; S[3:0] = AluOP;
  //   UOF = UnSigned_Overflow

  // Notes on the sheet:
  //   不要改变此引脚区域内容，也不要改变ALU封装形式
  //   输入引脚
  //   请在下方利用上方输入输出引脚的隧道信号构建ALU电路，ctrl+d复制选择部件
  //   华中科技大学计算机学院 计算机组成原理，鸣谢加州大学伯克利CS61C课程
  //   输出引脚
  //   探测区域
endmodule

module PC (
  input  [3:0] Branch_I,
  input  in_2,
  input  stall,
  input  sys,
  input  [31:0] in_5,
  input  [25:0] in_6,
  input  [15:0] in_7,
  input  in_8,
  input  in_9,
  input  in_10,
  input  in_11,
  input  pre_EX,
  input  [23:0] pre_PC,
  input  hit,
  input  hit_I,
  input  pre_J,
  input  [31:0] oPC_EX,
  input  [23:0] cur_JPC,
  output B_instruc,
  output [31:0] out_20,
  output [23:0] out_21,
  output [15:0] out_22,
  output [15:0] out_23,
  output [15:0] out_24,
  output [15:0] out_25,
  output [15:0] \气泡数 ,
  output [15:0] \load_use数 ,
  output [23:0] NPC,
  output write,
  output suc,
  output clear
);

  wire _BGTZ, _J, and_1_out, and_2_out, and_3_out, and_4_out, and_6_out, and_7_out, and_9_out, and_10_out,
       and_11_out, and_12_out, and_13_out, and_15_out, and_16_out, and_17_out, and_18_out, and_19_out,
       and_20_out, and_21_out, and_23_out, and_24_out, and_25_out, beq, bne, CNT, comparator_1_gt,
       comparator_2_eq, comparator_3_gt, comparator_4_eq, comparator_5_gt, decoder_1_out1, hit_nsuc,
       incrementer_1_p1, incrementer_1_p3, JE, JN, JR, not_1_out, not_3_out, not_4_out, or_1_out, or_2_out,
       or_5_out, or_6_out, or_7_out;
  wire [1:0] _PCW;
  wire [1:1] and_8_out;
  wire [23:0] adder_2_out;
  wire [31:0] adder_1_out, B_PC, bit_extender_1_out, bit_extender_2_out, J_PC, multiplexer_1_out,
       multiplexer_2_out, multiplexer_3_out, multiplexer_4_out, multiplexer_5_out, multiplexer_6_out, PC_1,
       shifter_1_out, shifter_2_out, shifter_3_out;
  wire [31:24] multiplexer_7_out, PC_q;

  Decoder #(.select(2)) decoder_1 (
    .out1(decoder_1_out1), .out2(beq), .out3(bne), .sel(Branch_I[2:1]));  // open: out0, en
  Shifter #(.width(32), .shift("ar")) shifter_1 (.in({in_7, {16{1'b0}}}), .\dist (5'b01110), .out(shifter_1_out));
  Adder #(.width(32)) adder_1 (.a(oPC_EX), .b(shifter_1_out), .out(adder_1_out));  // open: cin, cout
  Shifter #(.width(32), .shift("lr")) shifter_2 (.in(adder_1_out), .\dist (5'b00010), .out(shifter_2_out));
  and and_1 (and_1_out, beq, ~pre_EX, suc);  // AND_Gate
  and and_2 (and_2_out, beq, ~hit_I);  // AND_Gate
  and and_3 (and_3_out, bne, ~hit_I);  // AND_Gate
  and and_4 (and_4_out, bne, ~pre_EX, suc);  // AND_Gate
  // Incrementer incrementer_1: pin names not known; wires that end beside it: incrementer_1_p1, shifter_2_out, incrementer_1_p3, Branch_I[2:1], incrementer_1_p3
  Multiplexer #(.width(32)) multiplexer_1 (.in0(B_PC), .in1(PC_1), .out(multiplexer_1_out), .sel(in_8));  // open: en
  and and_5 (_J, Branch_I[0], ~hit_I);  // AND_Gate
  and and_6 (and_6_out, ~hit_I, Branch_I[3]);  // AND_Gate
  or or_1 (or_1_out, and_2_out, and_1_out);
  or or_2 (or_2_out, and_3_out, and_4_out);
  Shifter #(.width(32), .shift("lr")) shifter_3 (.in(in_5), .\dist (5'b00010), .out(shifter_3_out));
  Multiplexer #(.width(32)) multiplexer_2 (.in0(PC_1), .in1(B_PC), .out(multiplexer_2_out), .sel(in_8));  // open: en
  // Probe on multiplexer_2_out
  Comparator #(.width(32)) comparator_1 (.a(in_5), .b({32{1'b0}}), .gt(comparator_1_gt));  // open: eq, lt
  and and_7 (and_7_out, Branch_I[3], ~pre_EX, suc);  // AND_Gate
  Priority_Encoder #(.select(2)) priority_encoder_1 (
    .in0(1'b1), .in1(decoder_1_out1), .in2(or_1_out), .in3(or_2_out), .out(_PCW));  // open: gs, en_out, en_in
  // Probe on _PCW
  Comparator #(.width(4)) comparator_2 (.a(Branch_I), .b(4'b0000), .eq(comparator_2_eq));  // open: gt, lt
  Multiplexer #(.select(2), .width(32)) multiplexer_3 (
    .in0(PC_1), .in1(shifter_3_out), .in2(multiplexer_2_out), .in3(multiplexer_1_out),
    .out(multiplexer_3_out), .sel(_PCW));  // open: en
  Multiplexer #(.select(2), .width(32)) multiplexer_4 (
    .in0(multiplexer_3_out), .in1(J_PC), .in2(B_PC), .out(multiplexer_4_out), .sel({and_8_out[1], _J}));  // open: in3, en
  and and_8 (and_8_out[1], comparator_1_gt, _BGTZ);
  Subtractor #(.width(32)) subtractor_1 (.a({{6{1'b0}}, in_6}), .b(32'hc00), .out(J_PC));  // open: bin, bout
  or or_3 (_BGTZ, and_6_out, and_7_out);
  not not_1 (not_1_out, in_8);
  Comparator #(.width(32)) comparator_3 (.a(in_5), .b({32{1'b0}}), .gt(comparator_3_gt));  // open: eq, lt
  not not_2 (write, comparator_2_eq);
  assign bit_extender_1_out = {{8{1'b0}}, pre_PC};  // Bit_Extender bit_extender_1
  and and_9 (and_9_out, hit, pre_J);
  Multiplexer #(.width(32)) multiplexer_5 (
    .in0(multiplexer_4_out), .in1(bit_extender_1_out), .out(multiplexer_5_out), .sel(and_9_out));  // open: en
  Adder #(.width(24)) adder_2 (.a(cur_JPC), .b(24'h1), .out(adder_2_out));  // open: cin, cout
  and and_10 (and_10_out, beq, in_8);
  and and_11 (and_11_out, bne, not_1_out);
  and and_12 (and_12_out, Branch_I[3], comparator_3_gt);
  Multiplexer #(.width(32)) multiplexer_6 (
    .in0(multiplexer_5_out), .in1(bit_extender_2_out), .out(multiplexer_6_out), .sel(hit_nsuc));  // open: en
  and and_13 (and_13_out, in_10, not_3_out);
  assign bit_extender_2_out = {{8{1'b0}}, adder_2_out};  // Bit_Extender bit_extender_2
  Pull_Resistor pull_resistor_1 (.node(pre_PC));
  or or_4 (B_instruc, Branch_I[0], and_10_out, and_11_out, and_12_out);
  // Probe on multiplexer_6_out
  Register #(.width(32)) PC (.D(multiplexer_6_out), .en(and_13_out), .Q({PC_q, out_21}), .clk(in_11), .clr(in_9));
  not not_3 (not_3_out, stall);
  Multiplexer #(.width(32)) multiplexer_7 (
    .in0(B_PC), .in1(J_PC), .out({multiplexer_7_out, NPC}), .sel(Branch_I[0]));  // open: en
  Shifter #(.width(32)) shifter_4 (.in({PC_q, out_21}), .\dist (5'b00010), .out(out_20));
  // Incrementer incrementer_2: pin names not known; wires that end beside it: Branch_I[0], Branch_I[3], {PC_q, out_21}, PC_1
  Comparator #(.width(4)) comparator_4 (.a(Branch_I), .b(4'b0000), .eq(comparator_4_eq));  // open: gt, lt
  not not_4 (not_4_out, comparator_4_eq);
  Counter #(.width(16), .max('hffff)) counter_1 (
    .count(CNT), .Q(out_22), .clk(in_11), .clr(in_9));  // open: load, D, carry
  or or_5 (or_5_out, JN, Branch_I[3], JE);
  and and_14 (suc, B_instruc, not_4_out);
  Counter #(.width(16), .max('hffff)) counter_2 (
    .count(and_15_out), .Q(out_24), .clk(in_11), .clr(in_9));  // open: load, D, carry
  and and_15 (and_15_out, or_5_out, CNT);
  Comparator #(.width(32)) comparator_5 (.a(in_5), .b({32{1'b0}}), .gt(comparator_5_gt));  // open: eq, lt
  and and_16 (and_16_out, comparator_5_gt, Branch_I[3]);
  and and_17 (and_17_out, JN, ~in_8);  // AND_Gate
  and and_18 (and_18_out, in_8, JE);
  Counter #(.width(16), .max('hffff)) counter_3 (
    .count(and_19_out), .Q(\load_use数 ), .clk(in_11));  // open: load, D, carry, clr
  and and_19 (and_19_out, stall, CNT);
  and and_20 (and_20_out, B_instruc, ~hit_I);  // AND_Gate
  and and_21 (and_21_out, ~pre_EX, hit_I, suc);  // AND_Gate
  and and_22 (hit_nsuc, ~suc, hit_I);  // AND_Gate
  or or_6 (or_6_out, JR, Branch_I[0]);
  and and_23 (and_23_out, or_6_out, CNT);
  or or_7 (or_7_out, and_16_out, and_17_out, and_18_out);
  and and_24 (and_24_out, or_7_out, CNT);
  Decoder #(.select(2)) decoder_2 (.out1(JR), .out2(JE), .out3(JN), .sel(Branch_I[2:1]));  // open: out0, en
  or or_8 (clear, and_20_out, and_21_out, hit_nsuc);
  Counter #(.width(16), .max('hffff)) counter_4 (
    .count(and_23_out), .Q(out_23), .clk(in_11), .clr(in_9));  // open: load, D, carry
  or or_9 (CNT, in_10, in_2);
  Counter #(.width(16), .max('hffff)) counter_5 (
    .count(and_24_out), .Q(out_25), .clk(in_11), .clr(in_9));  // open: load, D, carry
  Counter #(.width(16), .max('hffff)) counter_6 (
    .count(and_25_out), .Q(\气泡数 ), .clk(in_11));  // open: load, D, carry, clr
  and and_25 (and_25_out, stall, CNT);

  // Other names for the same wires on the sheet: immi[15:0] = in_7; inst[25:0] = in_6; PC[23:0] = out_21;
  //   AluEq = in_8; J = Branch_I[0]; PCW[1:0] = Branch_I[2:1]; BGTZ = Branch_I[3]; EN = in_10; END = in_2;
  //   oPC[31:0] = out_20; rS[31:0] = in_5; RST = in_9; T = in_11; 总周期数[15:0] = out_22; 无条件分支指令数[15:0] = out_23;
  //   有条件分支成功跳转[15:0] = out_25; 有条件分支指令数[15:0] = out_24
endmodule

module Syscall (
  input  [31:0] in_1,
  input  [31:0] in_2,
  input  in_3,
  input  in_4,
  input  in_5,
  input  GO,
  output out_7,
  output [31:0] out_8
);

  wire and_1_out, and_2_out, comparator_1_eq, not_1_out, or_1_out, or_2_out, register_2_q, stall;
  wire [31:0] multiplexer_1_out;

  Comparator #(.width(32)) comparator_1 (.a(in_1), .b(32'h22), .eq(comparator_1_eq));  // open: gt, lt
  and and_1 (and_1_out, in_3, not_1_out);
  not not_1 (not_1_out, comparator_1_eq);
  and and_2 (and_2_out, ~not_1_out, in_3);  // AND_Gate
  Register #(.width(32)) register_1 (.D(multiplexer_1_out), .Q(out_8), .clk(in_4), .clr(in_5));  // open: en
  Multiplexer #(.width(32)) multiplexer_1 (
    .in0(out_8), .in1(in_2), .out(multiplexer_1_out), .sel(and_2_out));  // open: en
  or or_1 (or_1_out, register_2_q, and_1_out);
  Register #(.width(1)) register_2 (.D(or_1_out), .Q(register_2_q), .clk(in_4), .clr(or_2_out));  // open: en
  or or_2 (or_2_out, GO, in_5);
  not not_2 (out_7, register_2_q);
  // NOT_Gate not_3 has open pins: in=stall, out=open

  // Other names for the same wires on the sheet: EN = out_7; rS[31:0] = in_1; RST = in_5; rT[31:0] = in_2; Sys = in_3;
  //   SyscallOut[31:0] = out_8; T = in_4
endmodule

module AluI (
  input  [1:0] in_1,
  input  [2:0] in_2,
  input  [31:0] in_3,
  input  [31:0] in_4,
  input  [31:0] in_5,
  input  [31:0] in_6,
  output [31:0] out_7,
  output [31:0] out_8
);

  wire [31:0] shifter_1_out, shifter_2_out;

  // Probe on nothing
  // Probe on nothing
  Shifter #(.width(32), .shift("ar")) shifter_1 (.in({in_3[15:0], {16{1'b0}}}), .\dist (5'b10000), .out(shifter_1_out));
  Shifter #(.width(32), .shift("lr")) shifter_2 (.in({in_3[15:0], {16{1'b0}}}), .\dist (5'b10000), .out(shifter_2_out));
  Multiplexer #(.select(2), .width(32)) multiplexer_1 (
    .in0(in_4), .in1(in_5), .in2(in_6), .out(out_7), .sel(in_1));  // open: in3, en
  // Probe on in_1
  Multiplexer #(.select(3), .width(32)) multiplexer_2 (
    .in0(in_5), .in1({{27{1'b0}}, in_3[10:6]}), .in2(shifter_1_out), .in3(shifter_2_out), .in4(32'h4),
    .in5(in_4), .out(out_8), .sel(in_2));  // open: in6, in7, en
  // Probe on in_2

  // Other names for the same wires on the sheet: Instruction[31:0] = in_3; AluX[1:0] = in_1; AluY[2:0] = in_2;
  //   oPC[31:0] = in_6; rS[31:0] = in_4; rT[31:0] = in_5; X[31:0] = out_7; Y[31:0] = out_8

  // Notes on the sheet:
  //   Immi
  //   Immi
  //   sa
endmodule

module Reg_File (
  input  rW,
  input  rWE,
  input  [1:0] rW_2,
  input  Syscall,
  input  [31:0] RES,
  input  [31:0] Din,
  input  [31:0] Instruction_I,
  input  [4:0] rs,
  input  [4:0] rt,
  input  [4:0] rt_I,
  input  [4:0] rd,
  input  [4:0] rd_I,
  input  clk,
  output [31:0] RF_D1,
  output [31:0] RF_D2
);

  wire undriven;
  wire [4:0] multiplexer_2_out, multiplexer_3_out, multiplexer_4_out;
  wire [31:0] multiplexer_1_out;

  Multiplexer #(.width(32)) multiplexer_1 (.in0(Din), .in1(RES), .out(multiplexer_1_out), .sel(rW));  // open: en
  Multiplexer #(.select(2), .width(5)) multiplexer_2 (
    .in0(Instruction_I[15:11]), .in2(Instruction_I[20:16]), .in3({5{1'b1}}), .out(multiplexer_2_out),
    .sel(rW_2));  // open: in1, en
  Multiplexer #(.width(5)) multiplexer_3 (
    .in0(rt), .in1(5'b00100), .out(multiplexer_3_out), .sel(Syscall), .en(undriven));
  Multiplexer #(.width(5)) multiplexer_4 (
    .in0(rs), .in1(5'b00010), .out(multiplexer_4_out), .sel(Syscall), .en(undriven));
  // RegisterFile registerfile_1: pin names not known; wires that end beside it: Instruction_I[25:21], multiplexer_1_out, clk, rWE, multiplexer_2_out, multiplexer_4_out, multiplexer_3_out, RF_D1, RF_D2

  // Other names for the same wires on the sheet: rW_t[1:0] = rW_2
endmodule

module ID_EX (
  input  [31:0] Instruction_I,
  input  [31:0] rs_I,
  input  [31:0] rt_I,
  input  [31:0] oPC_I,
  input  clk,
  input  RST,
  input  rW_I,
  input  [1:0] rW_I_2,
  input  rWE_I,
  input  syscall_I,
  input  MemW_I,
  input  EN_I,
  input  [2:0] des_reg_I,
  input  stall,
  input  clear,
  input  LHU_I,
  input  [3:0] Branch_I,
  input  hit_I,
  input  [2:0] sel_I,
  input  pre_I,
  input  [1:0] AluX_I,
  input  [2:0] AluY_I,
  input  [3:0] AluOp_I,
  output [1:0] AluX_O,
  output [2:0] AluY_O,
  output [3:0] AluOp_O,
  output [31:0] Instruction_O,
  output [31:0] rs_O,
  output [31:0] rt_O,
  output [31:0] oPC_O,
  output [2:0] des_reg_O,
  output MemW_O,
  output [3:0] WB,
  output EN_O,
  output rW_O,
  output [3:0] Branch_O,
  output LHU_O,
  output sys_O,
  output hit_O,
  output [2:0] sel_O,
  output pre_O
);

  wire multiplexer_6_out, multiplexer_10_out, multiplexer_11_out, multiplexer_17_out, multiplexer_18_out,
       multiplexer_19_out, multiplexer_20_out, or_1_out, syscall_O;
  wire [1:0] multiplexer_4_out;
  wire [2:0] multiplexer_5_out, multiplexer_15_out, multiplexer_21_out;
  wire [3:0] multiplexer_7_out, multiplexer_12_out, multiplexer_16_out;
  wire [4:0] multiplexer_1_out, multiplexer_2_out, multiplexer_3_out, rd_I, rd_O, rs_I_t, rs_O_t, rt_I_t,
       rt_O_t;
  wire [31:0] multiplexer_8_out, multiplexer_9_out, multiplexer_13_out, multiplexer_14_out;

  or or_1 (or_1_out, clear, stall);
  Register #(.width(5)) register_1 (.D(multiplexer_1_out), .en(EN_I), .Q(rs_O_t), .clk(clk), .clr(RST));
  Multiplexer #(.width(5)) multiplexer_1 (
    .in0(rs_I_t), .in1({5{1'b0}}), .out(multiplexer_1_out), .sel(or_1_out));  // open: en
  Multiplexer #(.width(5)) multiplexer_2 (
    .in0(rt_I_t), .in1({5{1'b0}}), .out(multiplexer_2_out), .sel(or_1_out));  // open: en
  Register #(.width(5)) register_2 (.D(multiplexer_2_out), .en(EN_I), .Q(rt_O_t), .clk(clk), .clr(RST));
  Multiplexer #(.width(5)) multiplexer_3 (
    .in0(rd_I), .in1({5{1'b0}}), .out(multiplexer_3_out), .sel(or_1_out));  // open: en
  Register #(.width(5)) register_3 (.D(multiplexer_3_out), .en(EN_I), .Q(rd_O), .clk(clk), .clr(RST));
  Register #(.width(2)) register_4 (.D(multiplexer_4_out), .en(EN_I), .Q(AluX_O), .clk(clk), .clr(RST));
  Multiplexer #(.width(2)) multiplexer_4 (
    .in0(AluX_I), .in1(2'b00), .out(multiplexer_4_out), .sel(or_1_out));  // open: en
  Register #(.width(3)) register_5 (.D(multiplexer_5_out), .en(EN_I), .Q(AluY_O), .clk(clk), .clr(RST));
  Multiplexer #(.width(3)) multiplexer_5 (
    .in0(AluY_I), .in1(3'b000), .out(multiplexer_5_out), .sel(or_1_out));  // open: en
  Multiplexer multiplexer_6 (.in0(pre_I), .in1(1'b0), .out(multiplexer_6_out), .sel(or_1_out));  // open: en
  Register #(.width(1)) register_6 (.D(multiplexer_6_out), .en(EN_I), .Q(pre_O), .clk(clk), .clr(RST));
  Multiplexer #(.width(4)) multiplexer_7 (
    .in0(AluOp_I), .in1(4'b0000), .out(multiplexer_7_out), .sel(or_1_out));  // open: en
  Multiplexer #(.width(32)) multiplexer_8 (
    .in0(oPC_I), .in1({32{1'b0}}), .out(multiplexer_8_out), .sel(or_1_out));  // open: en
  Multiplexer #(.width(32)) multiplexer_9 (
    .in0(Instruction_I), .in1({32{1'b0}}), .out(multiplexer_9_out), .sel(or_1_out));  // open: en
  Multiplexer multiplexer_10 (.in0(syscall_I), .in1(1'b0), .out(multiplexer_10_out), .sel(or_1_out));  // open: en
  Multiplexer multiplexer_11 (.in0(MemW_I), .in1(1'b0), .out(multiplexer_11_out), .sel(or_1_out));  // open: en
  Register #(.width(4)) register_7 (.D(multiplexer_7_out), .en(EN_I), .Q(AluOp_O), .clk(clk), .clr(RST));
  Register #(.width(32)) register_8 (.D(multiplexer_8_out), .en(EN_I), .Q(oPC_O), .clk(clk), .clr(RST));
  Register #(.width(32)) register_9 (.D(multiplexer_9_out), .en(EN_I), .Q(Instruction_O), .clk(clk), .clr(RST));
  Register #(.width(1)) register_10 (.D(multiplexer_10_out), .en(EN_I), .Q(syscall_O), .clk(clk), .clr(RST));
  Register #(.width(1)) register_11 (.D(multiplexer_11_out), .en(EN_I), .Q(MemW_O), .clk(clk), .clr(RST));
  Register #(.width(4)) register_12 (.D(multiplexer_12_out), .en(EN_I), .Q(WB), .clk(clk), .clr(RST));
  Multiplexer #(.width(4)) multiplexer_12 (
    .in0({rWE_I, rW_I_2, rW_I}), .in1(4'b0000), .out(multiplexer_12_out), .sel(or_1_out));  // open: en
  Register #(.width(32)) register_13 (.D(multiplexer_13_out), .en(EN_I), .Q(rs_O), .clk(clk), .clr(RST));
  Multiplexer #(.width(32)) multiplexer_13 (
    .in0(rs_I), .in1({32{1'b0}}), .out(multiplexer_13_out), .sel(or_1_out));  // open: en
  Register #(.width(32)) register_14 (.D(multiplexer_14_out), .en(EN_I), .Q(rt_O), .clk(clk), .clr(RST));
  Multiplexer #(.width(32)) multiplexer_14 (
    .in0(rt_I), .in1({32{1'b0}}), .out(multiplexer_14_out), .sel(or_1_out));  // open: en
  Multiplexer #(.width(3)) multiplexer_15 (
    .in0(des_reg_I), .in1(3'b000), .out(multiplexer_15_out), .sel(or_1_out));  // open: en
  Register #(.width(3)) register_15 (.D(multiplexer_15_out), .en(EN_I), .Q(des_reg_O), .clk(clk), .clr(RST));
  Register #(.width(1)) register_16 (.D(EN_I), .Q(EN_O), .clk(clk), .clr(RST));  // open: en
  Multiplexer #(.width(4)) multiplexer_16 (
    .in0(Branch_I), .in1(4'b0000), .out(multiplexer_16_out), .sel(or_1_out));  // open: en
  Multiplexer multiplexer_17 (.in0(LHU_I), .in1(1'b0), .out(multiplexer_17_out), .sel(or_1_out));  // open: en
  Multiplexer multiplexer_18 (.in0(syscall_I), .in1(1'b0), .out(multiplexer_18_out), .sel(or_1_out));  // open: en
  Multiplexer multiplexer_19 (.in0(rW_I), .in1(1'b0), .out(multiplexer_19_out), .sel(or_1_out));  // open: en
  Register #(.width(1)) register_17 (.D(multiplexer_20_out), .en(EN_I), .Q(hit_O), .clk(clk), .clr(RST));
  Multiplexer multiplexer_20 (.in0(hit_I), .in1(1'b0), .out(multiplexer_20_out), .sel(or_1_out));  // open: en
  Register #(.width(4)) register_18 (.D(multiplexer_16_out), .en(EN_I), .Q(Branch_O), .clk(clk), .clr(RST));
  Register #(.width(1)) register_19 (.D(multiplexer_17_out), .en(EN_I), .Q(LHU_O), .clk(clk), .clr(RST));
  Register #(.width(1)) register_20 (.D(multiplexer_18_out), .en(EN_I), .Q(sys_O), .clk(clk), .clr(RST));
  Register #(.width(1)) register_21 (.D(multiplexer_19_out), .en(EN_I), .Q(rW_O), .clk(clk), .clr(RST));
  Multiplexer #(.width(3)) multiplexer_21 (
    .in0(sel_I), .in1(3'b000), .out(multiplexer_21_out), .sel(or_1_out));  // open: en
  Register #(.width(3)) register_22 (.D(multiplexer_21_out), .en(EN_I), .Q(sel_O), .clk(clk), .clr(RST));

  // Other names for the same wires on the sheet: rW_I_t[1:0] = rW_I_2
endmodule

module IF_ID (
  input  stall,
  input  clear,
  input  [31:0] Data_I,
  input  [31:0] oPC_I,
  input  HALT,
  input  clk,
  input  RST,
  input  pre_I,
  input  hit_I,
  input  [2:0] sel_I,
  output [31:0] Data_O,
  output [31:0] oPC_O,
  output pre_O,
  output hit_O,
  output [2:0] sel_O
);

  wire and_1_out, multiplexer_3_out, multiplexer_5_out, not_1_out;
  wire [2:0] multiplexer_4_out;
  wire [31:0] multiplexer_1_out, multiplexer_2_out;

  not not_1 (not_1_out, stall);
  and and_1 (and_1_out, not_1_out, HALT);
  Register #(.width(32)) register_1 (.D(multiplexer_1_out), .en(and_1_out), .Q(Data_O), .clk(clk), .clr(RST));
  Multiplexer #(.width(32)) multiplexer_1 (
    .in0(Data_I), .in1({32{1'b0}}), .out(multiplexer_1_out), .sel(clear));  // open: en
  Multiplexer #(.width(32)) multiplexer_2 (
    .in0(oPC_I), .in1({32{1'b0}}), .out(multiplexer_2_out), .sel(clear));  // open: en
  Register #(.width(32)) register_2 (.D(multiplexer_2_out), .en(and_1_out), .Q(oPC_O), .clk(clk), .clr(RST));
  Register #(.width(1)) register_3 (.D(multiplexer_3_out), .en(and_1_out), .Q(hit_O), .clk(clk), .clr(RST));
  Multiplexer multiplexer_3 (.in0(hit_I), .in1(1'b0), .out(multiplexer_3_out), .sel(clear));  // open: en
  Multiplexer #(.width(3)) multiplexer_4 (.in0(sel_I), .in1(3'b000), .out(multiplexer_4_out), .sel(clear));  // open: en
  Register #(.width(3)) register_4 (.D(multiplexer_4_out), .en(and_1_out), .Q(sel_O), .clk(clk), .clr(RST));
  Register #(.width(1)) register_5 (.D(multiplexer_5_out), .en(and_1_out), .Q(pre_O), .clk(clk), .clr(RST));
  Multiplexer multiplexer_5 (.in0(pre_I), .in1(1'b0), .out(multiplexer_5_out), .sel(clear));  // open: en
endmodule

module EX_MEM (
  input  MemW_I,
  input  [3:0] WB_I,
  input  [31:0] rs_I,
  input  [31:0] Instruction_I,
  input  [23:0] Addr_I,
  input  [31:0] Data_I,
  input  [31:0] RES_I,
  input  [2:0] des_reg_I,
  input  rs_EX_MEM_I,
  input  rt_EX_MEM_I,
  input  HALT,
  input  clk,
  input  RST,
  input  LHU_I,
  input  EN_I,
  output MemW_O,
  output [3:0] WB_O,
  output [23:0] Addr_O,
  output [31:0] Data_O,
  output [31:0] RES_O,
  output [31:0] Instruction_O,
  output [31:0] rs_O,
  output rs_EX_MEM_O,
  output rt_EX_MEM_O,
  output [2:0] des_reg_O,
  output EN_O,
  output LHU_O
);

  Register #(.width(1)) register_1 (.D(MemW_I), .en(HALT), .Q(MemW_O), .clk(clk), .clr(RST));
  Register #(.width(1)) register_2 (.D(rs_EX_MEM_I), .en(HALT), .Q(rs_EX_MEM_O), .clk(clk), .clr(RST));
  Register #(.width(4)) register_3 (.D(WB_I), .en(HALT), .Q(WB_O), .clk(clk), .clr(RST));
  Register #(.width(1)) register_4 (.D(rt_EX_MEM_I), .en(HALT), .Q(rt_EX_MEM_O), .clk(clk), .clr(RST));
  Register #(.width(24)) register_5 (.D(Addr_I), .en(HALT), .Q(Addr_O), .clk(clk), .clr(RST));
  Register #(.width(32)) register_6 (.D(Data_I), .en(HALT), .Q(Data_O), .clk(clk), .clr(RST));
  Register #(.width(32)) register_7 (.D(Instruction_I), .en(HALT), .Q(Instruction_O), .clk(clk), .clr(RST));
  Register #(.width(32)) register_8 (.D(RES_I), .en(HALT), .Q(RES_O), .clk(clk), .clr(RST));
  Register #(.width(1)) register_9 (.D(EN_I), .Q(EN_O), .clk(clk), .clr(RST));  // open: en
  Register #(.width(3)) register_10 (.D(des_reg_I), .en(HALT), .Q(des_reg_O), .clk(clk), .clr(RST));
  Register #(.width(1)) register_11 (.D(LHU_I), .en(HALT), .Q(LHU_O), .clk(clk), .clr(RST));
  Register #(.width(32)) register_12 (.D(rs_I), .en(HALT), .Q(rs_O), .clk(clk), .clr(RST));
endmodule

module MEM_WB (
  input  [3:0] WB_I,
  input  [31:0] Data_I,
  input  [31:0] RES_I,
  input  [31:0] Instruction_I,
  input  HALT,
  input  [4:0] rt_I,
  input  [4:0] rd_I,
  input  EN_I,
  input  clk,
  input  RST,
  output [3:0] WB_O,
  output [31:0] Instruction_O,
  output [31:0] Data_O,
  output [31:0] RES_O,
  output EN_O,
  output [4:0] rt_O,
  output [4:0] rd_O
);

  Register #(.width(4)) register_1 (.D(WB_I), .en(HALT), .Q(WB_O), .clk(clk), .clr(RST));
  Register #(.width(5)) register_2 (.D(rt_I), .en(HALT), .Q(rt_O), .clk(clk), .clr(RST));
  Register #(.width(5)) register_3 (.D(rd_I), .en(HALT), .Q(rd_O), .clk(clk), .clr(RST));
  Register #(.width(32)) register_4 (.D(Data_I), .en(HALT), .Q(Data_O), .clk(clk), .clr(RST));
  Register #(.width(32)) register_5 (.D(Instruction_I), .en(HALT), .Q(Instruction_O), .clk(clk), .clr(RST));
  Register #(.width(32)) register_6 (.D(RES_I), .en(HALT), .Q(RES_O), .clk(clk), .clr(RST));
  Register #(.width(1)) register_7 (.D(EN_I), .Q(EN_O), .clk(clk), .clr(RST));  // open: en
endmodule

module data_confilct (
  input  in_1,
  input  in_2,
  input  [31:0] Instruction_ID,
  input  [31:0] Instruction_EX,
  input  [31:0] Instruction_MEM,
  input  [2:0] src_reg_ID,
  input  [2:0] des_reg_EX,
  input  [2:0] des_reg_MEM,
  input  rW,
  output stall,
  output rs_EX_MEM,
  output rt_EX_MEM,
  output rs_EX_WB,
  output rt_EX_WB
);

  wire and_11_out, and_12_out, and_14_out, and_25_out, comparator_1_eq, comparator_2_eq, comparator_3_eq,
       comparator_4_eq, comparator_5_eq, comparator_6_eq, comparator_7_eq, comparator_8_eq, comparator_9_eq,
       comparator_10_eq, comparator_11_eq, comparator_12_eq, comparator_13_eq, comparator_14_eq,
       comparator_15_eq, comparator_16_eq, comparator_17_eq, comparator_18_eq, comparator_19_eq,
       comparator_20_eq, comparator_21_eq, comparator_22_eq, confilct2, not_1_out, not_2_out, or_1_out,
       or_2_out, or_3_out, or_4_out, or_5_out, or_6_out, rs_EX_MEM_1, rs_EX_MEM_2, rs_EX_MEM_3, rs_EX_MEM_4,
       rs_EX_MEM_5, rs_EX_WB_1, rs_EX_WB_2, rs_EX_WB_3, rs_EX_WB_4, rs_EX_WB_5, rt_EX_MEM_1, rt_EX_MEM_2,
       rt_EX_MEM_3, rt_EX_MEM_4, rt_EX_MEM_5, rt_EX_WB_1, rt_EX_WB_2, rt_EX_WB_3, rt_EX_WB_4, rt_EX_WB_5;

  Comparator #(.width(5)) comparator_1 (
    .a(Instruction_ID[25:21]), .b(Instruction_EX[20:16]), .eq(comparator_1_eq));  // open: gt, lt
  Comparator #(.width(5)) comparator_2 (
    .a(Instruction_ID[25:21]), .b(Instruction_EX[15:11]), .eq(comparator_2_eq));  // open: gt, lt
  Comparator #(.width(5)) comparator_3 (
    .a(Instruction_ID[25:21]), .b({5{1'b1}}), .eq(comparator_3_eq));  // open: gt, lt
  Comparator #(.width(5)) comparator_4 (
    .a(Instruction_ID[20:16]), .b(Instruction_EX[20:16]), .eq(comparator_4_eq));  // open: gt, lt
  Comparator #(.width(5)) comparator_5 (
    .a(Instruction_ID[20:16]), .b(Instruction_EX[15:11]), .eq(comparator_5_eq));  // open: gt, lt
  Comparator #(.width(5)) comparator_6 (
    .a(Instruction_ID[20:16]), .b({5{1'b1}}), .eq(comparator_6_eq));  // open: gt, lt
  Comparator #(.width(5)) comparator_7 (.a(5'b00010), .b(Instruction_EX[20:16]), .eq(comparator_7_eq));  // open: gt, lt
  Comparator #(.width(5)) comparator_8 (.a(5'b00010), .b(Instruction_EX[15:11]), .eq(comparator_8_eq));  // open: gt, lt
  Comparator #(.width(5)) comparator_9 (.a(5'b00100), .b(Instruction_EX[20:16]), .eq(comparator_9_eq));  // open: gt, lt
  Comparator #(.width(5)) comparator_10 (
    .a(5'b00100), .b(Instruction_EX[15:11]), .eq(comparator_10_eq));  // open: gt, lt
  and and_1 (rs_EX_MEM_1, src_reg_ID[0], comparator_1_eq, des_reg_EX[0]);
  and and_2 (rs_EX_MEM_2, src_reg_ID[0], comparator_2_eq, des_reg_EX[1]);
  and and_3 (rs_EX_MEM_3, src_reg_ID[0], comparator_3_eq, des_reg_EX[2]);
  and and_4 (rt_EX_MEM_1, src_reg_ID[1], comparator_4_eq, des_reg_EX[0]);
  and and_5 (rt_EX_MEM_2, src_reg_ID[1], comparator_5_eq, des_reg_EX[1]);
  and and_6 (rt_EX_MEM_3, src_reg_ID[1], comparator_6_eq, des_reg_EX[2]);
  and and_7 (rs_EX_MEM_4, src_reg_ID[2], comparator_7_eq, des_reg_EX[0]);
  and and_8 (rs_EX_MEM_5, src_reg_ID[2], comparator_8_eq, des_reg_EX[1]);
  and and_9 (rt_EX_MEM_4, src_reg_ID[2], comparator_9_eq, des_reg_EX[0]);
  and and_10 (rt_EX_MEM_5, src_reg_ID[2], comparator_10_eq, des_reg_EX[1]);
  Comparator #(.width(32)) comparator_11 (.a(Instruction_EX), .b({32{1'b0}}), .eq(comparator_11_eq));  // open: gt, lt
  not not_1 (not_1_out, comparator_11_eq);
  or or_1 (or_1_out, rs_EX_MEM_1, rs_EX_MEM_2, rs_EX_MEM_3, rs_EX_MEM_4, rs_EX_MEM_5);
  or or_2 (or_2_out, rs_EX_WB_1, rs_EX_WB_2, rs_EX_WB_3, rs_EX_WB_4, rs_EX_WB_5);
  and and_11 (and_11_out, or_1_out, not_1_out, rW);
  Register #(.width(1)) register_1 (.D(and_11_out), .Q(rs_EX_MEM), .clk(in_1), .clr(in_2));  // open: en
  and and_12 (and_12_out, or_2_out, not_2_out);
  Register #(.width(1)) register_2 (.D(and_12_out), .Q(rs_EX_WB), .clk(in_1), .clr(in_2));  // open: en
  or or_3 (or_3_out, rs_EX_MEM_1, rs_EX_MEM_2, rs_EX_MEM_3, rt_EX_MEM_1, rt_EX_MEM_2, rt_EX_MEM_3, rs_EX_MEM_4, rs_EX_MEM_5, rt_EX_MEM_4, rt_EX_MEM_5);
  and and_13 (stall, or_3_out, ~rW, not_1_out);  // AND_Gate
  Comparator #(.width(5)) comparator_12 (
    .a(Instruction_ID[25:21]), .b(Instruction_MEM[20:16]), .eq(comparator_12_eq));  // open: gt, lt
  Comparator #(.width(5)) comparator_13 (
    .a(Instruction_ID[25:21]), .b(Instruction_MEM[15:11]), .eq(comparator_13_eq));  // open: gt, lt
  Comparator #(.width(5)) comparator_14 (
    .a(Instruction_ID[25:21]), .b({5{1'b1}}), .eq(comparator_14_eq));  // open: gt, lt
  Comparator #(.width(5)) comparator_15 (
    .a(Instruction_ID[20:16]), .b(Instruction_MEM[20:16]), .eq(comparator_15_eq));  // open: gt, lt
  Comparator #(.width(5)) comparator_16 (
    .a(Instruction_ID[20:16]), .b(Instruction_MEM[15:11]), .eq(comparator_16_eq));  // open: gt, lt
  Comparator #(.width(5)) comparator_17 (
    .a(Instruction_ID[20:16]), .b({5{1'b1}}), .eq(comparator_17_eq));  // open: gt, lt
  Comparator #(.width(5)) comparator_18 (
    .a(5'b00010), .b(Instruction_MEM[20:16]), .eq(comparator_18_eq));  // open: gt, lt
  Comparator #(.width(5)) comparator_19 (
    .a(5'b00010), .b(Instruction_MEM[15:11]), .eq(comparator_19_eq));  // open: gt, lt
  Comparator #(.width(5)) comparator_20 (
    .a(5'b00100), .b(Instruction_MEM[20:16]), .eq(comparator_20_eq));  // open: gt, lt
  Comparator #(.width(5)) comparator_21 (
    .a(5'b00100), .b(Instruction_MEM[15:11]), .eq(comparator_21_eq));  // open: gt, lt
  or or_4 (or_4_out, rt_EX_MEM_1, rt_EX_MEM_2, rt_EX_MEM_3, rt_EX_MEM_4, rt_EX_MEM_5);
  and and_14 (and_14_out, or_4_out, not_1_out, rW);
  or or_5 (or_5_out, rt_EX_WB_1, rt_EX_WB_2, rt_EX_WB_3, rt_EX_WB_4, rt_EX_WB_5);
  and and_15 (rs_EX_WB_1, src_reg_ID[0], comparator_12_eq, des_reg_MEM[0]);
  and and_16 (rs_EX_WB_2, src_reg_ID[0], comparator_13_eq, des_reg_MEM[1]);
  and and_17 (rs_EX_WB_3, src_reg_ID[0], comparator_14_eq, des_reg_MEM[2]);
  and and_18 (rt_EX_WB_1, src_reg_ID[1], comparator_15_eq, des_reg_MEM[0]);
  and and_19 (rt_EX_WB_2, src_reg_ID[1], comparator_16_eq, des_reg_MEM[1]);
  and and_20 (rt_EX_WB_3, src_reg_ID[1], comparator_17_eq, des_reg_MEM[2]);
  and and_21 (rs_EX_WB_4, src_reg_ID[2], comparator_18_eq, des_reg_MEM[0]);
  and and_22 (rs_EX_WB_5, src_reg_ID[2], comparator_19_eq, des_reg_MEM[1]);
  and and_23 (rt_EX_WB_4, src_reg_ID[2], comparator_20_eq, des_reg_MEM[0]);
  and and_24 (rt_EX_WB_5, src_reg_ID[2], comparator_21_eq, des_reg_MEM[1]);
  Comparator #(.width(32)) comparator_22 (.a(Instruction_MEM), .b({32{1'b0}}), .eq(comparator_22_eq));  // open: gt, lt
  Register #(.width(1)) register_3 (.D(and_14_out), .Q(rt_EX_MEM), .clk(in_1), .clr(in_2));  // open: en
  and and_25 (and_25_out, or_5_out, not_2_out);
  Register #(.width(1)) register_4 (.D(and_25_out), .Q(rt_EX_WB), .clk(in_1), .clr(in_2));  // open: en
  not not_2 (not_2_out, comparator_22_eq);
  or or_6 (or_6_out, rs_EX_WB_1, rs_EX_WB_2, rs_EX_WB_3, rt_EX_WB_1, rt_EX_WB_2, rt_EX_WB_3, rs_EX_WB_4, rs_EX_WB_5, rt_EX_WB_4, rt_EX_WB_5);
  and and_26 (confilct2, or_6_out, ~rW, not_2_out);  // AND_Gate

  // Other names for the same wires on the sheet: confilct1 = stall; des_rt = des_reg_EX[0]; des_rd = des_reg_EX[1];
  //   jal = des_reg_EX[2]; des_rt_2 = des_reg_MEM[0]; des_rd_2 = des_reg_MEM[1]; jal_2 = des_reg_MEM[2];
  //   Sp_EX[5:0] = Instruction_EX[5:0]; rd_EX[4:0] = Instruction_EX[15:11]; rt_EX[4:0] = Instruction_EX[20:16];
  //   rs_EX[4:0] = Instruction_EX[25:21]; Op_EX[5:0] = Instruction_EX[31:26]; Sp_ID[5:0] = Instruction_ID[5:0];
  //   rd_ID[4:0] = Instruction_ID[15:11]; rt_ID[4:0] = Instruction_ID[20:16]; rs_ID[4:0] = Instruction_ID[25:21];
  //   Op_ID[5:0] = Instruction_ID[31:26]; Sp_MEM[5:0] = Instruction_MEM[5:0]; rd_MEM[4:0] = Instruction_MEM[15:11];
  //   rt_MEM[4:0] = Instruction_MEM[20:16]; rs_MEM[4:0] = Instruction_MEM[25:21];
  //   Op_MEM[5:0] = Instruction_MEM[31:26]; RST = in_2; src_rs = src_reg_ID[0]; src_rt = src_reg_ID[1];
  //   sys = src_reg_ID[2]; T = in_1

  // Notes on the sheet:
  //   0->j
  //   1->rs
  //   2->rt
  //   3->rs&rt
  //   4->sys->2&4
  //   0->non
  //   1->rt
  //   2->rd
  //   3->$31
endmodule

module BHT (
  input  T,
  input  RST,
  input  suc,
  input  write,
  input  hit_I,
  input  [2:0] sel_I,
  input  [23:0] PC,
  input  [23:0] cur_PC,
  input  [23:0] NPC,
  output pre_J,
  output [23:0] pre_PC,
  output [2:0] sel,
  output hit,
  output [23:0] cur_JPC_O
);

  wire and_28_out, and_34_out, comparator_1_eq, comparator_2_eq, comparator_3_eq, comparator_4_eq,
       comparator_5_eq, comparator_6_eq, comparator_7_eq, comparator_8_eq, comparator_9_eq, comparator_10_eq,
       comparator_11_lt, comparator_12_lt, comparator_13_lt, comparator_14_lt, comparator_15_lt,
       comparator_16_lt, comparator_17_lt, decoder_1_out0, decoder_1_out1, decoder_1_out2, decoder_1_out3,
       decoder_1_out4, decoder_1_out5, decoder_1_out6, decoder_1_out7, decoder_2_out0, decoder_2_out1,
       decoder_2_out2, decoder_2_out3, decoder_2_out4, decoder_2_out5, decoder_2_out6, decoder_2_out7,
       decoder_3_out0, decoder_3_out1, decoder_3_out2, decoder_3_out3, decoder_3_out4, decoder_3_out5,
       decoder_3_out6, decoder_3_out7, hit0, hit1, hit2, hit3, hit4, hit5, hit6, hit7, not_1_out, not_2_out,
       not_3_out, or_1_out, or_2_out, or_3_out, or_4_out, or_5_out, or_6_out, or_7_out, or_8_out, or_9_out,
       or_10_out, or_11_out, or_12_out, or_13_out, or_14_out, or_15_out, or_16_out, or_17_out, or_18_out,
       or_19_out, or_20_out, or_21_out, or_22_out, or_23_out, or_24_out, pre0, pre1, pre2, pre3, pre4, pre5,
       pre6, pre7, replc, replc0, replc1, replc2, replc3, replc4, replc5, replc6, replc7, v0, v1, v2, v3, v4,
       v5, v6, v7, write0, write1, write2, write3, write4, write5, write6, write7;
  wire [0:0] multiplexer_3_out;
  wire [1:0] multiplexer_12_out, multiplexer_13_out, multiplexer_14_out, multiplexer_15_out,
       multiplexer_16_out, multiplexer_17_out, multiplexer_18_out, multiplexer_19_out, next_num0, next_num1,
       next_num2, next_num3, next_num4, next_num5, next_num6, next_num7, pre_num0, pre_num1, pre_num2,
       pre_num3, pre_num4, pre_num5, pre_num6, pre_num7;
  wire [2:0] final_LRU, multiplexer_5_out, multiplexer_6_out, multiplexer_9_out, multiplexer_11_out,
       multiplexer_21_out, multiplexer_22_out;
  wire [3:0] write_n;
  wire [15:0] adder_1_out, adder_2_out, adder_3_out, adder_4_out, adder_5_out, adder_6_out, adder_7_out,
       adder_8_out, LRU0, LRU1, LRU2, LRU3, LRU4, LRU5, LRU6, LRU7, multiplexer_4_out, multiplexer_7_out,
       multiplexer_8_out, multiplexer_10_out, multiplexer_20_out, multiplexer_23_out, multiplexer_24_out,
       multiplexer_25_out, multiplexer_26_out, multiplexer_27_out, multiplexer_28_out, multiplexer_29_out,
       multiplexer_30_out, multiplexer_31_out;
  wire [23:0] _PC0, _PC0_n, _PC1, _PC1_n, _PC2, _PC2_n, _PC3, _PC3_n, _PC4, _PC4_n, _PC5, _PC5_n, _PC6,
       _PC6_n, _PC7, _PC7_n, multiplexer_2_out, PC0, PC0_n, PC1, PC1_n, PC2, PC2_n, PC3, PC3_n, PC4, PC4_n,
       PC5, PC5_n, PC6, PC6_n, PC7, PC7_n;

  // Probe on v0
  // Probe on v1
  // Probe on v2
  // Probe on v3
  // Probe on v4
  // Probe on v5
  // Probe on v6
  // Probe on v7
  Decoder #(.select(3)) decoder_1 (
    .out0(decoder_1_out0), .out1(decoder_1_out1), .out2(decoder_1_out2), .out3(decoder_1_out3),
    .out4(decoder_1_out4), .out5(decoder_1_out5), .out6(decoder_1_out6), .out7(decoder_1_out7), .sel(sel_I));  // open: en
  Decoder #(.select(4)) decoder_2 (
    .out0(decoder_2_out0), .out1(decoder_2_out1), .out2(decoder_2_out2), .out3(decoder_2_out3),
    .out4(decoder_2_out4), .out5(decoder_2_out5), .out6(decoder_2_out6), .out7(decoder_2_out7), .sel(write_n));  // open: out8, out9, out10, out11, out12, out13, out14, out15, en
  // Probe on next_num0
  sel_pre sel_pre_1 (.pre_num(pre_num0), .suc(suc), .next_num(next_num0));
  sel_pre sel_pre_2 (.pre_num(pre_num1), .suc(suc), .next_num(next_num1));
  sel_pre sel_pre_3 (.pre_num(pre_num2), .suc(suc), .next_num(next_num2));
  sel_pre sel_pre_4 (.pre_num(pre_num3), .suc(suc), .next_num(next_num3));
  // Probe on _PC0
  // Probe on _PC1
  // Probe on _PC2
  // Probe on _PC3
  // Probe on _PC4
  // Probe on _PC5
  // Probe on _PC6
  // Probe on _PC7
  and and_1 (pre0, decoder_1_out0, hit_I);
  and and_2 (pre1, decoder_1_out1, hit_I);
  Priority_Encoder #(.select(4)) priority_encoder_1 (
    .in0(1'b1), .in1(v0), .in2(v1), .in3(v2), .in4(v3), .in5(v4), .in6(v5), .in7(v6), .in8(v7), .out(write_n));  // open: in9, in10, in11, in12, in13, in14, in15, gs, en_out, en_in
  and and_3 (write1, decoder_2_out1, and_28_out);
  and and_4 (write0, decoder_2_out0, and_28_out);
  Comparator #(.width(24)) comparator_1 (.a(PC), .b({24{1'b0}}), .eq(comparator_1_eq));  // open: gt, lt
  not not_1 (not_1_out, comparator_1_eq);
  Multiplexer #(.select(3), .width(24)) multiplexer_1 (
    .in0(PC0_n), .in1(PC1_n), .in2(PC2_n), .in3(PC3_n), .in4(PC4_n), .in5(PC5_n), .in6(PC6_n), .in7(PC7_n),
    .out(pre_PC), .sel(sel), .en(hit));
  // Probe on _PC0_n
  // Probe on _PC1_n
  // Probe on _PC2_n
  // Probe on _PC3_n
  // Probe on _PC4_n
  // Probe on _PC5_n
  // Probe on _PC6_n
  // Probe on _PC7_n
  and and_5 (pre2, decoder_1_out2, hit_I);
  and and_6 (pre3, decoder_1_out3, hit_I);
  and and_7 (pre4, decoder_1_out4, hit_I);
  and and_8 (write4, decoder_2_out4, and_28_out);
  and and_9 (write2, decoder_2_out2, and_28_out);
  and and_10 (write3, decoder_2_out3, and_28_out);
  Comparator #(.width(24)) comparator_2 (.a(PC), .b(PC0), .eq(comparator_2_eq));  // open: gt, lt
  and and_11 (hit0, comparator_2_eq, not_1_out);
  Comparator #(.width(24)) comparator_3 (.a(PC), .b(PC1), .eq(comparator_3_eq));  // open: gt, lt
  and and_12 (hit1, comparator_3_eq, not_1_out);
  Comparator #(.width(24)) comparator_4 (.a(PC), .b(PC2), .eq(comparator_4_eq));  // open: gt, lt
  and and_13 (hit2, comparator_4_eq, not_1_out);
  Comparator #(.width(24)) comparator_5 (.a(PC), .b(PC3), .eq(comparator_5_eq));  // open: gt, lt
  and and_14 (hit3, comparator_5_eq, not_1_out);
  Comparator #(.width(24)) comparator_6 (.a(PC), .b(PC4), .eq(comparator_6_eq));  // open: gt, lt
  and and_15 (hit4, comparator_6_eq, not_1_out);
  Comparator #(.width(24)) comparator_7 (.a(PC), .b(PC5), .eq(comparator_7_eq));  // open: gt, lt
  and and_16 (hit5, comparator_7_eq, not_1_out);
  Comparator #(.width(24)) comparator_8 (.a(PC), .b(PC6), .eq(comparator_8_eq));  // open: gt, lt
  and and_17 (hit6, comparator_8_eq, not_1_out);
  Comparator #(.width(24)) comparator_9 (.a(PC), .b(PC7), .eq(comparator_9_eq));  // open: gt, lt
  and and_18 (hit7, comparator_9_eq, not_1_out);
  // Probe on multiplexer_2_out
  Multiplexer #(.select(3), .width(24)) multiplexer_2 (
    .in0(PC0), .in1(PC1), .in2(PC2), .in3(PC3), .in4(PC4), .in5(PC5), .in6(PC6), .in7(PC7),
    .out(multiplexer_2_out), .sel(sel), .en(hit));
  sel_pre sel_pre_5 (.pre_num(pre_num4), .suc(suc), .next_num(next_num4));
  sel_pre sel_pre_6 (.pre_num(pre_num5), .suc(suc), .next_num(next_num5));
  sel_pre sel_pre_7 (.pre_num(pre_num6), .suc(suc), .next_num(next_num6));
  sel_pre sel_pre_8 (.pre_num(pre_num7), .suc(suc), .next_num(next_num7));
  and and_19 (pre7, decoder_1_out7, hit_I);
  and and_20 (pre5, decoder_1_out5, hit_I);
  and and_21 (pre6, decoder_1_out6, hit_I);
  and and_22 (write5, decoder_2_out5, and_28_out);
  and and_23 (write6, decoder_2_out6, and_28_out);
  // Probe on cur_JPC_O
  Register #(.width(24)) register_1 (.D(multiplexer_2_out), .en(hit), .Q(cur_JPC_O), .clk(T));  // open: clr
  // Probe on pre_num0
  // Probe on pre_num1
  // Probe on pre_num2
  // Probe on pre_num3
  // Probe on pre_num4
  // Probe on pre_num5
  // Probe on pre_num6
  // Probe on pre_num7
  and and_24 (write7, decoder_2_out7, and_28_out);
  Priority_Encoder priority_encoder_2 (
    .in0(hit0), .in1(hit1), .in2(hit2), .in3(hit3), .in4(hit4), .in5(hit5), .in6(hit6), .in7(hit7),
    .out(sel), .gs(hit));  // open: en_in, en_out
  Multiplexer #(.select(3), .width(2)) multiplexer_3 (
    .in0(pre_num0), .in1(pre_num1), .in2(pre_num2), .in3(pre_num3), .in4(pre_num4), .in5(pre_num5),
    .in6(pre_num6), .in7(pre_num5), .out({pre_J, multiplexer_3_out[0]}), .sel(sel), .en(hit));
  Decoder #(.select(3)) decoder_3 (
    .out0(decoder_3_out0), .out1(decoder_3_out1), .out2(decoder_3_out2), .out3(decoder_3_out3),
    .out4(decoder_3_out4), .out5(decoder_3_out5), .out6(decoder_3_out6), .out7(decoder_3_out7),
    .sel(final_LRU));  // open: en
  or or_1 (or_1_out, write0, replc0);
  // Probe on LRU0
  // Probe on LRU1
  // Probe on LRU2
  // Probe on LRU3
  // Probe on LRU4
  // Probe on LRU5
  // Probe on LRU6
  // Probe on LRU7
  Comparator #(.width(4)) comparator_10 (.a(write_n), .b(4'b1000), .eq(comparator_10_eq));  // open: gt, lt
  not not_2 (not_2_out, comparator_10_eq);
  and and_25 (replc0, decoder_3_out0, replc);
  and and_26 (replc2, decoder_3_out2, replc);
  and and_27 (replc1, decoder_3_out1, replc);
  // Probe on PC
  or or_2 (or_2_out, replc1, write1);
  or or_3 (or_3_out, write2, replc2);
  or or_4 (or_4_out, write3, replc3);
  or or_5 (or_5_out, write4, replc4);
  and and_28 (and_28_out, write, ~hit_I, not_2_out);  // AND_Gate
  or or_6 (or_6_out, write5, replc5);
  or or_7 (or_7_out, write6, replc6);
  or or_8 (or_8_out, write7, replc7);
  Multiplexer #(.width(16)) multiplexer_4 (
    .in0(LRU0), .in1(LRU1), .out(multiplexer_4_out), .sel(comparator_11_lt));  // open: en
  Comparator #(.width(16)) comparator_11 (.a(LRU0), .b(LRU1), .lt(comparator_11_lt));  // open: gt, eq
  Multiplexer #(.width(3)) multiplexer_5 (
    .in0(3'b000), .in1(3'b001), .out(multiplexer_5_out), .sel(comparator_11_lt));  // open: en
  and and_29 (replc3, decoder_3_out3, replc);
  and and_30 (replc5, decoder_3_out5, replc);
  and and_31 (replc4, decoder_3_out4, replc);
  // Probe on cur_PC
  Register #(.width(1)) register_2 (.D(1'b1), .en(or_1_out), .Q(v0), .clk(T), .clr(RST));
  Register #(.width(1)) register_3 (.D(1'b1), .en(or_2_out), .Q(v1), .clk(T), .clr(RST));
  // Probe on nothing
  Register #(.width(1)) register_4 (.D(1'b1), .en(or_3_out), .Q(v2), .clk(T), .clr(RST));
  Register #(.width(1)) register_5 (.D(1'b1), .en(or_4_out), .Q(v3), .clk(T), .clr(RST));
  Register #(.width(1)) register_6 (.D(1'b1), .en(or_5_out), .Q(v4), .clk(T), .clr(RST));
  Register #(.width(1)) register_7 (.D(1'b1), .en(or_6_out), .Q(v5), .clk(T), .clr(RST));
  Register #(.width(1)) register_8 (.D(1'b1), .en(or_7_out), .Q(v6), .clk(T), .clr(RST));
  Register #(.width(1)) register_9 (.D(1'b1), .en(or_8_out), .Q(v7), .clk(T), .clr(RST));
  Multiplexer #(.width(3)) multiplexer_6 (
    .in0(multiplexer_5_out), .in1(3'b010), .out(multiplexer_6_out), .sel(comparator_12_lt));  // open: en
  and and_32 (replc6, decoder_3_out6, replc);
  and and_33 (replc7, decoder_3_out7, replc);
  // Probe on NPC
  // Probe on PC0
  Register #(.width(24)) register_10 (.D(cur_PC), .en(or_1_out), .Q(PC0), .clk(T), .clr(RST));
  Register #(.width(24)) register_11 (.D(cur_PC), .en(or_2_out), .Q(PC1), .clk(T), .clr(RST));
  Register #(.width(24)) register_12 (.D(cur_PC), .en(or_3_out), .Q(PC2), .clk(T), .clr(RST));
  Register #(.width(24)) register_13 (.D(cur_PC), .en(or_4_out), .Q(PC3), .clk(T), .clr(RST));
  Register #(.width(24)) register_14 (.D(cur_PC), .en(or_5_out), .Q(PC4), .clk(T), .clr(RST));
  Register #(.width(24)) register_15 (.D(cur_PC), .en(or_6_out), .Q(PC5), .clk(T), .clr(RST));
  Register #(.width(24)) register_16 (.D(cur_PC), .en(or_7_out), .Q(PC6), .clk(T), .clr(RST));
  Register #(.width(24)) register_17 (.D(cur_PC), .en(or_8_out), .Q(PC7), .clk(T), .clr(RST));
  Multiplexer #(.width(16)) multiplexer_7 (
    .in0(multiplexer_4_out), .in1(LRU2), .out(multiplexer_7_out), .sel(comparator_12_lt));  // open: en
  Comparator #(.width(16)) comparator_12 (.a(multiplexer_4_out), .b(LRU2), .lt(comparator_12_lt));  // open: gt, eq
  Multiplexer #(.width(16)) multiplexer_8 (
    .in0(multiplexer_7_out), .in1(LRU3), .out(multiplexer_8_out), .sel(comparator_13_lt));  // open: en
  Comparator #(.width(16)) comparator_13 (.a(multiplexer_7_out), .b(LRU3), .lt(comparator_13_lt));  // open: gt, eq
  Multiplexer #(.width(3)) multiplexer_9 (
    .in0(multiplexer_6_out), .in1(3'b011), .out(multiplexer_9_out), .sel(comparator_13_lt));  // open: en
  // Probe on pre_PC
  // Probe on PC0_n
  Register #(.width(24)) register_18 (.D(NPC), .en(or_1_out), .Q(PC0_n), .clk(T), .clr(RST));
  Register #(.width(24)) register_19 (.D(NPC), .en(or_2_out), .Q(PC1_n), .clk(T), .clr(RST));
  Register #(.width(24)) register_20 (.D(NPC), .en(or_3_out), .Q(PC2_n), .clk(T), .clr(RST));
  Register #(.width(24)) register_21 (.D(NPC), .en(or_4_out), .Q(PC3_n), .clk(T), .clr(RST));
  Register #(.width(24)) register_22 (.D(NPC), .en(or_5_out), .Q(PC4_n), .clk(T), .clr(RST));
  Register #(.width(24)) register_23 (.D(NPC), .en(or_6_out), .Q(PC5_n), .clk(T), .clr(RST));
  Register #(.width(24)) register_24 (.D(NPC), .en(or_7_out), .Q(PC6_n), .clk(T), .clr(RST));
  Register #(.width(24)) register_25 (.D(NPC), .en(or_8_out), .Q(PC7_n), .clk(T), .clr(RST));
  Multiplexer #(.width(16)) multiplexer_10 (
    .in0(multiplexer_8_out), .in1(LRU4), .out(multiplexer_10_out), .sel(comparator_14_lt));  // open: en
  Comparator #(.width(16)) comparator_14 (.a(multiplexer_8_out), .b(LRU4), .lt(comparator_14_lt));  // open: gt, eq
  Multiplexer #(.width(3)) multiplexer_11 (
    .in0(multiplexer_9_out), .in1(3'b100), .out(multiplexer_11_out), .sel(comparator_14_lt));  // open: en
  and and_34 (and_34_out, v0, v1, v2, v3, v4, v5, v6, v7, write);
  not not_3 (not_3_out, hit_I);
  Multiplexer #(.width(2)) multiplexer_12 (
    .in0(2'b11), .in1(next_num0), .out(multiplexer_12_out), .sel(pre0));  // open: en
  or or_9 (or_9_out, or_1_out, pre0);
  Multiplexer #(.width(2)) multiplexer_13 (
    .in0(2'b11), .in1(next_num1), .out(multiplexer_13_out), .sel(pre1));  // open: en
  or or_10 (or_10_out, or_2_out, pre1);
  Multiplexer #(.width(2)) multiplexer_14 (
    .in0(2'b11), .in1(next_num2), .out(multiplexer_14_out), .sel(pre2));  // open: en
  or or_11 (or_11_out, or_3_out, pre2);
  Multiplexer #(.width(2)) multiplexer_15 (
    .in0(2'b11), .in1(next_num3), .out(multiplexer_15_out), .sel(pre3));  // open: en
  or or_12 (or_12_out, or_4_out, pre3);
  Multiplexer #(.width(2)) multiplexer_16 (
    .in0(2'b11), .in1(next_num4), .out(multiplexer_16_out), .sel(pre4));  // open: en
  or or_13 (or_13_out, or_5_out, pre4);
  Multiplexer #(.width(2)) multiplexer_17 (
    .in0(2'b11), .in1(next_num5), .out(multiplexer_17_out), .sel(pre5));  // open: en
  or or_14 (or_14_out, or_6_out, pre5);
  Multiplexer #(.width(2)) multiplexer_18 (
    .in0(2'b11), .in1(next_num6), .out(multiplexer_18_out), .sel(pre6));  // open: en
  or or_15 (or_15_out, or_7_out, pre6);
  Multiplexer #(.width(2)) multiplexer_19 (
    .in0(2'b11), .in1(next_num7), .out(multiplexer_19_out), .sel(pre7));  // open: en
  or or_16 (or_16_out, or_8_out, pre7);
  Multiplexer #(.width(16)) multiplexer_20 (
    .in0(multiplexer_10_out), .in1(LRU5), .out(multiplexer_20_out), .sel(comparator_15_lt));  // open: en
  Comparator #(.width(16)) comparator_15 (.a(multiplexer_10_out), .b(LRU5), .lt(comparator_15_lt));  // open: gt, eq
  Multiplexer #(.width(3)) multiplexer_21 (
    .in0(multiplexer_11_out), .in1(3'b101), .out(multiplexer_21_out), .sel(comparator_15_lt));  // open: en
  and and_35 (replc, and_34_out, not_3_out);
  Pull_Resistor pull_resistor_1 (.node(pre_J));
  // Probe on pre_num0
  Register #(.width(2)) register_26 (.D(multiplexer_12_out), .en(or_9_out), .Q(pre_num0), .clk(T), .clr(RST));
  Register #(.width(2)) register_27 (.D(multiplexer_13_out), .en(or_10_out), .Q(pre_num1), .clk(T), .clr(RST));
  Register #(.width(2)) register_28 (.D(multiplexer_14_out), .en(or_11_out), .Q(pre_num2), .clk(T), .clr(RST));
  Register #(.width(2)) register_29 (.D(multiplexer_15_out), .en(or_12_out), .Q(pre_num3), .clk(T), .clr(RST));
  Register #(.width(2)) register_30 (.D(multiplexer_16_out), .en(or_13_out), .Q(pre_num4), .clk(T), .clr(RST));
  Register #(.width(2)) register_31 (.D(multiplexer_17_out), .en(or_14_out), .Q(pre_num5), .clk(T), .clr(RST));
  Register #(.width(2)) register_32 (.D(multiplexer_18_out), .en(or_15_out), .Q(pre_num6), .clk(T), .clr(RST));
  Register #(.width(2)) register_33 (.D(multiplexer_19_out), .en(or_16_out), .Q(pre_num7), .clk(T), .clr(RST));
  Multiplexer #(.width(3)) multiplexer_22 (
    .in0(multiplexer_21_out), .in1(3'b110), .out(multiplexer_22_out), .sel(comparator_16_lt));  // open: en
  or or_17 (or_17_out, hit0, write0, replc0);
  Multiplexer #(.width(16)) multiplexer_23 (
    .in0(adder_1_out), .in1({16{1'b0}}), .out(multiplexer_23_out), .sel(or_17_out));  // open: en
  or or_18 (or_18_out, hit1, write1, replc1);
  Multiplexer #(.width(16)) multiplexer_24 (
    .in0(adder_2_out), .in1({16{1'b0}}), .out(multiplexer_24_out), .sel(or_18_out));  // open: en
  or or_19 (or_19_out, hit2, write2, replc2);
  Multiplexer #(.width(16)) multiplexer_25 (
    .in0(adder_3_out), .in1({16{1'b0}}), .out(multiplexer_25_out), .sel(or_19_out));  // open: en
  or or_20 (or_20_out, hit3, write3, replc3);
  or or_21 (or_21_out, hit4, write4, replc4);
  or or_22 (or_22_out, hit5, write5, replc5);
  or or_23 (or_23_out, hit6, write6, replc6);
  or or_24 (or_24_out, hit7, write7, replc7);
  Multiplexer #(.width(16)) multiplexer_26 (
    .in0(adder_8_out), .in1({16{1'b0}}), .out(multiplexer_26_out), .sel(or_24_out));  // open: en
  Multiplexer #(.width(16)) multiplexer_27 (
    .in0(multiplexer_20_out), .in1(LRU6), .out(multiplexer_27_out), .sel(comparator_16_lt));  // open: en
  Comparator #(.width(16)) comparator_16 (.a(multiplexer_20_out), .b(LRU6), .lt(comparator_16_lt));  // open: gt, eq
  // Probe on LRU0
  Register #(.width(16)) register_34 (.D(multiplexer_23_out), .Q(LRU0), .clk(T), .clr(RST));  // open: en
  Register #(.width(16)) register_35 (.D(multiplexer_24_out), .Q(LRU1), .clk(T), .clr(RST));  // open: en
  Register #(.width(16)) register_36 (.D(multiplexer_25_out), .Q(LRU2), .clk(T), .clr(RST));  // open: en
  Register #(.width(16)) register_37 (.D(multiplexer_28_out), .Q(LRU3), .clk(T), .clr(RST));  // open: en
  Multiplexer #(.width(16)) multiplexer_28 (
    .in0(adder_4_out), .in1({16{1'b0}}), .out(multiplexer_28_out), .sel(or_20_out));  // open: en
  Register #(.width(16)) register_38 (.D(multiplexer_29_out), .Q(LRU4), .clk(T), .clr(RST));  // open: en
  Multiplexer #(.width(16)) multiplexer_29 (
    .in0(adder_5_out), .in1({16{1'b0}}), .out(multiplexer_29_out), .sel(or_21_out));  // open: en
  Register #(.width(16)) register_39 (.D(multiplexer_30_out), .Q(LRU5), .clk(T), .clr(RST));  // open: en
  Multiplexer #(.width(16)) multiplexer_30 (
    .in0(adder_6_out), .in1({16{1'b0}}), .out(multiplexer_30_out), .sel(or_22_out));  // open: en
  Register #(.width(16)) register_40 (.D(multiplexer_31_out), .Q(LRU6), .clk(T), .clr(RST));  // open: en
  Multiplexer #(.width(16)) multiplexer_31 (
    .in0(adder_7_out), .in1({16{1'b0}}), .out(multiplexer_31_out), .sel(or_23_out));  // open: en
  Register #(.width(16)) register_41 (.D(multiplexer_26_out), .Q(LRU7), .clk(T), .clr(RST));  // open: en
  Comparator #(.width(16)) comparator_17 (.a(multiplexer_27_out), .b(LRU7), .lt(comparator_17_lt));  // open: gt, eq
  Multiplexer #(.width(3)) multiplexer_32 (
    .in0(multiplexer_22_out), .in1(3'b111), .out(final_LRU), .sel(comparator_17_lt));  // open: en
  Adder #(.width(16)) adder_1 (.a(LRU0), .b(16'h1), .out(adder_1_out));  // open: cin, cout
  Adder #(.width(16)) adder_2 (.a(LRU1), .b(16'h1), .out(adder_2_out));  // open: cin, cout
  Adder #(.width(16)) adder_3 (.a(LRU2), .b(16'h1), .out(adder_3_out));  // open: cin, cout
  Adder #(.width(16)) adder_4 (.a(LRU3), .b(16'h1), .out(adder_4_out));  // open: cin, cout
  Adder #(.width(16)) adder_5 (.a(LRU4), .b(16'h1), .out(adder_5_out));  // open: cin, cout
  Adder #(.width(16)) adder_6 (.a(LRU5), .b(16'h1), .out(adder_6_out));  // open: cin, cout
  Adder #(.width(16)) adder_7 (.a(LRU6), .b(16'h1), .out(adder_7_out));  // open: cin, cout
  Adder #(.width(16)) adder_8 (.a(LRU7), .b(16'h1), .out(adder_8_out));  // open: cin, cout
  Multiplier #(.width(24)) multiplier_1 (.a(PC0), .b(24'h4), .out(_PC0));  // open: cin, cout
  Multiplier #(.width(24)) multiplier_2 (.a(PC1), .b(24'h4), .out(_PC1));  // open: cin, cout
  Multiplier #(.width(24)) multiplier_3 (.a(PC2), .b(24'h4), .out(_PC2));  // open: cin, cout
  Multiplier #(.width(24)) multiplier_4 (.a(PC3), .b(24'h4), .out(_PC3));  // open: cin, cout
  Multiplier #(.width(24)) multiplier_5 (.a(PC4), .b(24'h4), .out(_PC4));  // open: cin, cout
  Multiplier #(.width(24)) multiplier_6 (.a(PC5), .b(24'h4), .out(_PC5));  // open: cin, cout
  Multiplier #(.width(24)) multiplier_7 (.a(PC6), .b(24'h4), .out(_PC6));  // open: cin, cout
  Multiplier #(.width(24)) multiplier_8 (.a(PC7), .b(24'h4), .out(_PC7));  // open: cin, cout
  Multiplier #(.width(24)) multiplier_9 (.a(PC0_n), .b(24'h4), .out(_PC0_n));  // open: cin, cout
  Multiplier #(.width(24)) multiplier_10 (.a(PC1_n), .b(24'h4), .out(_PC1_n));  // open: cin, cout
  Multiplier #(.width(24)) multiplier_11 (.a(PC2_n), .b(24'h4), .out(_PC2_n));  // open: cin, cout
  Multiplier #(.width(24)) multiplier_12 (.a(PC3_n), .b(24'h4), .out(_PC3_n));  // open: cin, cout
  Multiplier #(.width(24)) multiplier_13 (.a(PC4_n), .b(24'h4), .out(_PC4_n));  // open: cin, cout
  Multiplier #(.width(24)) multiplier_14 (.a(PC5_n), .b(24'h4), .out(_PC5_n));  // open: cin, cout
  Multiplier #(.width(24)) multiplier_15 (.a(PC6_n), .b(24'h4), .out(_PC6_n));  // open: cin, cout
  Multiplier #(.width(24)) multiplier_16 (.a(PC7_n), .b(24'h4), .out(_PC7_n));  // open: cin, cout
endmodule

module sel_pre (
  input  [1:0] pre_num,
  input  suc,
  output [1:0] next_num
);

  Multiplexer #(.select(3), .width(2)) multiplexer_1 (
    .in0(2'b00), .in1(2'b01), .in2(2'b00), .in3(2'b11), .in4(2'b00), .in5(2'b11), .in6(2'b10), .in7(2'b11),
    .out(next_num), .sel({pre_num, suc}));  // open: en
endmodule
